// Logisim project cpu_bubble.circ as structural Verilog: 13 circuits, main circuit cpu
module cpu (
);

  wire alu_1_equal, and_1_out, and_2_out, and_3_out, CLK, conflitctrl_1_id_ex_clear, controller_1_disp,
       controller_1_dmld, controller_1_dmstr, controller_1_halt, controller_1_pause, controller_1_sha, En,
       Enn, ex_mem_1_dispout, ex_mem_1_dmldout, ex_mem_1_dmstrout, ex_mem_1_haltout, ex_mem_1_pauseout,
       id_ex_1_dispout, id_ex_1_dmldout, id_ex_1_dmstrout, id_ex_1_haltout, id_ex_1_pauseout, id_ex_1_shaout,
       istrsplit_1_syscall, mem_wb_1_haltout, mem_wb_1_pauseout, or_1_out, PAU, Pause, power, RST, Success,
       WE, WE_DE, WE_ID, WE_ME;
  wire [1:0] controller_1_m1, controller_1_m2, controller_1_m3, controller_1_m4, ex_mem_1_m3out,
       id_ex_1_m1out, id_ex_1_m2out, id_ex_1_m3out, id_ex_1_m4out, mem_wb_1_m3out;
  wire [3:0] controller_1_alu, controller_1_dmsel, ex_mem_1_dmselout, id_ex_1_aluout, id_ex_1_dmselout;
  wire [4:0] ex_mem_1__5bout1, id_ex_1__5bout1, id_ex_1__5bout2, istrsplit_1_rd, istrsplit_1_rs,
       istrsplit_1_rt, istrsplit_1_shamt, multiplexer_4_out, registerfile_1_p4;
  wire [5:0] istrsplit_1_func, istrsplit_1_op;
  wire [15:0] istrsplit_1_imm16, \总周期数 , \无条件分支指令数 , \有条件分支成功跳转 , \有条件分支指令数 ;
  wire [25:0] istrsplit_1_imm26;
  wire [27:0] Istr, Istr1, Istr2, Istr3;
  wire [31:0] adder_1_out, adder_2_out, alu_1_result, ex_mem_1__32bout2, ex_mem_1__32bout3,
       ex_mem_1__32bout4, id_ex_1__32bout1, id_ex_1__32bout2, id_ex_1__32bout3, id_ex_1__32bout4,
       id_ex_1_r1out, id_ex_1_r2out, if_id_1_instrout, if_id_1_pcout, mem_wb_1__32bout1, mem_wb_1__32bout2,
       mem_wb_1__32bout3, mips_ram_1_p8, multiplexer_1_out, multiplexer_2_out, multiplexer_3_out,
       multiplexer_5_out, PC_q, registerfile_1_p1, registerfile_1_p7, rom_1_data, romshm_1_dataout,
       signextend_1_out_2, SyscallOut, undriven;

  xor xor_1 (Enn, Pause, PAU);
  and and_1 (and_1_out, Enn, power, En);
  Register #(.width(32)) PC (.D(multiplexer_1_out), .en(and_1_out), .Q(PC_q), .clk(CLK), .clr(RST));
  Multiplexer #(.width(32)) multiplexer_1 (
    .in0(adder_1_out), .in1(multiplexer_5_out), .out(multiplexer_1_out), .sel(Success));  // open: en
  InstCounter instcounter_1 (
    .CLK(CLK), .Halt(and_2_out), .Success(Success), .Clr(RST), .IstrIn(Istr1), .J(\无条件分支指令数 ),
    .B(\有条件分支指令数 ), .Br(\有条件分支成功跳转 ), .All(\总周期数 ));  // open: LESS, Brcount
  and and_2 (and_2_out, Enn, En);
  ROM #(.addrWidth(10), .dataWidth(32)) rom_1 (.addr(PC_q[9:0]), .data(rom_1_data));  // open: sel
  Adder #(.width(32)) adder_1 (.a({{22{1'b0}}, PC_q[9:0]}), .b(32'h1), .out(adder_1_out));  // open: cin, cout
  and and_3 (and_3_out, power, Enn);
  Button \u_总复位  (.out(RST));
  Clock clock_1 (.out(CLK));
  Button \continue  (.out(PAU));
  IF_ID if_id_1 (
    .InstrIn(rom_1_data), .\传输状态In (and_3_out), .CLK(CLK), .InstrOut(if_id_1_instrout), .\同步清零 (Success),
    .PcIn(adder_1_out), .PcOut(if_id_1_pcout), .\异步清零 (1'b0));  // open: 传输状态Out
  IstrSplit istrsplit_1 (
    .in_1(if_id_1_instrout), .OP(istrsplit_1_op), .FUNC(istrsplit_1_func), .RD(istrsplit_1_rd),
    .IMM16(istrsplit_1_imm16), .IMM26(istrsplit_1_imm26), .SHAMT(istrsplit_1_shamt), .RS(istrsplit_1_rs),
    .RT(istrsplit_1_rt), .Syscall(istrsplit_1_syscall));
  Hex_Digit_Display hex_digit_display_1 (.value(SyscallOut[31:28]));  // open: dp
  Hex_Digit_Display hex_digit_display_2 (.value(SyscallOut[27:24]));  // open: dp
  Controller controller_1 (
    .OP(istrsplit_1_op), .RS(undriven), .FUNCT(istrsplit_1_func), .Alu(controller_1_alu),
    .M1(controller_1_m1), .RegWrite(WE_ID), .M2(controller_1_m2), .DmStr(controller_1_dmstr),
    .M3(controller_1_m3), .DmSel(controller_1_dmsel), .M4(controller_1_m4), .DmLd(controller_1_dmld),
    .Halt(controller_1_halt), .Disp(controller_1_disp), .Syscall(istrsplit_1_syscall),
    .Sha(controller_1_sha), .out_17(Istr), .RT(registerfile_1_p7), .Pause(controller_1_pause));  // open: BrCount, BCount, JCount
  ConflitCtrl conflitctrl_1 (
    .RS(istrsplit_1_rs), .RD_EX(multiplexer_4_out), .RT(istrsplit_1_rt), .Istr1(Istr1),
    .RD_ID(istrsplit_1_rd), .IF_ID_STOP(power), .ID_EX_CLEAR(conflitctrl_1_id_ex_clear),
    .RD_MEM(ex_mem_1__5bout1), .Istr2(Istr2), .Istr(Istr));
  Hex_Digit_Display hex_digit_display_3 (.value(SyscallOut[19:16]));  // open: dp
  Hex_Digit_Display hex_digit_display_4 (.value(SyscallOut[23:20]));  // open: dp
  Hex_Digit_Display hex_digit_display_5 (.value(SyscallOut[11:8]));  // open: dp
  Hex_Digit_Display hex_digit_display_6 (.value(SyscallOut[15:12]));  // open: dp
  SignExtend signextend_1 (.in_1(istrsplit_1_imm16), .out_2(signextend_1_out_2));
  Hex_Digit_Display hex_digit_display_7 (.value(SyscallOut[3:0]));  // open: dp
  Hex_Digit_Display hex_digit_display_8 (.value(SyscallOut[7:4]));  // open: dp
  // RegisterFile registerfile_1: pin names not known; wires that end beside it: registerfile_1_p1, CLK, WE, registerfile_1_p4, istrsplit_1_rs, istrsplit_1_rt, registerfile_1_p7
  ID_EX id_ex_1 (
    ._32bIn3({{6{1'b0}}, istrsplit_1_imm26}), ._32bOut3(id_ex_1__32bout3), ._32bIn4(if_id_1_pcout),
    ._32bOut4(id_ex_1__32bout4), .\传输状态In (Enn), .CLK(CLK), .\同步清零 (or_1_out), ._32bIn2(signextend_1_out_2),
    ._32bOut2(id_ex_1__32bout2), ._32bIn1({{27{1'b0}}, istrsplit_1_shamt}), ._32bOut1(id_ex_1__32bout1),
    .R2In(registerfile_1_p7), .R2Out(id_ex_1_r2out), .R1In(undriven), .R1Out(id_ex_1_r1out),
    ._5bIn2(istrsplit_1_rt), ._5bOut2(id_ex_1__5bout2), ._5bIn1(istrsplit_1_rd), ._5bOut1(id_ex_1__5bout1),
    .M2In(controller_1_m2), .M2Out(id_ex_1_m2out), .M1In(controller_1_m1), .M1Out(id_ex_1_m1out),
    .DispIn(controller_1_disp), .DispOut(id_ex_1_dispout), .M4In(controller_1_m4), .M4Out(id_ex_1_m4out),
    .M3In(controller_1_m3), .M3Out(id_ex_1_m3out), .RegWriteIn(WE_ID), .RegWriteOut(WE_DE),
    .DmStrIn(controller_1_dmstr), .DmStrOut(id_ex_1_dmstrout), .shaIn(controller_1_sha),
    .shaOut(id_ex_1_shaout), .DmLdIn(controller_1_dmld), .DmLdOut(id_ex_1_dmldout),
    .DmSelIn(controller_1_dmsel), .DmSelOut(id_ex_1_dmselout), .AluIn(controller_1_alu),
    .AluOut(id_ex_1_aluout), .haltIn(controller_1_halt), .haltOut(id_ex_1_haltout), .\异步清零 (1'b0),
    .IstrIn(Istr), .IstrOut(Istr1), .pauseIn(controller_1_pause), .pauseOut(id_ex_1_pauseout));  // open: 传输状态Out
  or or_1 (or_1_out, Success, conflitctrl_1_id_ex_clear);
  // Probe on \总周期数 
  // Probe on \无条件分支指令数 
  // Probe on \有条件分支指令数 
  // Probe on \有条件分支成功跳转 
  Multiplexer #(.width(32)) multiplexer_2 (
    .in0(id_ex_1_r1out), .in1(id_ex_1_r2out), .out(multiplexer_2_out), .sel(id_ex_1_shaout));  // open: en
  Multiplexer #(.select(2), .width(32)) multiplexer_3 (
    .in0(id_ex_1_r2out), .in1(id_ex_1__32bout2), .in2(id_ex_1__32bout1), .in3(id_ex_1_r1out),
    .out(multiplexer_3_out), .sel(id_ex_1_m2out));  // open: en
  Multiplexer #(.select(2), .width(5)) multiplexer_4 (
    .in0(id_ex_1__5bout2), .in1(id_ex_1__5bout1), .in2({5{1'b1}}), .in3({5{1'b0}}), .out(multiplexer_4_out),
    .sel(id_ex_1_m1out));  // open: en
  Adder #(.width(32)) adder_2 (.a(id_ex_1__32bout4), .b(id_ex_1__32bout2), .out(adder_2_out));  // open: cin, cout
  ALU alu_1 (
    .AluOP(id_ex_1_aluout), .X(multiplexer_2_out), .Equal(alu_1_equal), .Result(alu_1_result),
    .Y(multiplexer_3_out));  // open: Signed_Overflow, Result_2, UnSigned_Overflow
  Multiplexer #(.select(2), .width(32)) multiplexer_5 (
    .in0(id_ex_1__32bout4), .in1(id_ex_1__32bout3), .in2(adder_2_out), .in3(multiplexer_2_out),
    .out(multiplexer_5_out), .sel(id_ex_1_m4out));  // open: en
  Comparator #(.width(2), .mode("unsigned")) comparator_1 (.a(id_ex_1_m4out), .b(2'b00), .gt(Success));  // open: eq, lt
  EX_MEM ex_mem_1 (
    ._5bIn1(multiplexer_4_out), ._5bOut1(ex_mem_1__5bout1), .DmSelIn(id_ex_1_dmselout),
    .DmSelOut(ex_mem_1_dmselout), .DmLdIn(id_ex_1_dmldout), .DmLdOut(ex_mem_1_dmldout),
    .DmStrIn(id_ex_1_dmstrout), .DmStrOut(ex_mem_1_dmstrout), .RegWriteIn(WE_DE), .RegWriteOut(WE_ME),
    ._32bIn2(alu_1_result), ._32bOut2(ex_mem_1__32bout2), .M3In(id_ex_1_m3out), .M3Out(ex_mem_1_m3out),
    ._32bIn3(id_ex_1_r2out), ._32bOut3(ex_mem_1__32bout3), ._1bIn1(alu_1_equal), .\传输状态In (Enn),
    .DispIn(id_ex_1_dispout), .DispOut(ex_mem_1_dispout), .CLK(CLK), .\同步清零 (1'b0),
    ._32bIn4(id_ex_1__32bout4), ._32bOut4(ex_mem_1__32bout4), .haltIn(id_ex_1_haltout),
    .haltOut(ex_mem_1_haltout), .\异步清零 (1'b0), .IstrIn(Istr1), .IstrOut(Istr2), .pauseIn(id_ex_1_pauseout),
    .pauseOut(ex_mem_1_pauseout));  // open: _32bIn1, _32bOut1, _1bOut1, 传输状态Out, _1bOut2, _1bIn2
  romshm romshm_1 (.DataIn(ex_mem_1__32bout3), .selIn(ex_mem_1_dmselout), .DataOut(romshm_1_dataout));
  Register #(.width(32)) register_1 (.D(romshm_1_dataout), .en(ex_mem_1_dispout), .Q(SyscallOut), .clk(CLK), .clr(RST));
  // MIPS_RAM mips_ram_1: pin names not known; wires that end beside it: ex_mem_1__32bout2[21:2], romshm_1_dataout, ex_mem_1_dmstrout, ex_mem_1_dmselout, CLK, ex_mem_1_dmldout, RST, mips_ram_1_p8
  MEM_WB mem_wb_1 (
    ._1bIn1(WE_ME), ._1bOut1(WE), ._32bIn1(mips_ram_1_p8), ._32bOut1(mem_wb_1__32bout1),
    ._32bIn2(ex_mem_1__32bout4), ._32bOut2(mem_wb_1__32bout2), ._5bIn1(ex_mem_1__5bout1),
    ._5bOut1(registerfile_1_p4), .M3In(ex_mem_1_m3out), .M3Out(mem_wb_1_m3out), .\传输状态In (Enn), .CLK(CLK),
    .\同步清零 (1'b0), ._32bIn3(ex_mem_1__32bout2), ._32bOut3(mem_wb_1__32bout3), .haltIn(ex_mem_1_haltout),
    .haltOut(mem_wb_1_haltout), .\异步清零 (1'b0), .IstrIn(Istr2), .IstrOut(Istr3), .pauseIn(ex_mem_1_pauseout),
    .pauseOut(mem_wb_1_pauseout));  // open: 传输状态Out
  lock lock_1 (.en(mem_wb_1_haltout), .Clk(CLK), .rst(RST), .En_2(En), .pauseIn(mem_wb_1_pauseout), .pause(Pause));
  Multiplexer #(.select(2), .width(32)) multiplexer_6 (
    .in0(mem_wb_1__32bout3), .in1(mem_wb_1__32bout1), .in2(mem_wb_1__32bout2), .out(registerfile_1_p1),
    .sel(mem_wb_1_m3out));  // open: in3, en

  // Notes on the sheet:
  //   指令存储器
  //   contents of rom_1 (hex, n*v repeats v):
  //   20110001 8000c05 20110001 20120002 20130003 8000c09 20110001 20120002 20130003 8000c0d 20110001
  //   20120002 20130003 8000c11 20110001 20120002 20130003 c000ce4 20100001 20110001 118fc0 112020
  //   20020022 c 118882 12200001 8000c15 112020 20020022 c 20110001 118880 112020 20020022 c 12200001
  //   8000c1f 20110001 118fc0 112020 20020022 c 1188c3 112020 20020022 c 118903 112020 20020022 c 118903
  //   112020 20020022 c 118903 112020 20020022 c 118903 112020 20020022 c 118903 112020 20020022 c 118903
  //   112020 20020022 c 118903 112020 20020022 c 20100001 109fc0 139fc3 8021 2012000c 24160003 26100001
  //   3210000f 20080008 20090001 139900 2709825 132020 20020022 c 1094022 1500fff9 22100001 2018000f
  //   2188024 108700 20080008 20090001 139902 2709825 132021 20020022 c 1094022 1500fff9 108702 2c9b022
  //   12c00001 8000c50 4020 1084027 84400 3508ffff 82021 20020022 c 2010ffff 20110000 ae300000 22100001
  //   22310004 ae300000 22100001 22310004 ae300000 22100001 22310004 ae300000 22100001 22310004 ae300000
  //   22100001 22310004 ae300000 22100001 22310004 ae300000 22100001 22310004 ae300000 22100001 22310004
  //   ae300000 22100001 22310004 ae300000 22100001 22310004 ae300000 22100001 22310004 ae300000 22100001
  //   22310004 ae300000 22100001 22310004 ae300000 22100001 22310004 ae300000 22100001 22310004 ae300000
  //   22100001 22310004 22100001 8020 2011003c 8e130000 8e340000 274402a 11000002 ae330000 ae140000
  //   2231fffc 1611fff8 102020 20020022 c 22100004 2011003c 1611fff2 20020032 c 20080001 20090003 20110876
  //   118d00 112020 20020022 c 200b0008 1118806 1318806 112020 20020022 c 216bffff 1560fff9 20090000
  //   200b0020 20110000 20120001 a1310000 112020 20020022 c 2328820 21290001 216bffff 1560fff8 200b0008
  //   20090000 8d310000 112020 20020022 c 21290004 216bffff 1560fff9 2011fff1 112020 20020022 c 22310001
  //   620fffb 2002000a c 20100000 22100001 102020 20020022 c 22100002 102020 20020022 c 22100003 102020
  //   20020022 c 22100004 102020 20020022 c 22100005 102020 20020022 c 22100006 102020 20020022 c 22100007
  //   102020 20020022 c 22100008 102020 20020022 20020022 c 3e00008
  //   数码管输出应该用寄存器锁存，否则显示数据只能一闪而过
  //   可以通过项目增加Logisim库的方式将前几次实验完成的电路作为子电路引入到本电路中使用
  //   寄存器文件
  //   数码管输出
  //   总复位信号应将除ROM以外所有存储组件全部清零
  //   M1
  //   sha
  //   M2
  //   M4
  //   数据存储器
  //   M3
endmodule

// Sign Extend
module SignExtend (
  input  [15:0] in_1,
  output [31:0] out_2
);


  assign out_2 = {{17{in_1[15]}}, in_1[14:0]};
endmodule

module IstrSplit (
  input  [31:0] in_1,
  output [5:0] OP,
  output [5:0] FUNC,
  output [4:0] RS,
  output [4:0] RT,
  output [4:0] RD,
  output [15:0] IMM16,
  output [25:0] IMM26,
  output [4:0] SHAMT,
  output Syscall
);

  wire comparator_2_eq, ISR, NR;

  Comparator #(.width(6)) comparator_1 (.a(in_1[31:26]), .b({6{1'b0}}), .eq(ISR));  // open: gt, lt
  Comparator #(.width(6)) comparator_2 (.a(in_1[5:0]), .b(6'b001100), .eq(comparator_2_eq));  // open: gt, lt
  not not_1 (NR, ISR);
  and and_1 (Syscall, comparator_2_eq, ISR);
  Multiplexer #(.width(5)) multiplexer_1 (.in0(in_1[25:21]), .in1(5'b00010), .out(RS), .sel(Syscall));  // open: en
  Multiplexer #(.width(5)) multiplexer_2 (.in0(in_1[20:16]), .in1(5'b00100), .out(RT), .sel(Syscall));  // open: en

  assign FUNC = in_1[5:0];
  assign IMM16 = in_1[15:0];
  assign IMM26 = in_1[25:0];
  assign OP = in_1[31:26];
  assign RD = in_1[15:11];
  assign SHAMT = in_1[10:6];

  // Other names for the same wires on the sheet: RT_t[4:0] = in_1[20:16]; RS_t[4:0] = in_1[25:21]; SYSCAL = Syscall
endmodule

module Controller (
  input  [5:0] OP,
  input  Syscall,
  input  [5:0] FUNCT,
  input  [31:0] RS,
  input  [31:0] RT,
  output [3:0] Alu,
  output [1:0] M2,
  output DmLd,
  output Sha,
  output BrCount,
  output Pause,
  output RegWrite,
  output [1:0] M3,
  output [3:0] DmSel,
  output Halt,
  output BCount,
  output [27:0] out_17,
  output Disp,
  output JCount,
  output [1:0] M1,
  output [1:0] M4,
  output DmStr
);

  wire add_t, and_29_out, and_30_out, and_31_out, and_32_out, and_33_out, and_t, cmpu, comparator_3_eq,
       comparator_4_eq, comparator_5_eq, comparator_6_eq, comparator_7_eq, comparator_8_eq, comparator_9_eq,
       comparator_10_eq, comparator_11_eq, comparator_12_eq, comparator_13_eq, comparator_14_eq,
       comparator_15_eq, comparator_17_eq, comparator_18_eq, comparator_19_eq, comparator_20_eq,
       comparator_21_eq, comparator_22_eq, comparator_23_eq, comparator_24_eq, comparator_25_eq,
       comparator_26_eq, comparator_27_eq, comparator_28_eq, comparator_29_eq, comparator_30_eq,
       comparator_31_eq, comparator_32_eq, comparator_33_eq, comparator_34_eq, EQUAL, ISR, LESS, NR, or_t,
       sra_t, srl_t;
  wire [3:0] sel_t;

  Comparator #(.width(32)) comparator_1 (.a(RS), .b({32{1'b0}}), .lt(LESS));  // open: gt, eq
  Comparator #(.width(6)) comparator_2 (.a(OP), .b({6{1'b0}}), .eq(ISR));  // open: gt, lt
  not not_1 (NR, ISR);
  Comparator #(.width(6)) comparator_3 (.a(OP), .b(6'b001000), .eq(comparator_3_eq));  // open: gt, lt
  Comparator #(.width(6)) comparator_4 (.a(OP), .b(6'b001001), .eq(comparator_4_eq));  // open: gt, lt
  Comparator #(.width(6)) comparator_5 (.a(OP), .b(6'b001100), .eq(comparator_5_eq));  // open: gt, lt
  Comparator #(.width(6)) comparator_6 (.a(OP), .b(6'b001101), .eq(comparator_6_eq));  // open: gt, lt
  Comparator #(.width(6)) comparator_7 (.a(OP), .b(6'b100011), .eq(comparator_7_eq));  // open: gt, lt
  Comparator #(.width(6)) comparator_8 (.a(OP), .b(6'b101011), .eq(comparator_8_eq));  // open: gt, lt
  Comparator #(.width(6)) comparator_9 (.a(OP), .b(6'b000100), .eq(comparator_9_eq));  // open: gt, lt
  Comparator #(.width(6)) comparator_10 (.a(OP), .b(6'b000101), .eq(comparator_10_eq));  // open: gt, lt
  Comparator #(.width(6)) comparator_11 (.a(OP), .b(6'b001010), .eq(comparator_11_eq));  // open: gt, lt
  Comparator #(.width(6)) comparator_12 (.a(OP), .b(6'b000010), .eq(comparator_12_eq));  // open: gt, lt
  Comparator #(.width(6)) comparator_13 (.a(OP), .b(6'b000011), .eq(comparator_13_eq));  // open: gt, lt
  Comparator #(.width(6)) comparator_14 (.a(OP), .b(6'b101000), .eq(comparator_14_eq));  // open: gt, lt
  Comparator #(.width(6)) comparator_15 (.a(OP), .b(6'b000001), .eq(comparator_15_eq));  // open: gt, lt
  and and_1 (out_17[0], comparator_3_eq, NR);
  and and_2 (out_17[1], comparator_4_eq, NR);
  and and_3 (out_17[2], comparator_5_eq, NR);
  and and_4 (out_17[3], comparator_6_eq, NR);
  and and_5 (DmLd, comparator_7_eq, NR);
  and and_6 (out_17[5], comparator_8_eq, NR);
  and and_7 (out_17[6], comparator_9_eq, NR);
  and and_8 (out_17[7], comparator_10_eq, NR);
  and and_9 (out_17[8], comparator_11_eq, NR);
  and and_10 (out_17[9], comparator_12_eq, NR);
  and and_11 (M3[1], comparator_13_eq, NR);
  and and_12 (out_17[11], comparator_14_eq, NR);
  and and_13 (out_17[12], comparator_15_eq, NR);
  Comparator #(.width(32)) comparator_16 (.a(RS), .b(RT), .eq(EQUAL));  // open: gt, lt
  Comparator #(.width(6)) comparator_17 (.a(FUNCT), .b(6'b100000), .eq(comparator_17_eq));  // open: gt, lt
  Comparator #(.width(6)) comparator_18 (.a(FUNCT), .b(6'b100001), .eq(comparator_18_eq));  // open: gt, lt
  Comparator #(.width(6)) comparator_19 (.a(FUNCT), .b(6'b100100), .eq(comparator_19_eq));  // open: gt, lt
  Comparator #(.width(6)) comparator_20 (.a(FUNCT), .b(6'b100010), .eq(comparator_20_eq));  // open: gt, lt
  Comparator #(.width(6)) comparator_21 (.a(FUNCT), .b(6'b100101), .eq(comparator_21_eq));  // open: gt, lt
  Comparator #(.width(6)) comparator_22 (.a(FUNCT), .b(6'b100111), .eq(comparator_22_eq));  // open: gt, lt
  Comparator #(.width(6)) comparator_23 (.a(FUNCT), .b(6'b101010), .eq(comparator_23_eq));  // open: gt, lt
  Comparator #(.width(6)) comparator_24 (.a(FUNCT), .b(6'b101011), .eq(comparator_24_eq));  // open: gt, lt
  Comparator #(.width(6)) comparator_25 (.a(FUNCT), .b(6'b000110), .eq(comparator_25_eq));  // open: gt, lt
  Comparator #(.width(6)) comparator_26 (.a(FUNCT), .b(6'b000111), .eq(comparator_26_eq));  // open: gt, lt
  Comparator #(.width(6)) comparator_27 (.a(FUNCT), .b({6{1'b0}}), .eq(comparator_27_eq));  // open: gt, lt
  Comparator #(.width(6)) comparator_28 (.a(FUNCT), .b(6'b000011), .eq(comparator_28_eq));  // open: gt, lt
  Comparator #(.width(6)) comparator_29 (.a(FUNCT), .b(6'b000010), .eq(comparator_29_eq));  // open: gt, lt
  Comparator #(.width(6)) comparator_30 (.a(FUNCT), .b(6'b001000), .eq(comparator_30_eq));  // open: gt, lt
  Comparator #(.width(6)) comparator_31 (.a(FUNCT), .b(6'b001100), .eq(comparator_31_eq));  // open: gt, lt
  and and_14 (out_17[13], comparator_17_eq, ISR);
  and and_15 (out_17[14], comparator_18_eq, ISR);
  and and_16 (out_17[15], comparator_19_eq, ISR);
  and and_17 (out_17[16], comparator_20_eq, ISR);
  and and_18 (out_17[17], comparator_21_eq, ISR);
  and and_19 (out_17[18], comparator_22_eq, ISR);
  and and_20 (out_17[19], comparator_23_eq, ISR);
  and and_21 (out_17[20], comparator_24_eq, ISR);
  and and_22 (out_17[21], comparator_25_eq, ISR);
  and and_23 (out_17[22], comparator_26_eq, ISR);
  and and_24 (out_17[23], comparator_27_eq, ISR);
  and and_25 (out_17[24], comparator_28_eq, ISR);
  and and_26 (out_17[25], comparator_29_eq, ISR);
  and and_27 (out_17[26], comparator_30_eq, ISR);
  and and_28 (out_17[27], comparator_31_eq, ISR);
  or or_1 (and_t, out_17[15], out_17[2]);
  or or_2 (or_t, out_17[17], out_17[3]);
  or or_3 (sra_t, out_17[24], out_17[22]);
  or or_4 (srl_t, out_17[21], out_17[25]);
  or or_5 (add_t, out_17[13], out_17[0], out_17[1], out_17[14], DmLd, out_17[5], out_17[11]);
  or or_6 (cmpu, out_17[19], out_17[20], out_17[8]);
  nor nor_1 (RegWrite, out_17[5], out_17[6], out_17[7], out_17[9], out_17[27], out_17[26], out_17[12], out_17[11]);
  Multiplexer #(.select(2), .width(4)) multiplexer_1 (
    .in0(4'b0001), .in1(4'b0010), .in2(4'b0100), .in3(4'b1000), .out(sel_t), .sel(RS[1:0]));  // open: en
  Multiplexer #(.width(4)) multiplexer_2 (.in0(4'b1111), .in1(sel_t), .out(DmSel), .sel(out_17[11]));  // open: en
  or or_7 (M1[1], out_17[5], M3[1], out_17[11]);
  or or_8 (DmStr, out_17[5], out_17[11]);
  or or_9 (M1[0], out_17[13], out_17[14], out_17[15], out_17[23], out_17[24], out_17[25], out_17[16], out_17[17], out_17[18], out_17[5], out_17[19], out_17[20], out_17[21], out_17[22], out_17[11]);
  or or_10 (M2[1], out_17[23], out_17[21], out_17[25], M3[1], out_17[24], out_17[22]);
  or or_11 (M2[0], out_17[22], out_17[1], out_17[2], out_17[0], out_17[3], DmLd, out_17[5], out_17[11], M3[1], out_17[8], out_17[21]);
  and and_29 (and_29_out, EQUAL, out_17[6]);
  and and_30 (and_30_out, ~EQUAL, out_17[7]);  // AND_Gate
  and and_31 (and_31_out, out_17[12], LESS);
  or or_12 (M4[1], and_29_out, and_30_out, and_31_out, out_17[26]);
  or or_13 (JCount, out_17[26], M3[1], out_17[9]);
  AluCtrl aluctrl_1 (
    .add(add_t), .sub(out_17[16]), .\and (and_t), .\or (or_t), .sra(sra_t), .srl(srl_t), .sll(out_17[23]),
    .cmpu(cmpu), .\nor (out_17[18]), .A3(Alu[3]), .A2(Alu[2]), .A1(Alu[1]), .A0(Alu[0]));
  Comparator #(.width(32)) comparator_32 (.a(RS), .b(32'h22), .eq(comparator_32_eq));  // open: gt, lt
  Comparator #(.width(32)) comparator_33 (.a(RS), .b(32'ha), .eq(comparator_33_eq));  // open: gt, lt
  Comparator #(.width(32)) comparator_34 (.a(RS), .b(32'h32), .eq(comparator_34_eq));  // open: gt, lt
  and and_32 (and_32_out, EQUAL, out_17[6]);
  or or_14 (BrCount, and_32_out, and_33_out);
  and and_33 (and_33_out, ~EQUAL, out_17[7]);  // AND_Gate
  or or_15 (BCount, out_17[6], out_17[7]);
  or or_16 (Sha, out_17[23], out_17[22], out_17[25], out_17[21], out_17[24]);
  and and_34 (Disp, out_17[27], comparator_32_eq);
  and and_35 (Halt, out_17[27], comparator_33_eq);
  and and_36 (Pause, out_17[27], comparator_34_eq);

  assign M3[0] = DmLd;
  assign M4[0] = JCount;
  assign {out_17[10], out_17[4]} = {M3[1], DmLd};

  // Other names for the same wires on the sheet: ADDI = out_17[0];
  //   Istr[27:0] = {out_17[27:11], M3[1], out_17[9:5], DmLd, out_17[3:0]}; ADDIU = out_17[1]; ANDI = out_17[2];
  //   ORI = out_17[3]; SW = out_17[5]; BEQ = out_17[6]; BNE = out_17[7]; SLTI = out_17[8]; J = out_17[9];
  //   SB = out_17[11]; BLTZ = out_17[12]; ADD = out_17[13]; ADDU = out_17[14]; AND = out_17[15]; SUB = out_17[16];
  //   OR = out_17[17]; NOR = out_17[18]; SLT = out_17[19]; SLTU = out_17[20]; SRLV = out_17[21]; SRAV = out_17[22];
  //   SLL = out_17[23]; SRA = out_17[24]; SRL = out_17[25]; JR = out_17[26]; SYSCAL = out_17[27]; LD = DmLd;
  //   LW = DmLd; M30 = DmLd; JAL = M3[1]; M40 = JCount; SEL[3:0] = DmSel; STR = DmStr; WE = RegWrite
endmodule

module AluCtrl (
  input  add,
  input  sub,
  input  \and ,
  input  \or ,
  input  sra,
  input  srl,
  input  sll,
  input  cmpu,
  input  \nor ,
  output A3,
  output A2,
  output A1,
  output A0
);

  wire and_2_out, and_3_out, and_4_out, and_5_out, and_6_out, and_7_out, and_8_out, and_9_out, not_1_out,
       not_2_out, not_3_out, not_4_out, not_5_out, not_6_out, not_7_out, not_8_out, not_9_out, not_10_out,
       not_11_out, not_12_out, not_13_out, not_14_out, not_15_out, not_16_out, not_17_out, not_18_out,
       not_19_out, not_20_out, not_21_out, not_22_out, not_23_out, not_24_out, not_25_out, not_26_out,
       not_27_out, not_28_out, not_29_out, not_30_out, not_31_out, not_32_out, not_33_out, not_34_out,
       not_35_out, not_36_out, not_37_out, not_38_out, not_39_out, not_40_out, not_41_out, not_42_out,
       not_43_out, not_44_out, not_45_out, not_46_out, not_47_out, not_48_out, not_49_out, not_50_out,
       not_51_out, not_52_out, not_53_out, not_54_out;

  not not_1 (not_1_out, add);
  not not_2 (not_2_out, sub);
  not not_3 (not_3_out, \and );
  not not_4 (not_4_out, sra);
  not not_5 (not_5_out, srl);
  not not_6 (not_6_out, sll);
  not not_7 (not_7_out, \or );
  not not_8 (not_8_out, sra);
  not not_9 (not_9_out, srl);
  not not_10 (not_10_out, sll);
  not not_11 (not_11_out, cmpu);
  not not_12 (not_12_out, \nor );
  not not_13 (not_13_out, \or );
  not not_14 (not_14_out, sra);
  not not_15 (not_15_out, srl);
  not not_16 (not_16_out, sll);
  not not_17 (not_17_out, \nor );
  not not_18 (not_18_out, \or );
  not not_19 (not_19_out, sra);
  not not_20 (not_20_out, srl);
  not not_21 (not_21_out, sll);
  not not_22 (not_22_out, \nor );
  not not_23 (not_23_out, \or );
  not not_24 (not_24_out, sra);
  not not_25 (not_25_out, srl);
  not not_26 (not_26_out, sll);
  not not_27 (not_27_out, \nor );
  not not_28 (not_28_out, add);
  not not_29 (not_29_out, sub);
  not not_30 (not_30_out, \and );
  not not_31 (not_31_out, \or );
  not not_32 (not_32_out, sra);
  not not_33 (not_33_out, srl);
  not not_34 (not_34_out, sll);
  not not_35 (not_35_out, \nor );
  not not_36 (not_36_out, add);
  not not_37 (not_37_out, \or );
  not not_38 (not_38_out, sra);
  not not_39 (not_39_out, sll);
  not not_40 (not_40_out, cmpu);
  not not_41 (not_41_out, add);
  not not_42 (not_42_out, sub);
  not not_43 (not_43_out, \and );
  not not_44 (not_44_out, \or );
  not not_45 (not_45_out, sra);
  not not_46 (not_46_out, srl);
  not not_47 (not_47_out, sll);
  not not_48 (not_48_out, \nor );
  not not_49 (not_49_out, sub);
  not not_50 (not_50_out, \or );
  not not_51 (not_51_out, srl);
  not not_52 (not_52_out, sll);
  not not_53 (not_53_out, cmpu);
  not not_54 (not_54_out, \nor );
  and and_1 (A3, not_1_out, not_2_out, not_3_out, not_4_out, not_5_out, not_6_out);
  and and_2 (and_2_out, not_7_out, not_8_out, not_9_out, not_10_out, not_11_out, not_12_out);
  and and_3 (and_3_out, \and , not_13_out, not_14_out, not_15_out, not_16_out, not_17_out);
  and and_4 (and_4_out, sub, not_18_out, not_19_out, not_20_out, not_21_out, not_22_out);
  and and_5 (and_5_out, add, not_23_out, not_24_out, not_25_out, not_26_out, not_27_out);
  and and_6 (and_6_out, not_28_out, not_29_out, not_30_out, not_31_out, not_32_out, not_33_out, not_34_out, not_35_out);
  and and_7 (and_7_out, not_36_out, not_37_out, not_38_out, not_39_out, not_40_out);
  and and_8 (and_8_out, not_41_out, not_42_out, not_43_out, not_44_out, not_45_out, not_46_out, not_47_out, not_48_out);
  and and_9 (and_9_out, not_49_out, not_50_out, not_51_out, not_52_out, not_53_out, not_54_out);
  or or_1 (A2, and_2_out, and_3_out, and_4_out, and_5_out);
  or or_2 (A1, and_6_out, and_7_out);
  or or_3 (A0, and_8_out, and_9_out);
endmodule

module InstCounter (
  input  CLK,
  input  Halt,
  input  Success,
  input  Clr,
  input  LESS,
  input  Brcount,
  input  [27:0] IstrIn,
  output [15:0] J,
  output [15:0] B,
  output [15:0] Br,
  output [15:0] All
);

  wire BC, BrC, JC, or_2_out;
  wire [15:0] adder_1_out, adder_2_out, adder_3_out, adder_4_out, multiplexer_1_out, multiplexer_2_out,
       multiplexer_3_out;

  Register #(.width(16)) register_1 (.D(adder_1_out), .en(Halt), .Q(All), .clk(CLK), .clr(Clr));
  Register #(.width(16)) register_2 (.D(adder_2_out), .en(Halt), .Q(J), .clk(CLK), .clr(Clr));
  Register #(.width(16)) register_3 (.D(adder_3_out), .en(Halt), .Q(B), .clk(CLK), .clr(Clr));
  Register #(.width(16)) register_4 (.D(adder_4_out), .en(Halt), .Q(Br), .clk(CLK), .clr(Clr));
  Adder #(.width(16)) adder_1 (.a(All), .b(16'h1), .out(adder_1_out));  // open: cin, cout
  Adder #(.width(16)) adder_2 (.a(J), .b(multiplexer_1_out), .out(adder_2_out));  // open: cin, cout
  Multiplexer #(.width(16)) multiplexer_1 (
    .in0({16{1'b0}}), .in1(16'h1), .out(multiplexer_1_out), .sel(JC));  // open: en
  Adder #(.width(16)) adder_3 (.a(B), .b(multiplexer_2_out), .out(adder_3_out));  // open: cin, cout
  Multiplexer #(.width(16)) multiplexer_2 (
    .in0({16{1'b0}}), .in1(16'h1), .out(multiplexer_2_out), .sel(BC));  // open: en
  Adder #(.width(16)) adder_4 (.a(Br), .b(multiplexer_3_out), .out(adder_4_out));  // open: cin, cout
  Multiplexer #(.width(16)) multiplexer_3 (
    .in0({16{1'b0}}), .in1(16'h1), .out(multiplexer_3_out), .sel(BrC));  // open: en
  or or_1 (BC, IstrIn[6], IstrIn[7], IstrIn[12]);
  and and_1 (BrC, BC, Success);
  or or_2 (or_2_out, IstrIn[26], IstrIn[10], IstrIn[9]);
  and and_2 (JC, or_2_out, Success);

  // Other names for the same wires on the sheet: ADDI = IstrIn[0]; Istr[27:0] = IstrIn; ADDIU = IstrIn[1];
  //   ANDI = IstrIn[2]; ORI = IstrIn[3]; LW = IstrIn[4]; SW = IstrIn[5]; BEQ = IstrIn[6]; BNE = IstrIn[7];
  //   SLTI = IstrIn[8]; JI = IstrIn[9]; JAL = IstrIn[10]; SB = IstrIn[11]; BLTZ = IstrIn[12]; ADD = IstrIn[13];
  //   ADDU = IstrIn[14]; AND = IstrIn[15]; SUB = IstrIn[16]; OR = IstrIn[17]; NOR = IstrIn[18]; SLT = IstrIn[19];
  //   SLTU = IstrIn[20]; SRLV = IstrIn[21]; SRAV = IstrIn[22]; SLL = IstrIn[23]; SRA = IstrIn[24]; SRL = IstrIn[25];
  //   JR = IstrIn[26]; SYSCAL = IstrIn[27]
endmodule

module lock (
  input  en,
  input  pauseIn,
  input  Clk,
  input  rst,
  output En_2,
  output pause
);

  wire register_1_q, register_2_q;

  Register #(.width(1)) register_1 (.D(en), .en(En_2), .Q(register_1_q), .clk(Clk), .clr(rst));
  not not_1 (En_2, register_1_q);
  not not_2 (pause, register_2_q);
  Register #(.width(1)) register_2 (.D(pauseIn), .en(pause), .Q(register_2_q), .clk(Clk), .clr(rst));
endmodule

module IF_ID (
  input  [31:0] PcIn,
  input  [31:0] InstrIn,
  input  \传输状态In ,
  input  CLK,
  input  \同步清零 ,
  input  \异步清零 ,
  output [31:0] PcOut,
  output [31:0] InstrOut,
  output \传输状态Out 
);

  wire multiplexer_3_out;
  wire [31:0] multiplexer_1_out, multiplexer_2_out;

  Multiplexer #(.width(32), .enable("false")) multiplexer_1 (
    .in0(PcIn), .in1({32{1'b0}}), .out(multiplexer_1_out), .sel(\同步清零 ));
  Multiplexer #(.width(32), .enable("false")) multiplexer_2 (
    .in0(InstrIn), .in1({32{1'b0}}), .out(multiplexer_2_out), .sel(\同步清零 ));
  Multiplexer #(.enable("false")) multiplexer_3 (.in0(\传输状态In ), .in1(1'b0), .out(multiplexer_3_out), .sel(\同步清零 ));
  Register #(.width(32)) register_1 (.D(multiplexer_1_out), .en(\传输状态In ), .Q(PcOut), .clk(CLK), .clr(\异步清零 ));
  Register #(.width(32)) register_2 (.D(multiplexer_2_out), .en(\传输状态In ), .Q(InstrOut), .clk(CLK), .clr(\异步清零 ));
  Register #(.width(1)) register_3 (.D(multiplexer_3_out), .en(\传输状态In ), .Q(\传输状态Out ), .clk(CLK), .clr(\异步清零 ));
endmodule

module ID_EX (
  input  [27:0] IstrIn,
  input  pauseIn,
  input  [4:0] _5bIn1,
  input  haltIn,
  input  [4:0] _5bIn2,
  input  [3:0] AluIn,
  input  [31:0] R1In,
  input  [3:0] DmSelIn,
  input  shaIn,
  input  [31:0] R2In,
  input  DmLdIn,
  input  [31:0] _32bIn1,
  input  DmStrIn,
  input  RegWriteIn,
  input  [31:0] _32bIn2,
  input  [1:0] M4In,
  input  [1:0] M3In,
  input  [31:0] _32bIn3,
  input  [1:0] M2In,
  input  [31:0] _32bIn4,
  input  [1:0] M1In,
  input  \传输状态In ,
  input  DispIn,
  input  CLK,
  input  \同步清零 ,
  input  \异步清零 ,
  output [27:0] IstrOut,
  output pauseOut,
  output [4:0] _5bOut1,
  output haltOut,
  output [4:0] _5bOut2,
  output [3:0] AluOut,
  output [31:0] R1Out,
  output [3:0] DmSelOut,
  output shaOut,
  output [31:0] R2Out,
  output DmLdOut,
  output [31:0] _32bOut1,
  output DmStrOut,
  output RegWriteOut,
  output [31:0] _32bOut2,
  output [1:0] M4Out,
  output [1:0] M3Out,
  output [31:0] _32bOut3,
  output [1:0] M2Out,
  output [31:0] _32bOut4,
  output [1:0] M1Out,
  output \传输状态Out ,
  output DispOut
);

  wire multiplexer_10_out, multiplexer_11_out, multiplexer_12_out, multiplexer_15_out, multiplexer_16_out,
       multiplexer_17_out, multiplexer_18_out, multiplexer_23_out;
  wire [1:0] multiplexer_19_out, multiplexer_20_out, multiplexer_21_out, multiplexer_22_out;
  wire [3:0] multiplexer_13_out, multiplexer_14_out;
  wire [4:0] multiplexer_2_out, multiplexer_3_out;
  wire [27:0] multiplexer_1_out;
  wire [31:0] multiplexer_4_out, multiplexer_5_out, multiplexer_6_out, multiplexer_7_out, multiplexer_8_out,
       multiplexer_9_out;

  Multiplexer #(.width(28), .enable("false")) multiplexer_1 (
    .in0(IstrIn), .in1({28{1'b0}}), .out(multiplexer_1_out), .sel(\同步清零 ));
  Multiplexer #(.width(5), .enable("false")) multiplexer_2 (
    .in0(_5bIn1), .in1({5{1'b0}}), .out(multiplexer_2_out), .sel(\同步清零 ));
  Multiplexer #(.width(5), .enable("false")) multiplexer_3 (
    .in0(_5bIn2), .in1({5{1'b0}}), .out(multiplexer_3_out), .sel(\同步清零 ));
  Multiplexer #(.width(32), .enable("false")) multiplexer_4 (
    .in0(R1In), .in1({32{1'b0}}), .out(multiplexer_4_out), .sel(\同步清零 ));
  Multiplexer #(.width(32), .enable("false")) multiplexer_5 (
    .in0(R2In), .in1({32{1'b0}}), .out(multiplexer_5_out), .sel(\同步清零 ));
  Multiplexer #(.width(32), .enable("false")) multiplexer_6 (
    .in0(_32bIn1), .in1({32{1'b0}}), .out(multiplexer_6_out), .sel(\同步清零 ));
  Multiplexer #(.width(32), .enable("false")) multiplexer_7 (
    .in0(_32bIn2), .in1({32{1'b0}}), .out(multiplexer_7_out), .sel(\同步清零 ));
  Multiplexer #(.width(32), .enable("false")) multiplexer_8 (
    .in0(_32bIn3), .in1({32{1'b0}}), .out(multiplexer_8_out), .sel(\同步清零 ));
  Multiplexer #(.width(32), .enable("false")) multiplexer_9 (
    .in0(_32bIn4), .in1({32{1'b0}}), .out(multiplexer_9_out), .sel(\同步清零 ));
  Multiplexer #(.enable("false")) multiplexer_10 (.in0(\传输状态In ), .in1(1'b0), .out(multiplexer_10_out), .sel(\同步清零 ));
  Register #(.width(28)) register_1 (.D(multiplexer_1_out), .en(\传输状态In ), .Q(IstrOut), .clk(CLK), .clr(\异步清零 ));
  Register #(.width(5)) register_2 (.D(multiplexer_2_out), .en(\传输状态In ), .Q(_5bOut1), .clk(CLK), .clr(\异步清零 ));
  Register #(.width(5)) register_3 (.D(multiplexer_3_out), .en(\传输状态In ), .Q(_5bOut2), .clk(CLK), .clr(\异步清零 ));
  Register #(.width(32)) register_4 (.D(multiplexer_4_out), .en(\传输状态In ), .Q(R1Out), .clk(CLK), .clr(\异步清零 ));
  Register #(.width(32)) register_5 (.D(multiplexer_5_out), .en(\传输状态In ), .Q(R2Out), .clk(CLK), .clr(\异步清零 ));
  Register #(.width(32)) register_6 (.D(multiplexer_6_out), .en(\传输状态In ), .Q(_32bOut1), .clk(CLK), .clr(\异步清零 ));
  Register #(.width(32)) register_7 (.D(multiplexer_7_out), .en(\传输状态In ), .Q(_32bOut2), .clk(CLK), .clr(\异步清零 ));
  Register #(.width(32)) register_8 (.D(multiplexer_8_out), .en(\传输状态In ), .Q(_32bOut3), .clk(CLK), .clr(\异步清零 ));
  Register #(.width(32)) register_9 (.D(multiplexer_9_out), .en(\传输状态In ), .Q(_32bOut4), .clk(CLK), .clr(\异步清零 ));
  Register #(.width(1)) register_10 (.D(multiplexer_10_out), .en(\传输状态In ), .Q(\传输状态Out ), .clk(CLK), .clr(\异步清零 ));
  Multiplexer #(.enable("false")) multiplexer_11 (.in0(pauseIn), .in1(1'b0), .out(multiplexer_11_out), .sel(\同步清零 ));
  Multiplexer #(.enable("false")) multiplexer_12 (.in0(haltIn), .in1(1'b0), .out(multiplexer_12_out), .sel(\同步清零 ));
  Multiplexer #(.width(4), .enable("false")) multiplexer_13 (
    .in0(AluIn), .in1(4'b0000), .out(multiplexer_13_out), .sel(\同步清零 ));
  Multiplexer #(.width(4), .enable("false")) multiplexer_14 (
    .in0(DmSelIn), .in1(4'b0000), .out(multiplexer_14_out), .sel(\同步清零 ));
  Multiplexer #(.enable("false")) multiplexer_15 (.in0(shaIn), .in1(1'b0), .out(multiplexer_15_out), .sel(\同步清零 ));
  Multiplexer #(.enable("false")) multiplexer_16 (.in0(DmLdIn), .in1(1'b0), .out(multiplexer_16_out), .sel(\同步清零 ));
  Multiplexer #(.enable("false")) multiplexer_17 (.in0(DmStrIn), .in1(1'b0), .out(multiplexer_17_out), .sel(\同步清零 ));
  Multiplexer #(.enable("false")) multiplexer_18 (.in0(RegWriteIn), .in1(1'b0), .out(multiplexer_18_out), .sel(\同步清零 ));
  Multiplexer #(.width(2), .enable("false")) multiplexer_19 (
    .in0(M4In), .in1(2'b00), .out(multiplexer_19_out), .sel(\同步清零 ));
  Multiplexer #(.width(2), .enable("false")) multiplexer_20 (
    .in0(M3In), .in1(2'b00), .out(multiplexer_20_out), .sel(\同步清零 ));
  Multiplexer #(.width(2), .enable("false")) multiplexer_21 (
    .in0(M2In), .in1(2'b00), .out(multiplexer_21_out), .sel(\同步清零 ));
  Multiplexer #(.width(2), .enable("false")) multiplexer_22 (
    .in0(M1In), .in1(2'b00), .out(multiplexer_22_out), .sel(\同步清零 ));
  Multiplexer #(.enable("false")) multiplexer_23 (.in0(DispIn), .in1(1'b0), .out(multiplexer_23_out), .sel(\同步清零 ));
  Register #(.width(1)) register_11 (.D(multiplexer_11_out), .en(\传输状态In ), .Q(pauseOut), .clk(CLK), .clr(\异步清零 ));
  Register #(.width(1)) register_12 (.D(multiplexer_12_out), .en(\传输状态In ), .Q(haltOut), .clk(CLK), .clr(\异步清零 ));
  Register #(.width(4)) register_13 (.D(multiplexer_13_out), .en(\传输状态In ), .Q(AluOut), .clk(CLK), .clr(\异步清零 ));
  Register #(.width(4)) register_14 (.D(multiplexer_14_out), .en(\传输状态In ), .Q(DmSelOut), .clk(CLK), .clr(\异步清零 ));
  Register #(.width(1)) register_15 (.D(multiplexer_15_out), .en(\传输状态In ), .Q(shaOut), .clk(CLK), .clr(\异步清零 ));
  Register #(.width(1)) register_16 (.D(multiplexer_16_out), .en(\传输状态In ), .Q(DmLdOut), .clk(CLK), .clr(\异步清零 ));
  Register #(.width(1)) register_17 (.D(multiplexer_17_out), .en(\传输状态In ), .Q(DmStrOut), .clk(CLK), .clr(\异步清零 ));
  Register #(.width(1)) register_18 (.D(multiplexer_18_out), .en(\传输状态In ), .Q(RegWriteOut), .clk(CLK), .clr(\异步清零 ));
  Register #(.width(2)) register_19 (.D(multiplexer_19_out), .en(\传输状态In ), .Q(M4Out), .clk(CLK), .clr(\异步清零 ));
  Register #(.width(2)) register_20 (.D(multiplexer_20_out), .en(\传输状态In ), .Q(M3Out), .clk(CLK), .clr(\异步清零 ));
  Register #(.width(2)) register_21 (.D(multiplexer_21_out), .en(\传输状态In ), .Q(M2Out), .clk(CLK), .clr(\异步清零 ));
  Register #(.width(2)) register_22 (.D(multiplexer_22_out), .en(\传输状态In ), .Q(M1Out), .clk(CLK), .clr(\异步清零 ));
  Register #(.width(1)) register_23 (.D(multiplexer_23_out), .en(\传输状态In ), .Q(DispOut), .clk(CLK), .clr(\异步清零 ));
endmodule

module EX_MEM (
  input  [27:0] IstrIn,
  input  [31:0] _32bIn4,
  input  _1bIn1,
  input  _1bIn2,
  input  pauseIn,
  input  [31:0] _32bIn1,
  input  haltIn,
  input  [3:0] DmSelIn,
  input  [31:0] _32bIn2,
  input  DmLdIn,
  input  DmStrIn,
  input  [31:0] _32bIn3,
  input  RegWriteIn,
  input  [4:0] _5bIn1,
  input  [1:0] M3In,
  input  \传输状态In ,
  input  DispIn,
  input  CLK,
  input  \同步清零 ,
  input  \异步清零 ,
  output [27:0] IstrOut,
  output [31:0] _32bOut4,
  output _1bOut1,
  output _1bOut2,
  output pauseOut,
  output [31:0] _32bOut1,
  output haltOut,
  output [3:0] DmSelOut,
  output [31:0] _32bOut2,
  output DmLdOut,
  output DmStrOut,
  output [31:0] _32bOut3,
  output RegWriteOut,
  output [4:0] _5bOut1,
  output [1:0] M3Out,
  output \传输状态Out ,
  output DispOut
);

  wire multiplexer_3_out, multiplexer_4_out, multiplexer_9_out, multiplexer_10_out, multiplexer_11_out,
       multiplexer_13_out, multiplexer_14_out, multiplexer_15_out, multiplexer_17_out;
  wire [1:0] multiplexer_16_out;
  wire [3:0] multiplexer_12_out;
  wire [4:0] multiplexer_8_out;
  wire [27:0] multiplexer_1_out;
  wire [31:0] multiplexer_2_out, multiplexer_5_out, multiplexer_6_out, multiplexer_7_out;

  Multiplexer #(.width(28), .enable("false")) multiplexer_1 (
    .in0(IstrIn), .in1({28{1'b0}}), .out(multiplexer_1_out), .sel(\同步清零 ));
  Multiplexer #(.width(32), .enable("false")) multiplexer_2 (
    .in0(_32bIn4), .in1({32{1'b0}}), .out(multiplexer_2_out), .sel(\同步清零 ));
  Multiplexer #(.enable("false")) multiplexer_3 (.in0(_1bIn1), .in1(1'b0), .out(multiplexer_3_out), .sel(\同步清零 ));
  Multiplexer #(.enable("false")) multiplexer_4 (.in0(_1bIn2), .in1(1'b0), .out(multiplexer_4_out), .sel(\同步清零 ));
  Multiplexer #(.width(32), .enable("false")) multiplexer_5 (
    .in0(_32bIn1), .in1({32{1'b0}}), .out(multiplexer_5_out), .sel(\同步清零 ));
  Multiplexer #(.width(32), .enable("false")) multiplexer_6 (
    .in0(_32bIn2), .in1({32{1'b0}}), .out(multiplexer_6_out), .sel(\同步清零 ));
  Multiplexer #(.width(32), .enable("false")) multiplexer_7 (
    .in0(_32bIn3), .in1({32{1'b0}}), .out(multiplexer_7_out), .sel(\同步清零 ));
  Multiplexer #(.width(5), .enable("false")) multiplexer_8 (
    .in0(_5bIn1), .in1({5{1'b0}}), .out(multiplexer_8_out), .sel(\同步清零 ));
  Multiplexer #(.enable("false")) multiplexer_9 (.in0(\传输状态In ), .in1(1'b0), .out(multiplexer_9_out), .sel(\同步清零 ));
  Register #(.width(28)) register_1 (.D(multiplexer_1_out), .en(\传输状态In ), .Q(IstrOut), .clk(CLK), .clr(\异步清零 ));
  Register #(.width(32)) register_2 (.D(multiplexer_2_out), .en(\传输状态In ), .Q(_32bOut4), .clk(CLK), .clr(\异步清零 ));
  Register #(.width(1)) register_3 (.D(multiplexer_3_out), .en(\传输状态In ), .Q(_1bOut1), .clk(CLK), .clr(\异步清零 ));
  Register #(.width(1)) register_4 (.D(multiplexer_4_out), .en(\传输状态In ), .Q(_1bOut2), .clk(CLK), .clr(\异步清零 ));
  Register #(.width(32)) register_5 (.D(multiplexer_5_out), .en(\传输状态In ), .Q(_32bOut1), .clk(CLK), .clr(\异步清零 ));
  Register #(.width(32)) register_6 (.D(multiplexer_6_out), .en(\传输状态In ), .Q(_32bOut2), .clk(CLK), .clr(\异步清零 ));
  Register #(.width(32)) register_7 (.D(multiplexer_7_out), .en(\传输状态In ), .Q(_32bOut3), .clk(CLK), .clr(\异步清零 ));
  Register #(.width(5)) register_8 (.D(multiplexer_8_out), .en(\传输状态In ), .Q(_5bOut1), .clk(CLK), .clr(\异步清零 ));
  Register #(.width(1)) register_9 (.D(multiplexer_9_out), .en(\传输状态In ), .Q(\传输状态Out ), .clk(CLK), .clr(\异步清零 ));
  Multiplexer #(.enable("false")) multiplexer_10 (.in0(pauseIn), .in1(1'b0), .out(multiplexer_10_out), .sel(\同步清零 ));
  Multiplexer #(.enable("false")) multiplexer_11 (.in0(haltIn), .in1(1'b0), .out(multiplexer_11_out), .sel(\同步清零 ));
  Multiplexer #(.width(4), .enable("false")) multiplexer_12 (
    .in0(DmSelIn), .in1(4'b0000), .out(multiplexer_12_out), .sel(\同步清零 ));
  Multiplexer #(.enable("false")) multiplexer_13 (.in0(DmLdIn), .in1(1'b0), .out(multiplexer_13_out), .sel(\同步清零 ));
  Multiplexer #(.enable("false")) multiplexer_14 (.in0(DmStrIn), .in1(1'b0), .out(multiplexer_14_out), .sel(\同步清零 ));
  Multiplexer #(.enable("false")) multiplexer_15 (.in0(RegWriteIn), .in1(1'b0), .out(multiplexer_15_out), .sel(\同步清零 ));
  Multiplexer #(.width(2), .enable("false")) multiplexer_16 (
    .in0(M3In), .in1(2'b00), .out(multiplexer_16_out), .sel(\同步清零 ));
  Multiplexer #(.enable("false")) multiplexer_17 (.in0(DispIn), .in1(1'b0), .out(multiplexer_17_out), .sel(\同步清零 ));
  Register #(.width(1)) register_10 (.D(multiplexer_10_out), .en(\传输状态In ), .Q(pauseOut), .clk(CLK), .clr(\异步清零 ));
  Register #(.width(1)) register_11 (.D(multiplexer_11_out), .en(\传输状态In ), .Q(haltOut), .clk(CLK), .clr(\异步清零 ));
  Register #(.width(4)) register_12 (.D(multiplexer_12_out), .en(\传输状态In ), .Q(DmSelOut), .clk(CLK), .clr(\异步清零 ));
  Register #(.width(1)) register_13 (.D(multiplexer_13_out), .en(\传输状态In ), .Q(DmLdOut), .clk(CLK), .clr(\异步清零 ));
  Register #(.width(1)) register_14 (.D(multiplexer_14_out), .en(\传输状态In ), .Q(DmStrOut), .clk(CLK), .clr(\异步清零 ));
  Register #(.width(1)) register_15 (.D(multiplexer_15_out), .en(\传输状态In ), .Q(RegWriteOut), .clk(CLK), .clr(\异步清零 ));
  Register #(.width(2)) register_16 (.D(multiplexer_16_out), .en(\传输状态In ), .Q(M3Out), .clk(CLK), .clr(\异步清零 ));
  Register #(.width(1)) register_17 (.D(multiplexer_17_out), .en(\传输状态In ), .Q(DispOut), .clk(CLK), .clr(\异步清零 ));
endmodule

module MEM_WB (
  input  [27:0] IstrIn,
  input  [31:0] _32bIn3,
  input  _1bIn1,
  input  [31:0] _32bIn1,
  input  pauseIn,
  input  [31:0] _32bIn2,
  input  [4:0] _5bIn1,
  input  haltIn,
  input  \传输状态In ,
  input  [1:0] M3In,
  input  CLK,
  input  \同步清零 ,
  input  \异步清零 ,
  output [27:0] IstrOut,
  output [31:0] _32bOut3,
  output _1bOut1,
  output [31:0] _32bOut1,
  output pauseOut,
  output [31:0] _32bOut2,
  output [4:0] _5bOut1,
  output haltOut,
  output \传输状态Out ,
  output [1:0] M3Out
);

  wire multiplexer_3_out, multiplexer_7_out, multiplexer_8_out, multiplexer_9_out;
  wire [1:0] multiplexer_10_out;
  wire [4:0] multiplexer_6_out;
  wire [27:0] multiplexer_1_out;
  wire [31:0] multiplexer_2_out, multiplexer_4_out, multiplexer_5_out;

  Multiplexer #(.width(28), .enable("false")) multiplexer_1 (
    .in0(IstrIn), .in1({28{1'b0}}), .out(multiplexer_1_out), .sel(\同步清零 ));
  Multiplexer #(.width(32), .enable("false")) multiplexer_2 (
    .in0(_32bIn3), .in1({32{1'b0}}), .out(multiplexer_2_out), .sel(\同步清零 ));
  Multiplexer #(.enable("false")) multiplexer_3 (.in0(_1bIn1), .in1(1'b0), .out(multiplexer_3_out), .sel(\同步清零 ));
  Multiplexer #(.width(32), .enable("false")) multiplexer_4 (
    .in0(_32bIn1), .in1({32{1'b0}}), .out(multiplexer_4_out), .sel(\同步清零 ));
  Multiplexer #(.width(32), .enable("false")) multiplexer_5 (
    .in0(_32bIn2), .in1({32{1'b0}}), .out(multiplexer_5_out), .sel(\同步清零 ));
  Multiplexer #(.width(5), .enable("false")) multiplexer_6 (
    .in0(_5bIn1), .in1({5{1'b0}}), .out(multiplexer_6_out), .sel(\同步清零 ));
  Multiplexer #(.enable("false")) multiplexer_7 (.in0(\传输状态In ), .in1(1'b0), .out(multiplexer_7_out), .sel(\同步清零 ));
  Register #(.width(28)) register_1 (.D(multiplexer_1_out), .en(\传输状态In ), .Q(IstrOut), .clk(CLK), .clr(\异步清零 ));
  Register #(.width(32)) register_2 (.D(multiplexer_2_out), .en(\传输状态In ), .Q(_32bOut3), .clk(CLK), .clr(\异步清零 ));
  Register #(.width(1)) register_3 (.D(multiplexer_3_out), .en(\传输状态In ), .Q(_1bOut1), .clk(CLK), .clr(\异步清零 ));
  Register #(.width(32)) register_4 (.D(multiplexer_4_out), .en(\传输状态In ), .Q(_32bOut1), .clk(CLK), .clr(\异步清零 ));
  Register #(.width(32)) register_5 (.D(multiplexer_5_out), .en(\传输状态In ), .Q(_32bOut2), .clk(CLK), .clr(\异步清零 ));
  Register #(.width(5)) register_6 (.D(multiplexer_6_out), .en(\传输状态In ), .Q(_5bOut1), .clk(CLK), .clr(\异步清零 ));
  Register #(.width(1)) register_7 (.D(multiplexer_7_out), .en(\传输状态In ), .Q(\传输状态Out ), .clk(CLK), .clr(\异步清零 ));
  Multiplexer #(.enable("false")) multiplexer_8 (.in0(pauseIn), .in1(1'b0), .out(multiplexer_8_out), .sel(\同步清零 ));
  Multiplexer #(.enable("false")) multiplexer_9 (.in0(haltIn), .in1(1'b0), .out(multiplexer_9_out), .sel(\同步清零 ));
  Multiplexer #(.width(2), .enable("false")) multiplexer_10 (
    .in0(M3In), .in1(2'b00), .out(multiplexer_10_out), .sel(\同步清零 ));
  Register #(.width(1)) register_8 (.D(multiplexer_8_out), .en(\传输状态In ), .Q(pauseOut), .clk(CLK), .clr(\异步清零 ));
  Register #(.width(1)) register_9 (.D(multiplexer_9_out), .en(\传输状态In ), .Q(haltOut), .clk(CLK), .clr(\异步清零 ));
  Register #(.width(2)) register_10 (.D(multiplexer_10_out), .en(\传输状态In ), .Q(M3Out), .clk(CLK), .clr(\异步清零 ));
endmodule

// CfltCtrl
module ConflitCtrl (
  input  [4:0] RS,
  input  [4:0] RD_EX,
  input  [4:0] RD_MEM,
  input  [4:0] RT,
  input  [27:0] Istr1,
  input  [27:0] Istr2,
  input  [27:0] Istr,
  input  [4:0] RD_ID,
  output IF_ID_STOP,
  output ID_EX_CLEAR
);

  wire _RD1, _RD2, _RS, _RT, and_7_out, and_8_out, and_9_out, and_10_out, and_11_out, and_12_out, and_13_out,
       and_14_out, and_15_out, and_16_out, and_17_out, and_18_out, comparator_5_eq, comparator_6_eq,
       comparator_7_eq, comparator_8_eq, nor_1_out, nor_2_out, or_5_out, or_6_out, RD_RS1, RD_RS2, RD_RT1,
       RD_RT2, RDEX_IS0, RDMEM_IS0, RS_IS0, RS_RT, RT_IS0, undriven, WriteReg1, WriteReg2;

  Comparator #(.width(5)) comparator_1 (.a({5{1'b0}}), .b(RS), .eq(RS_IS0));  // open: gt, lt
  Comparator #(.width(5)) comparator_2 (.a({5{1'b0}}), .b(RT), .eq(RT_IS0));  // open: gt, lt
  Comparator #(.width(5)) comparator_3 (.a({5{1'b0}}), .b(RD_EX), .eq(RDEX_IS0));  // open: gt, lt
  Comparator #(.width(5)) comparator_4 (.a({5{1'b0}}), .b(RD_MEM), .eq(RDMEM_IS0));  // open: gt, lt
  or or_1 (RS_RT, Istr[5], Istr[13], Istr[14], Istr[15], Istr[16], Istr[17], Istr[18], Istr[27], Istr[7], Istr[6], Istr[20], Istr[19], Istr[22], Istr[21], Istr[4]);
  or or_2 (_RS, Istr[0], Istr[1], Istr[2], Istr[3], Istr[10], Istr[26], Istr[8], Istr[12]);
  or or_3 (_RT, Istr[23], Istr[11], undriven, Istr[25], Istr[24]);
  Comparator #(.width(5)) comparator_5 (.a(RD_EX), .b(RS), .eq(comparator_5_eq));  // open: gt, lt
  Comparator #(.width(5)) comparator_6 (.a(RD_EX), .b(RT), .eq(comparator_6_eq));  // open: gt, lt
  Comparator #(.width(5)) comparator_7 (.a(RD_MEM), .b(RS), .eq(comparator_7_eq));  // open: gt, lt
  Comparator #(.width(5)) comparator_8 (.a(RD_MEM), .b(RT), .eq(comparator_8_eq));  // open: gt, lt
  and and_1 (WriteReg1, _RD1, ~RDEX_IS0);  // AND_Gate
  and and_2 (WriteReg2, _RD2, ~RDMEM_IS0);  // AND_Gate
  and and_3 (RD_RS1, ~RS_IS0, comparator_5_eq);  // AND_Gate
  and and_4 (RD_RT1, ~RT_IS0, comparator_6_eq);  // AND_Gate
  and and_5 (RD_RS2, ~RS_IS0, comparator_7_eq);  // AND_Gate
  and and_6 (RD_RT2, ~RT_IS0, comparator_8_eq);  // AND_Gate
  or or_4 (_RD2, Istr2[0], Istr2[2], Istr2[4], Istr2[1], Istr2[8], Istr2[3], Istr2[10], Istr2[13], Istr2[14], Istr2[15], Istr2[17], Istr2[16], Istr2[19], Istr2[18], Istr2[21], Istr2[20], Istr2[23], Istr2[22], Istr2[25], Istr2[24]);
  or or_5 (or_5_out, RD_RS1, RD_RT1);
  and and_7 (and_7_out, RS_RT, WriteReg1);
  and and_8 (and_8_out, _RT, WriteReg1);
  and and_9 (and_9_out, _RS, WriteReg1);
  or or_6 (or_6_out, RD_RS2, RD_RT2);
  and and_10 (and_10_out, RS_RT, WriteReg2);
  and and_11 (and_11_out, _RT, WriteReg2);
  and and_12 (and_12_out, _RS, WriteReg2);
  and and_13 (and_13_out, or_5_out, and_7_out);
  and and_14 (and_14_out, RD_RT1, and_8_out);
  nor nor_1 (nor_1_out, and_13_out, and_14_out, and_15_out);
  and and_15 (and_15_out, RD_RS1, and_9_out);
  and and_16 (and_16_out, or_6_out, and_10_out);
  and and_17 (and_17_out, RD_RT2, and_11_out);
  nor nor_2 (nor_2_out, and_16_out, and_17_out, and_18_out);
  and and_18 (and_18_out, RD_RS2, and_12_out);
  or or_7 (_RD1, Istr1[0], Istr1[2], Istr1[4], Istr1[1], Istr1[8], Istr1[3], Istr1[10], Istr1[13], Istr1[14], Istr1[15], Istr1[17], Istr1[16], Istr1[19], Istr1[18], Istr1[21], Istr1[20], Istr1[23], Istr1[22], Istr1[25], Istr1[24]);
  and and_19 (IF_ID_STOP, nor_1_out, nor_2_out);
  not not_1 (ID_EX_CLEAR, IF_ID_STOP);

  // Other names for the same wires on the sheet: clearID_EX = ID_EX_CLEAR; ADDI = Istr[0]; ADDIU = Istr[1];
  //   ANDI = Istr[2]; ORI = Istr[3]; LW = Istr[4]; SW = Istr[5]; BEQ = Istr[6]; BNE = Istr[7]; SLTI = Istr[8];
  //   J = Istr[9]; JAL = Istr[10]; SB = Istr[11]; BLTZ = Istr[12]; ADD = Istr[13]; ADDU = Istr[14]; AND = Istr[15];
  //   SUB = Istr[16]; OR = Istr[17]; NOR = Istr[18]; SLT = Istr[19]; SLTU = Istr[20]; SRLV = Istr[21];
  //   SRAV = Istr[22]; SLL = Istr[23]; SRA = Istr[24]; SRL = Istr[25]; JR = Istr[26]; SYSCAL = Istr[27];
  //   ADDI1 = Istr1[0]; ADDIU1 = Istr1[1]; ANDI1 = Istr1[2]; ORI1 = Istr1[3]; LW1 = Istr1[4]; SW1 = Istr1[5];
  //   BEQ1 = Istr1[6]; BNE1 = Istr1[7]; SLTI1 = Istr1[8]; J1 = Istr1[9]; JAL1 = Istr1[10]; SB1 = Istr1[11];
  //   BLTZ1 = Istr1[12]; ADD1 = Istr1[13]; ADDU1 = Istr1[14]; AND1 = Istr1[15]; SUB1 = Istr1[16]; OR1 = Istr1[17];
  //   NOR1 = Istr1[18]; SLT1 = Istr1[19]; SLTU1 = Istr1[20]; SRLV1 = Istr1[21]; SRAV1 = Istr1[22]; SLL1 = Istr1[23];
  //   SRA1 = Istr1[24]; SRL1 = Istr1[25]; JR1 = Istr1[26]; SYSCAL1 = Istr1[27]; ADDI2 = Istr2[0]; ADDIU2 = Istr2[1];
  //   ANDI2 = Istr2[2]; ORI2 = Istr2[3]; LW2 = Istr2[4]; SW2 = Istr2[5]; BEQ2 = Istr2[6]; BNE2 = Istr2[7];
  //   SLTI2 = Istr2[8]; J2 = Istr2[9]; JAL2 = Istr2[10]; SB2 = Istr2[11]; BLTZ2 = Istr2[12]; ADD2 = Istr2[13];
  //   ADDU2 = Istr2[14]; AND2 = Istr2[15]; SUB2 = Istr2[16]; OR2 = Istr2[17]; NOR2 = Istr2[18]; SLT2 = Istr2[19];
  //   SLTU2 = Istr2[20]; SRLV2 = Istr2[21]; SRAV2 = Istr2[22]; SLL2 = Istr2[23]; SRA2 = Istr2[24]; SRL2 = Istr2[25];
  //   JR2 = Istr2[26]; SYSCAL2 = Istr2[27]; stopIF_ID = IF_ID_STOP
endmodule

// dproc
module romshm (
  input  [31:0] DataIn,
  input  [3:0] selIn,
  output [31:0] DataOut
);

  wire comparator_1_eq, comparator_2_eq, comparator_3_eq, comparator_4_eq, comparator_5_eq, comparator_6_eq,
       comparator_7_eq, or_1_out, or_2_out;
  wire [1:0] or_3_out;

  Comparator #(.width(4)) comparator_1 (.a(selIn), .b(4'b1111), .eq(comparator_1_eq));  // open: gt, lt
  Comparator #(.width(4)) comparator_2 (.a(selIn), .b(4'b0011), .eq(comparator_2_eq));  // open: gt, lt
  Comparator #(.width(4)) comparator_3 (.a(selIn), .b(4'b1100), .eq(comparator_3_eq));  // open: gt, lt
  Comparator #(.width(4)) comparator_4 (.a(selIn), .b(4'b0001), .eq(comparator_4_eq));  // open: gt, lt
  Comparator #(.width(4)) comparator_5 (.a(selIn), .b(4'b0010), .eq(comparator_5_eq));  // open: gt, lt
  Comparator #(.width(4)) comparator_6 (.a(selIn), .b(4'b0100), .eq(comparator_6_eq));  // open: gt, lt
  Comparator #(.width(4)) comparator_7 (.a(selIn), .b(4'b1000), .eq(comparator_7_eq));  // open: gt, lt
  or or_1 (or_1_out, comparator_2_eq, comparator_3_eq);
  or or_2 (or_2_out, comparator_4_eq, comparator_5_eq, comparator_6_eq, comparator_7_eq);
  or or_3 (or_3_out[0], comparator_1_eq, or_1_out);
  or or_4 (or_3_out[1], comparator_1_eq, or_2_out);
  Multiplexer #(.select(2), .width(32)) multiplexer_1 (
    .in0(DataIn), .in1({DataIn[15:0], DataIn[15:0]}),
    .in2({DataIn[7:0], DataIn[7:0], DataIn[7:0], DataIn[7:0]}), .in3(DataIn), .out(DataOut), .sel(or_3_out));  // open: en

  // Other names for the same wires on the sheet: Byte[31:0] = {DataIn[7:0], DataIn[7:0], DataIn[7:0], DataIn[7:0]};
  //   Half[31:0] = {DataIn[15:0], DataIn[15:0]}
endmodule
