// Logisim project cpu_int _recursive.circ as structural Verilog: 13 circuits, main circuit cpu
module cpu (
);

  wire _1_out, \_1号中断 , \_1号中断等待指示 , _2_out, \_2号中断 , \_2号中断等待指示 , _3_out, \_3号中断 , \_3号中断等待指示 , alu_1_equal,
       and_1_out, and_2_out, and_3_out, button_int_1_and_1, button_int_1_and_2, button_int_1_and_3, cli, CLK,
       controller_1_bcount, controller_1_brcount, controller_1_disp, controller_1_dmld, controller_1_dmstr,
       controller_1_efc, controller_1_halt, controller_1_jcount, controller_1_sha, decoder_1_out1,
       decoder_1_out2, decoder_1_out3, En, eret, etc, ie, inm_1_out_1, inm_1_out_2, inm_1_out_3, int1, int2,
       int3, IntC, istrsplit_1_syscall, multiplexer_5_out, not_1_out, not_2_out, not_3_out, or_1_out,
       or_2_out, RST, sti, WE;
  wire [1:0] controller_1_m1, controller_1_m2, controller_1_m3, controller_1_m4, IR_CLR, irclr;
  wire [3:0] controller_1_alu, controller_1_dmsel;
  wire [4:0] istrsplit_1_rd, istrsplit_1_rs, istrsplit_1_rt, istrsplit_1_shamt, registerfile_1_p4;
  wire [5:0] istrsplit_1_func, istrsplit_1_op;
  wire [15:0] istrsplit_1_imm16, \总周期数 , \无条件分支指令数 , \有条件分支成功跳转 , \有条件分支指令数 ;
  wire [19:0] alu_1_result_2;
  wire [25:0] istrsplit_1_imm26;
  wire [31:0] adder_1_out, adder_2_out, alu_1_result, epc, idt_1_addr, istrsplit_1_istrout, mips_ram_1_p9,
       multiplexer_1_out, multiplexer_2_out, multiplexer_3_out, multiplexer_8_out, multiplexer_9_out,
       multiplexer_10_out, multiplexer_11_out, PC_q, registerfile_1_p1, rom_1_data, rt, signextend_1_out_2,
       SyscallOut, undriven;

  Decoder #(.select(2)) decoder_1 (
    .out1(decoder_1_out1), .out2(decoder_1_out2), .out3(decoder_1_out3), .sel(IR_CLR));  // open: out0, en
  Register #(.width(32)) PC (.D(multiplexer_2_out), .en(En), .Q(PC_q), .clk(CLK), .clr(RST));
  Button _1 (.out(_1_out));
  Button _2 (.out(_2_out));
  Button _3 (.out(_3_out));
  Button \u_总复位  (.out(RST));
  Clock clock_1 (.out(CLK));
  // Probe on rt
  Multiplexer #(.width(32)) multiplexer_1 (.in0(PC_q), .in1(rt), .out(multiplexer_1_out), .sel(etc));  // open: en
  EPC epc_1 (.Clk(CLK), .Rst(RST), .en(or_1_out), .PC_CUR(multiplexer_1_out), .PC_EPC(epc));
  or or_1 (or_1_out, IntC, etc);
  button_int button_int_1 (
    ._1st(\_1号中断 ), ._2nd(\_2号中断 ), ._3rd(\_3号中断 ), .Clk(CLK), .Rst(RST), ._1st_int_wait(\_1号中断等待指示 ),
    ._2nd_int_wait(\_2号中断等待指示 ), ._3rd_int_wait(\_3号中断等待指示 ), .clr_1(decoder_1_out1), .clr_2(decoder_1_out2),
    .clr_3(decoder_1_out3), .and_1(button_int_1_and_1), .and_2(button_int_1_and_2), .and_3(button_int_1_and_3));
  INM inm_1 (
    .Clk(CLK), .Rst(RST), .en_1(1'b0), .en_2(1'b0), .en_3(1'b0), .init_1(_1_out), .init_2(_2_out),
    .init_3(_3_out), .Out_1(inm_1_out_1), .Out_2(inm_1_out_2), .Out_3(inm_1_out_3));  // open: INM_1, INM_2, INM_3
  InstCounter instcounter_1 (
    .CLK(CLK), .Halt(En), .CLR(RST), .Bcount(controller_1_bcount), .Jcount(controller_1_jcount),
    .Brcount(controller_1_brcount), .J(\无条件分支指令数 ), .B(\有条件分支指令数 ), .Br(\有条件分支成功跳转 ), .All(\总周期数 ));
  // Probe on epc
  not not_1 (not_1_out, inm_1_out_1);
  not not_2 (not_2_out, inm_1_out_2);
  not not_3 (not_3_out, inm_1_out_3);
  Hex_Digit_Display hex_digit_display_1 (.value(SyscallOut[27:24]));  // open: dp
  Hex_Digit_Display hex_digit_display_2 (.value(SyscallOut[31:28]));  // open: dp
  ROM #(.addrWidth(10), .dataWidth(32)) rom_1 (.addr(PC_q[9:0]), .data(rom_1_data));  // open: sel
  IstrSplit istrsplit_1 (
    .Istr(rom_1_data), .OP(istrsplit_1_op), .FUNC(istrsplit_1_func), .RD(istrsplit_1_rd),
    .IMM16(istrsplit_1_imm16), .IMM26(istrsplit_1_imm26), .SHAMT(istrsplit_1_shamt), .RS(istrsplit_1_rs),
    .RT(istrsplit_1_rt), .Syscall(istrsplit_1_syscall), .eret(eret), .istrOut(istrsplit_1_istrout));
  Multiplexer #(.width(32)) multiplexer_2 (
    .in0(multiplexer_3_out), .in1(epc), .out(multiplexer_2_out), .sel(eret));  // open: en
  // Probe on multiplexer_3_out
  and and_1 (and_1_out, button_int_1_and_1, not_1_out);
  and and_2 (and_2_out, button_int_1_and_2, not_2_out);
  and and_3 (and_3_out, button_int_1_and_3, not_3_out);
  Hex_Digit_Display hex_digit_display_3 (.value(SyscallOut[23:20]));  // open: dp
  Hex_Digit_Display hex_digit_display_4 (.value(SyscallOut[19:16]));  // open: dp
  lock lock_1 (.en(controller_1_halt), .Clk(CLK), .rst(RST), .En_2(En));
  Controller controller_1 (
    .OP(istrsplit_1_op), .EQU(alu_1_equal), .RS(undriven), .FUNCT(istrsplit_1_func), .Alu(controller_1_alu),
    .M1(controller_1_m1), .RegWrite(WE), .M2(controller_1_m2), .DmStr(controller_1_dmstr),
    .M3(controller_1_m3), .DmSel(controller_1_dmsel), .M4(controller_1_m4), .DmLd(controller_1_dmld),
    .Halt(controller_1_halt), .Disp(controller_1_disp), .Sha(controller_1_sha),
    .BrCount(controller_1_brcount), .BCount(controller_1_bcount), .JCount(controller_1_jcount),
    .efc(controller_1_efc), .istr(istrsplit_1_istrout), .etc(etc), .RT(istrsplit_1_rt), .STI(sti), .CLI(cli));
  Adder #(.width(32)) adder_1 (.a({{22{1'b0}}, PC_q[9:0]}), .b(32'h1), .out(adder_1_out));  // open: cin, cout
  Priority_Encoder #(.select(2)) priority_encoder_1 (
    .in0(1'b1), .in1(and_1_out), .in2(and_2_out), .in3(and_3_out), .out(irclr));  // open: gs, en_out, en_in
  Hex_Digit_Display hex_digit_display_5 (.value(SyscallOut[15:12]));  // open: dp
  Hex_Digit_Display hex_digit_display_6 (.value(SyscallOut[11:8]));  // open: dp
  Multiplexer #(.width(32)) multiplexer_3 (
    .in0(multiplexer_11_out), .in1(idt_1_addr), .out(multiplexer_3_out), .sel(IntC));  // open: en
  Multiplexer #(.width(2)) multiplexer_4 (.in0(2'b00), .in1(irclr), .out(IR_CLR), .sel(eret));  // open: en
  IDT idt_1 (.Index(irclr), .Addr(idt_1_addr));
  Multiplexer multiplexer_5 (.in0(1'b1), .in1(1'b0), .out(multiplexer_5_out), .sel(sti));  // open: en
  or or_2 (or_2_out, cli, sti);
  Hex_Digit_Display hex_digit_display_7 (.value(SyscallOut[7:4]));  // open: dp
  Hex_Digit_Display hex_digit_display_8 (.value(SyscallOut[3:0]));  // open: dp
  // Probe on idt_1_addr
  IE ie_1 (.Clk(CLK), .Istr(multiplexer_5_out), .Rst(RST), .en(or_2_out), .ie(ie));
  wait_int wait_int_1 (
    .CLK(CLK), .ie(ie), .\_1号中断 (\_1号中断 ), .int1(int1), .\_2号中断 (\_2号中断 ), .int2(int2), .\_3号中断 (\_3号中断 ),
    .int3(int3), .IntC(IntC));
  // RegisterFile registerfile_1: pin names not known; wires that end beside it: registerfile_1_p1, CLK, WE, registerfile_1_p4, istrsplit_1_rs, istrsplit_1_rt, rt
  SignExtend signextend_1 (.in_1(istrsplit_1_imm16), .out_2(signextend_1_out_2));
  Decoder #(.select(2)) decoder_2 (.out1(int1), .out2(int2), .out3(int3), .sel(irclr));  // open: out0, en
  // Probe on irclr
  Multiplexer #(.width(32)) multiplexer_6 (
    .in0(multiplexer_10_out), .in1(epc), .out(registerfile_1_p1), .sel(controller_1_efc));  // open: en
  // Probe on \总周期数 
  // Probe on \无条件分支指令数 
  // Probe on \有条件分支指令数 
  // Probe on \有条件分支成功跳转 
  Multiplexer #(.select(2), .width(5)) multiplexer_7 (
    .in0(istrsplit_1_rt), .in1(istrsplit_1_rd), .in2({5{1'b1}}), .in3({5{1'b0}}), .out(registerfile_1_p4),
    .sel(controller_1_m1));  // open: en
  Adder #(.width(32)) adder_2 (.a(adder_1_out), .b(signextend_1_out_2), .out(adder_2_out));  // open: cin, cout
  Button _1_2 (.out(\_1号中断 ));
  Button _2_2 (.out(\_2号中断 ));
  Button _3_2 (.out(\_3号中断 ));
  Multiplexer #(.width(32)) multiplexer_8 (
    .in0(undriven), .in1(rt), .out(multiplexer_8_out), .sel(controller_1_sha));  // open: en
  Multiplexer #(.select(2), .width(32)) multiplexer_9 (
    .in0(rt), .in1(signextend_1_out_2), .in2({{27{1'b0}}, istrsplit_1_shamt}), .in3(undriven),
    .out(multiplexer_9_out), .sel(controller_1_m2));  // open: en
  Multiplexer #(.select(2), .width(32)) multiplexer_10 (
    .in0({alu_1_result[31:22], alu_1_result_2, alu_1_result[1:0]}), .in1(mips_ram_1_p9), .in2(adder_1_out),
    .out(multiplexer_10_out), .sel(controller_1_m3));  // open: in3, en
  ALU alu_1 (
    .AluOP(controller_1_alu), .X(multiplexer_8_out), .Equal(alu_1_equal),
    .Result({alu_1_result[31:22], alu_1_result_2, alu_1_result[1:0]}), .Y(multiplexer_9_out));  // open: Signed_Overflow, Result_2, UnSigned_Overflow
  LED _1_3 (.in(\_1号中断等待指示 ));
  LED _2_3 (.in(\_2号中断等待指示 ));
  LED _3_3 (.in(\_3号中断等待指示 ));
  Register #(.width(32)) register_1 (.D(rt), .en(controller_1_disp), .Q(SyscallOut), .clk(CLK), .clr(RST));
  // Probe on alu_1_result_2
  // Probe on rt
  Multiplexer #(.select(2), .width(32)) multiplexer_11 (
    .in0(adder_1_out), .in1({{6{1'b0}}, istrsplit_1_imm26}), .in2(adder_2_out), .in3(multiplexer_8_out),
    .out(multiplexer_11_out), .sel(controller_1_m4));  // open: en
  // Probe on \_1号中断 
  // Probe on \_2号中断 
  // Probe on \_3号中断 
  // MIPS_RAM mips_ram_1: pin names not known; wires that end beside it: alu_1_result_2, rt, alu_1_result_2, controller_1_dmstr, controller_1_dmsel, CLK, controller_1_dmld, RST, mips_ram_1_p9

  // Notes on the sheet:
  //   数码管输出应该用寄存器锁存，否则显示数据只能一闪而过
  //   指令存储器
  //   contents of rom_1 (hex, n*v repeats v):
  //   201d0100 20110001 8000c06 20110001 20120002 20130003 8000c0a 20110001 20120002 20130003 8000c0e
  //   20110001 20120002 20130003 8000c12 20110001 20120002 20130003 c000cf6 20100001 20110001 118fc0
  //   112020 20020022 c 118882 12200001 8000c16 112020 20020022 c 20110001 118880 112020 20020022 c
  //   12200001 8000c20 20110001 118fc0 112020 20020022 c 1188c3 112020 20020022 c 118903 112020 20020022 c
  //   118903 112020 20020022 c 118903 112020 20020022 c 118903 112020 20020022 c 118903 112020 20020022 c
  //   118903 112020 20020022 c 118903 112020 20020022 c 20100001 109fc0 139fc3 8021 2012000c 24160003
  //   26100001 3210000f 20080008 20090001 139900 2709825 132020 20020022 c 1094022 1500fff9 22100001
  //   2018000f 2188024 108700 20080008 20090001 139902 2709825 132021 20020022 c 1094022 1500fff9 108702
  //   2c9b022 12c00001 8000c51 4020 1084027 84400 3508ffff 82021 20020022 c 2010ffff 20110000 ae300000
  //   22100001 22310004 ae300000 22100001 22310004 ae300000 22100001 22310004 ae300000 22100001 22310004
  //   ae300000 22100001 22310004 ae300000 22100001 22310004 ae300000 22100001 22310004 ae300000 22100001
  //   22310004 ae300000 22100001 22310004 ae300000 22100001 22310004 ae300000 22100001 22310004 ae300000
  //   22100001 22310004 ae300000 22100001 22310004 ae300000 22100001 22310004 ae300000 22100001 22310004
  //   ae300000 22100001 22310004 22100001 8020 2011003c 8e130000 8e340000 274402a 11000002 ae330000
  //   ae140000 2231fffc 1611fff8 102020 20020022 c 22100004 2011003c 1611fff2 20020032 c 20080001 20090003
  //   20110876 118d00 112020 20020022 c 200b0008 1118806 1318806 112020 20020022 c 216bffff 1560fff9
  //   20090000 200b0020 20110000 20120001 a1310000 112020 20020022 c 2328820 21290001 216bffff 1560fff8
  //   200b0008 20090000 8d310000 112020 20020022 c 21290004 216bffff 1560fff9 2011fff1 112020 20020022 c
  //   22310001 620fffb 20080001 20090003 20110876 118d00 112020 20020022 c 200b0008 1118807 1318807 112020
  //   20020022 c 216bffff 1560fff9 2002000a c 2002000a c 20100000 22100001 102020 20020022 c 22100002
  //   102020 20020022 c 22100003 102020 20020022 c 22100004 102020 20020022 c 22100005 102020 20020022 c
  //   22100006 102020 20020022 c 22100007 102020 20020022 c 22100008 102020 20020022 20020022 c 3e00008
  //   afb00000 23bd0004 afb30000 23bd0004 afb40000 23bd0004 afb50000 23bd0004 afb60000 23bd0004 afa20000
  //   23bd0004 afa40000 23bd0004 40020000 afa20000 23bd0004 40000000 20160001 20140006 20150001 168020
  //   108100 2149825 132020 20020022 c 1600fffa 295a022 1680fff7 40800000 20010004 3a1e822 8fa20000
  //   40820000 20010004 3a1e822 8fa40000 20010004 3a1e822 8fa20000 20010004 3a1e822 8fb60000 20010004
  //   3a1e822 8fb50000 20010004 3a1e822 8fb40000 20010004 3a1e822 8fb30000 20010004 3a1e822 8fb00000
  //   40000000 42000018 2002000a c afb00000 23bd0004 afb30000 23bd0004 afb40000 23bd0004 afb50000 23bd0004
  //   afb60000 23bd0004 afa20000 23bd0004 afa40000 23bd0004 40020000 afa20000 23bd0004 40000000 20160002
  //   20140006 20150001 168020 108100 2149825 132020 20020022 c 1600fffa 295a022 1680fff7 40800000
  //   20010004 3a1e822 8fa20000 40820000 20010004 3a1e822 8fa40000 20010004 3a1e822 8fa20000 20010004
  //   3a1e822 8fb60000 20010004 3a1e822 8fb50000 20010004 3a1e822 8fb40000 20010004 3a1e822 8fb30000
  //   20010004 3a1e822 8fb00000 40000000 42000018 2002000a c afb00000 23bd0004 afb30000 23bd0004 afb40000
  //   23bd0004 afb50000 23bd0004 afb60000 23bd0004 afa20000 23bd0004 afa40000 23bd0004 40020000 afa20000
  //   23bd0004 40000000 20160003 20140006 20150001 168020 108100 2149825 132020 20020022 c 1600fffa
  //   295a022 1680fff7 40800000 20010004 3a1e822 8fa20000 40820000 20010004 3a1e822 8fa40000 20010004
  //   3a1e822 8fa20000 20010004 3a1e822 8fb60000 20010004 3a1e822 8fb50000 20010004 3a1e822 8fb40000
  //   20010004 3a1e822 8fb30000 20010004 3a1e822 8fb00000 40000000 42000018 2002000a c
  //   可以通过项目增加Logisim库的方式将前几次实验完成的电路作为子电路引入到本电路中使用
  //   数码管输出
  //   寄存器文件
  //   IE写0视为开中断
  //   总复位信号应将除ROM以外所有存储组件全部清零
  //   M1
  //   M2
  //   M3
  //   M4
  //   中断信号源及指示电路规范（优先级3>2>1>CPU(0）)
  //   数据存储器
endmodule

// Sign Extend
module SignExtend (
  input  [15:0] in_1,
  output [31:0] out_2
);


  assign out_2 = {{17{in_1[15]}}, in_1[14:0]};
endmodule

module IstrSplit (
  input  [31:0] Istr,
  output eret,
  output [31:0] istrOut,
  output [5:0] OP,
  output [5:0] FUNC,
  output [4:0] RS,
  output [4:0] RT,
  output [4:0] RD,
  output [15:0] IMM16,
  output [25:0] IMM26,
  output [4:0] SHAMT,
  output Syscall
);

  wire comparator_2_eq, ISR, NR;

  Comparator #(.width(6)) comparator_1 (.a(Istr[31:26]), .b({6{1'b0}}), .eq(ISR));  // open: gt, lt
  Comparator #(.width(6)) comparator_2 (.a(Istr[5:0]), .b(6'b001100), .eq(comparator_2_eq));  // open: gt, lt
  Comparator #(.width(32), .mode("unsigned")) comparator_3 (.a(32'h42000018), .b(Istr), .eq(eret));  // open: gt, lt
  not not_1 (NR, ISR);
  and and_1 (Syscall, comparator_2_eq, ISR);
  Multiplexer #(.width(5)) multiplexer_1 (.in0(Istr[25:21]), .in1(5'b00010), .out(RS), .sel(Syscall));  // open: en
  Multiplexer #(.width(5)) multiplexer_2 (.in0(Istr[20:16]), .in1(5'b00100), .out(RT), .sel(Syscall));  // open: en

  assign FUNC = Istr[5:0];
  assign IMM16 = Istr[15:0];
  assign IMM26 = Istr[25:0];
  assign istrOut = Istr;
  assign OP = Istr[31:26];
  assign RD = Istr[15:11];
  assign SHAMT = Istr[10:6];

  // Other names for the same wires on the sheet: RT_t[4:0] = Istr[20:16]; RS_t[4:0] = Istr[25:21]; SYSCAL = Syscall
endmodule

module Controller (
  input  [5:0] OP,
  input  [5:0] FUNCT,
  input  [31:0] RS,
  input  [31:0] istr,
  input  EQU,
  input  [4:0] RT,
  output [3:0] Alu,
  output [1:0] M2,
  output DmLd,
  output Sha,
  output BrCount,
  output efc,
  output CLI,
  output RegWrite,
  output [1:0] M3,
  output [3:0] DmSel,
  output Halt,
  output BCount,
  output etc,
  output Disp,
  output JCount,
  output [1:0] M1,
  output [1:0] M4,
  output DmStr,
  output STI
);

  wire ADD, add_t, ADDI, ADDIU, ADDU, AND, and_33_out, and_34_out, and_35_out, and_36_out, and_37_out, and_t,
       ANDI, BEQ, BLTZ, BNE, cmpu, comparator_3_eq, comparator_4_eq, comparator_5_eq, comparator_6_eq,
       comparator_7_eq, comparator_8_eq, comparator_9_eq, comparator_10_eq, comparator_11_eq,
       comparator_12_eq, comparator_13_eq, comparator_14_eq, comparator_15_eq, comparator_16_eq,
       comparator_17_eq, comparator_18_eq, comparator_19_eq, comparator_20_eq, comparator_21_eq,
       comparator_22_eq, comparator_23_eq, comparator_24_eq, comparator_25_eq, comparator_26_eq,
       comparator_27_eq, comparator_28_eq, comparator_29_eq, comparator_30_eq, comparator_33_eq,
       comparator_34_eq, comparator_35_eq, comparator_36_eq, comparator_37_eq, comparator_38_eq, EFC_t,
       ETC_t, ISR, J, JR, LESS, NOR, NR, OR, or_t, ORI, SB, SLL, SLT, SLTI, SLTU, SRA, sra_t, SRAV, SRL,
       srl_t, SRLV, SUB, SW, SYSCAL;

  Comparator #(.width(32)) comparator_1 (.a(RS), .b({32{1'b0}}), .lt(LESS));  // open: gt, eq
  Comparator #(.width(6)) comparator_2 (.a(OP), .b({6{1'b0}}), .eq(ISR));  // open: gt, lt
  not not_1 (NR, ISR);
  Comparator #(.width(6)) comparator_3 (.a(OP), .b(6'b001000), .eq(comparator_3_eq));  // open: gt, lt
  Comparator #(.width(6)) comparator_4 (.a(OP), .b(6'b001001), .eq(comparator_4_eq));  // open: gt, lt
  Comparator #(.width(6)) comparator_5 (.a(OP), .b(6'b001100), .eq(comparator_5_eq));  // open: gt, lt
  Comparator #(.width(6)) comparator_6 (.a(OP), .b(6'b001101), .eq(comparator_6_eq));  // open: gt, lt
  Comparator #(.width(6)) comparator_7 (.a(OP), .b(6'b100011), .eq(comparator_7_eq));  // open: gt, lt
  Comparator #(.width(6)) comparator_8 (.a(OP), .b(6'b101011), .eq(comparator_8_eq));  // open: gt, lt
  Comparator #(.width(6)) comparator_9 (.a(OP), .b(6'b000100), .eq(comparator_9_eq));  // open: gt, lt
  Comparator #(.width(6)) comparator_10 (.a(OP), .b(6'b000101), .eq(comparator_10_eq));  // open: gt, lt
  Comparator #(.width(6)) comparator_11 (.a(OP), .b(6'b001010), .eq(comparator_11_eq));  // open: gt, lt
  Comparator #(.width(6)) comparator_12 (.a(OP), .b(6'b000010), .eq(comparator_12_eq));  // open: gt, lt
  Comparator #(.width(6)) comparator_13 (.a(OP), .b(6'b000011), .eq(comparator_13_eq));  // open: gt, lt
  Comparator #(.width(6)) comparator_14 (.a(OP), .b(6'b101000), .eq(comparator_14_eq));  // open: gt, lt
  Comparator #(.width(6)) comparator_15 (.a(OP), .b(6'b000001), .eq(comparator_15_eq));  // open: gt, lt
  and and_1 (ADDI, comparator_3_eq, NR);
  and and_2 (ADDIU, comparator_4_eq, NR);
  and and_3 (ANDI, comparator_5_eq, NR);
  and and_4 (ORI, comparator_6_eq, NR);
  and and_5 (DmLd, comparator_7_eq, NR);
  and and_6 (SW, comparator_8_eq, NR);
  and and_7 (BEQ, comparator_9_eq, NR);
  and and_8 (BNE, comparator_10_eq, NR);
  and and_9 (SLTI, comparator_11_eq, NR);
  and and_10 (J, comparator_12_eq, NR);
  and and_11 (M3[1], comparator_13_eq, NR);
  and and_12 (SB, comparator_14_eq, NR);
  and and_13 (BLTZ, comparator_15_eq, NR);
  // Probe on istr[31:21]
  Comparator #(.width(6)) comparator_16 (.a(FUNCT), .b(6'b100000), .eq(comparator_16_eq));  // open: gt, lt
  Comparator #(.width(6)) comparator_17 (.a(FUNCT), .b(6'b100001), .eq(comparator_17_eq));  // open: gt, lt
  Comparator #(.width(6)) comparator_18 (.a(FUNCT), .b(6'b100100), .eq(comparator_18_eq));  // open: gt, lt
  Comparator #(.width(6)) comparator_19 (.a(FUNCT), .b(6'b100010), .eq(comparator_19_eq));  // open: gt, lt
  Comparator #(.width(6)) comparator_20 (.a(FUNCT), .b(6'b100101), .eq(comparator_20_eq));  // open: gt, lt
  Comparator #(.width(6)) comparator_21 (.a(FUNCT), .b(6'b100111), .eq(comparator_21_eq));  // open: gt, lt
  Comparator #(.width(6)) comparator_22 (.a(FUNCT), .b(6'b101010), .eq(comparator_22_eq));  // open: gt, lt
  Comparator #(.width(6)) comparator_23 (.a(FUNCT), .b(6'b101011), .eq(comparator_23_eq));  // open: gt, lt
  Comparator #(.width(6)) comparator_24 (.a(FUNCT), .b(6'b000110), .eq(comparator_24_eq));  // open: gt, lt
  Comparator #(.width(6)) comparator_25 (.a(FUNCT), .b(6'b000111), .eq(comparator_25_eq));  // open: gt, lt
  Comparator #(.width(6)) comparator_26 (.a(FUNCT), .b({6{1'b0}}), .eq(comparator_26_eq));  // open: gt, lt
  Comparator #(.width(6)) comparator_27 (.a(FUNCT), .b(6'b000011), .eq(comparator_27_eq));  // open: gt, lt
  Comparator #(.width(6)) comparator_28 (.a(FUNCT), .b(6'b000010), .eq(comparator_28_eq));  // open: gt, lt
  Comparator #(.width(6)) comparator_29 (.a(FUNCT), .b(6'b001000), .eq(comparator_29_eq));  // open: gt, lt
  Comparator #(.width(6)) comparator_30 (.a(FUNCT), .b(6'b001100), .eq(comparator_30_eq));  // open: gt, lt
  Comparator #(.width(11)) comparator_31 (.a(istr[31:21]), .b(11'h200), .eq(EFC_t));  // open: gt, lt
  Comparator #(.width(11)) comparator_32 (.a(istr[31:21]), .b(11'h204), .eq(ETC_t));  // open: gt, lt
  and and_14 (ADD, comparator_16_eq, ISR);
  and and_15 (ADDU, comparator_17_eq, ISR);
  and and_16 (AND, comparator_18_eq, ISR);
  and and_17 (SUB, comparator_19_eq, ISR);
  and and_18 (OR, comparator_20_eq, ISR);
  and and_19 (NOR, comparator_21_eq, ISR);
  and and_20 (SLT, comparator_22_eq, ISR);
  and and_21 (SLTU, comparator_23_eq, ISR);
  and and_22 (SRLV, comparator_24_eq, ISR);
  and and_23 (SRAV, comparator_25_eq, ISR);
  and and_24 (SLL, comparator_26_eq, ISR);
  and and_25 (SRA, comparator_27_eq, ISR);
  and and_26 (SRL, comparator_28_eq, ISR);
  and and_27 (JR, comparator_29_eq, ISR);
  and and_28 (SYSCAL, comparator_30_eq, ISR);
  Comparator #(.width(5)) comparator_33 (.a(RT), .b({5{1'b0}}), .eq(comparator_33_eq));  // open: gt, lt
  and and_29 (STI, comparator_33_eq, EFC_t);
  Comparator #(.width(5)) comparator_34 (.a(RT), .b({5{1'b0}}), .eq(comparator_34_eq));  // open: gt, lt
  and and_30 (CLI, comparator_34_eq, ETC_t);
  or or_1 (and_t, AND, ANDI);
  or or_2 (or_t, OR, ORI);
  or or_3 (sra_t, SRA, SRAV);
  or or_4 (srl_t, SRLV, SRL);
  or or_5 (add_t, ADD, ADDI, ADDIU, ADDU, DmLd, SW, SB);
  or or_6 (cmpu, SLT, SLTU, SLTI);
  nor nor_1 (RegWrite, SW, BEQ, BNE, J, SYSCAL, JR, BLTZ, SB);
  Comparator #(.width(5)) comparator_35 (.a(RT), .b({5{1'b0}}), .eq(comparator_35_eq));  // open: gt, lt
  and and_31 (efc, ~comparator_35_eq, EFC_t);  // AND_Gate
  Comparator #(.width(5)) comparator_36 (.a(RT), .b({5{1'b0}}), .eq(comparator_36_eq));  // open: gt, lt
  and and_32 (etc, ~comparator_36_eq, ETC_t);  // AND_Gate
  Multiplexer #(.width(4)) multiplexer_1 (.in0(4'b1111), .in1(4'b0011), .out(DmSel), .sel(SB));  // open: en
  or or_7 (M1[1], SW, M3[1], SB);
  or or_8 (DmStr, SW, SB);
  or or_9 (M1[0], ADD, ADDU, AND, SLL, SRA, SRL, SUB, OR, NOR, SW, SLT, SLTU, SRLV, SRAV, SB);
  or or_10 (M2[1], SLL, SRLV, SRL, M3[1], SRA, SRAV);
  or or_11 (M2[0], SRAV, ADDIU, ANDI, ADDI, ORI, DmLd, SW, SB, M3[1], SLTI, SRLV);
  and and_33 (and_33_out, EQU, BEQ);
  and and_34 (and_34_out, ~EQU, BNE);  // AND_Gate
  and and_35 (and_35_out, BLTZ, LESS);
  or or_12 (M4[1], and_33_out, and_34_out, and_35_out, JR);
  or or_13 (JCount, JR, M3[1], J);
  AluCtrl aluctrl_1 (
    .add(add_t), .sub(SUB), .\and (and_t), .\or (or_t), .sra(sra_t), .srl(srl_t), .sll(SLL), .cmpu(cmpu),
    .\nor (NOR), .A3(Alu[3]), .A2(Alu[2]), .A1(Alu[1]), .A0(Alu[0]));
  Comparator #(.width(32)) comparator_37 (.a(RS), .b(32'ha), .eq(comparator_37_eq));  // open: gt, lt
  Comparator #(.width(32)) comparator_38 (.a(RS), .b(32'ha), .eq(comparator_38_eq));  // open: gt, lt
  and and_36 (and_36_out, EQU, BEQ);
  or or_14 (BrCount, and_36_out, and_37_out);
  and and_37 (and_37_out, ~EQU, BNE);  // AND_Gate
  or or_15 (BCount, BEQ, BNE);
  or or_16 (Sha, SLL, SRAV, SRL, SRLV, SRA);
  and and_38 (Disp, SYSCAL, ~comparator_37_eq);  // AND_Gate
  and and_39 (Halt, SYSCAL, comparator_38_eq);

  assign M3[0] = DmLd;
  assign M4[0] = JCount;

  // Other names for the same wires on the sheet: EQUAL = EQU; LD = DmLd; LW = DmLd; M30 = DmLd; JAL = M3[1];
  //   M40 = JCount; SEL[3:0] = DmSel; STR = DmStr; WE = RegWrite

  // Notes on the sheet:
  //   SRAV, SRLV, SB, BLTZ
endmodule

module AluCtrl (
  input  add,
  input  sub,
  input  \and ,
  input  \or ,
  input  sra,
  input  srl,
  input  sll,
  input  cmpu,
  input  \nor ,
  output A3,
  output A2,
  output A1,
  output A0
);

  wire and_2_out, and_3_out, and_4_out, and_5_out, and_6_out, and_7_out, and_8_out, and_9_out, not_1_out,
       not_2_out, not_3_out, not_4_out, not_5_out, not_6_out, not_7_out, not_8_out, not_9_out, not_10_out,
       not_11_out, not_12_out, not_13_out, not_14_out, not_15_out, not_16_out, not_17_out, not_18_out,
       not_19_out, not_20_out, not_21_out, not_22_out, not_23_out, not_24_out, not_25_out, not_26_out,
       not_27_out, not_28_out, not_29_out, not_30_out, not_31_out, not_32_out, not_33_out, not_34_out,
       not_35_out, not_36_out, not_37_out, not_38_out, not_39_out, not_40_out, not_41_out, not_42_out,
       not_43_out, not_44_out, not_45_out, not_46_out, not_47_out, not_48_out, not_49_out, not_50_out,
       not_51_out, not_52_out, not_53_out, not_54_out;

  not not_1 (not_1_out, add);
  not not_2 (not_2_out, sub);
  not not_3 (not_3_out, \and );
  not not_4 (not_4_out, sra);
  not not_5 (not_5_out, srl);
  not not_6 (not_6_out, sll);
  not not_7 (not_7_out, \or );
  not not_8 (not_8_out, sra);
  not not_9 (not_9_out, srl);
  not not_10 (not_10_out, sll);
  not not_11 (not_11_out, cmpu);
  not not_12 (not_12_out, \nor );
  not not_13 (not_13_out, \or );
  not not_14 (not_14_out, sra);
  not not_15 (not_15_out, srl);
  not not_16 (not_16_out, sll);
  not not_17 (not_17_out, \nor );
  not not_18 (not_18_out, \or );
  not not_19 (not_19_out, sra);
  not not_20 (not_20_out, srl);
  not not_21 (not_21_out, sll);
  not not_22 (not_22_out, \nor );
  not not_23 (not_23_out, \or );
  not not_24 (not_24_out, sra);
  not not_25 (not_25_out, srl);
  not not_26 (not_26_out, sll);
  not not_27 (not_27_out, \nor );
  not not_28 (not_28_out, add);
  not not_29 (not_29_out, sub);
  not not_30 (not_30_out, \and );
  not not_31 (not_31_out, \or );
  not not_32 (not_32_out, sra);
  not not_33 (not_33_out, srl);
  not not_34 (not_34_out, sll);
  not not_35 (not_35_out, \nor );
  not not_36 (not_36_out, add);
  not not_37 (not_37_out, \or );
  not not_38 (not_38_out, sra);
  not not_39 (not_39_out, sll);
  not not_40 (not_40_out, cmpu);
  not not_41 (not_41_out, add);
  not not_42 (not_42_out, sub);
  not not_43 (not_43_out, \and );
  not not_44 (not_44_out, \or );
  not not_45 (not_45_out, sra);
  not not_46 (not_46_out, srl);
  not not_47 (not_47_out, sll);
  not not_48 (not_48_out, \nor );
  not not_49 (not_49_out, sub);
  not not_50 (not_50_out, \or );
  not not_51 (not_51_out, srl);
  not not_52 (not_52_out, sll);
  not not_53 (not_53_out, cmpu);
  not not_54 (not_54_out, \nor );
  and and_1 (A3, not_1_out, not_2_out, not_3_out, not_4_out, not_5_out, not_6_out);
  and and_2 (and_2_out, not_7_out, not_8_out, not_9_out, not_10_out, not_11_out, not_12_out);
  and and_3 (and_3_out, \and , not_13_out, not_14_out, not_15_out, not_16_out, not_17_out);
  and and_4 (and_4_out, sub, not_18_out, not_19_out, not_20_out, not_21_out, not_22_out);
  and and_5 (and_5_out, add, not_23_out, not_24_out, not_25_out, not_26_out, not_27_out);
  and and_6 (and_6_out, not_28_out, not_29_out, not_30_out, not_31_out, not_32_out, not_33_out, not_34_out, not_35_out);
  and and_7 (and_7_out, not_36_out, not_37_out, not_38_out, not_39_out, not_40_out);
  and and_8 (and_8_out, not_41_out, not_42_out, not_43_out, not_44_out, not_45_out, not_46_out, not_47_out, not_48_out);
  and and_9 (and_9_out, not_49_out, not_50_out, not_51_out, not_52_out, not_53_out, not_54_out);
  or or_1 (A2, and_2_out, and_3_out, and_4_out, and_5_out);
  or or_2 (A1, and_6_out, and_7_out);
  or or_3 (A0, and_8_out, and_9_out);
endmodule

module InstCounter (
  input  CLK,
  input  Halt,
  input  CLR,
  input  Bcount,
  input  Jcount,
  input  Brcount,
  output [15:0] J,
  output [15:0] B,
  output [15:0] Br,
  output [15:0] All
);

  wire [15:0] adder_1_out, adder_2_out, adder_3_out, adder_4_out, multiplexer_1_out, multiplexer_2_out,
       multiplexer_3_out;

  Register #(.width(16)) register_1 (.D(adder_1_out), .en(Halt), .Q(All), .clk(CLK), .clr(CLR));
  Register #(.width(16)) register_2 (.D(adder_2_out), .en(Halt), .Q(J), .clk(CLK), .clr(CLR));
  Register #(.width(16)) register_3 (.D(adder_3_out), .en(Halt), .Q(B), .clk(CLK), .clr(CLR));
  Register #(.width(16)) register_4 (.D(adder_4_out), .en(Halt), .Q(Br), .clk(CLK), .clr(CLR));
  Adder #(.width(16)) adder_1 (.a(All), .b(16'h1), .out(adder_1_out));  // open: cin, cout
  Adder #(.width(16)) adder_2 (.a(J), .b(multiplexer_1_out), .out(adder_2_out));  // open: cin, cout
  Multiplexer #(.width(16)) multiplexer_1 (
    .in0({16{1'b0}}), .in1(16'h1), .out(multiplexer_1_out), .sel(Jcount));  // open: en
  Adder #(.width(16)) adder_3 (.a(B), .b(multiplexer_2_out), .out(adder_3_out));  // open: cin, cout
  Multiplexer #(.width(16)) multiplexer_2 (
    .in0({16{1'b0}}), .in1(16'h1), .out(multiplexer_2_out), .sel(Bcount));  // open: en
  Adder #(.width(16)) adder_4 (.a(Br), .b(multiplexer_3_out), .out(adder_4_out));  // open: cin, cout
  Multiplexer #(.width(16)) multiplexer_3 (
    .in0({16{1'b0}}), .in1(16'h1), .out(multiplexer_3_out), .sel(Brcount));  // open: en
endmodule

module lock (
  input  en,
  input  Clk,
  input  rst,
  output En_2
);

  wire register_1_q;

  Register #(.width(1)) register_1 (.D(en), .en(En_2), .Q(register_1_q), .clk(Clk), .clr(rst));
  not not_1 (En_2, register_1_q);
endmodule

// IR
module button_int (
  input  _1st,
  input  _2nd,
  input  _3rd,
  input  Clk,
  input  clr_1,
  input  clr_2,
  input  clr_3,
  input  Rst,
  output _1st_int_wait,
  output _2nd_int_wait,
  output _3rd_int_wait,
  output and_1,
  output and_2,
  output and_3
);

  wire and_1_out, and_2_out, and_3_out, d_ff_1_q, d_ff_2_q, d_ff_3_q, or_4_out, or_5_out, or_6_out;

  LED \_1号中断等待指示灯  (.in(_1st_int_wait));
  LED \_2号中断等待指示灯  (.in(_2nd_int_wait));
  LED \_3号中断等待指示灯  (.in(_3rd_int_wait));
  D_Flip_Flop d_ff_1 (.clk(_1st), .D(1'b1), .Q(d_ff_1_q), .reset(and_1));  // open: Qn, preset, en
  or or_1 (_1st_int_wait, and_1, d_ff_1_q);
  D_Flip_Flop d_ff_2 (.clk(_2nd), .D(1'b1), .Q(d_ff_2_q), .reset(and_2));  // open: Qn, preset, en
  or or_2 (_2nd_int_wait, and_2, d_ff_2_q);
  D_Flip_Flop d_ff_3 (.clk(_3rd), .D(1'b1), .Q(d_ff_3_q), .reset(and_3));  // open: Qn, preset, en
  or or_3 (_3rd_int_wait, and_3, d_ff_3_q);
  or or_4 (or_4_out, d_ff_1_q, and_1);
  and u_and_1 (and_1_out, or_4_out, ~clr_1);  // AND_Gate
  or or_5 (or_5_out, d_ff_2_q, and_2);
  and u_and_2 (and_2_out, or_5_out, ~clr_2);  // AND_Gate
  or or_6 (or_6_out, d_ff_3_q, and_3);
  and u_and_3 (and_3_out, or_6_out, ~clr_3);  // AND_Gate
  D_Flip_Flop IR1 (.clk(Clk), .D(and_1_out), .Q(and_1), .preset(_1st), .reset(Rst));  // open: Qn, en
  D_Flip_Flop IR2 (.clk(Clk), .D(and_2_out), .Q(and_2), .preset(_2nd), .reset(Rst));  // open: Qn, en
  D_Flip_Flop IR3 (.clk(Clk), .D(and_3_out), .Q(and_3), .preset(_3rd), .reset(Rst));  // open: Qn, en

  // Notes on the sheet:
  //   Reset 
  //   Reset 
  //   Reset 
endmodule

module INM (
  input  Clk,
  input  INM_1,
  input  INM_2,
  input  INM_3,
  input  Rst,
  input  en_1,
  input  en_2,
  input  en_3,
  input  init_1,
  input  init_2,
  input  init_3,
  output Out_1,
  output Out_2,
  output Out_3
);

  D_Flip_Flop INM1 (.clk(Clk), .D(INM_1), .Q(Out_1), .preset(init_1), .en(en_1), .reset(Rst));  // open: Qn
  D_Flip_Flop INM2 (.clk(Clk), .D(INM_2), .Q(Out_2), .preset(init_2), .en(en_2), .reset(Rst));  // open: Qn
  D_Flip_Flop INM3 (.clk(Clk), .D(INM_3), .Q(Out_3), .preset(init_3), .en(en_3), .reset(Rst));  // open: Qn
endmodule

module IDT (
  input  [1:0] Index,
  output [31:0] Addr
);

  Multiplexer #(.select(2), .width(32)) multiplexer_1 (
    .in1(32'h119), .in2(32'h155), .in3(32'h191), .out(Addr), .sel(Index));  // open: in0, en
endmodule

module IE (
  input  Clk,
  input  Istr,
  input  Rst,
  input  en,
  output ie
);

  D_Flip_Flop d_ff_1 (.clk(Clk), .D(Istr), .Qn(ie), .en(en), .reset(Rst));  // open: Q, preset
endmodule

module EPC (
  input  Clk,
  input  Rst,
  input  en,
  input  [31:0] PC_CUR,
  output [31:0] PC_EPC
);

  Register #(.width(32)) EPC (.D(PC_CUR), .en(en), .Q(PC_EPC), .clk(Clk), .clr(Rst));
endmodule

// Wait_Int
module wait_int (
  input  CLK,
  input  ie,
  input  \_1号中断 ,
  input  int1,
  input  \_2号中断 ,
  input  int2,
  input  \_3号中断 ,
  input  int3,
  output IntC
);

  wire _1st_int_wait, _2st_int_wait, _3st_int_wait, and_1_out, and_2_out, and_3_out, and_4_out, and_5_out,
       and_6_out, and_7_out, and_8_out, and_9_out, and_10_out, and_11_out, and_12_out, and_13_out, d_ff_1_q,
       d_ff_2_q, d_ff_3_q, IR1_2_q, IR1_q, IR2_q, or_4_out, or_5_out, or_6_out, or_7_out;

  LED \_1号中断等待指示灯  (.in(_1st_int_wait));
  LED \_2号中断等待指示灯  (.in(_2st_int_wait));
  LED \_3号中断等待指示灯  (.in(_3st_int_wait));
  or or_1 (_1st_int_wait, IR1_q, d_ff_1_q);
  or or_2 (_2st_int_wait, IR2_q, d_ff_2_q);
  or or_3 (_3st_int_wait, IR1_2_q, d_ff_3_q);
  D_Flip_Flop d_ff_1 (.clk(\_1号中断 ), .D(1'b1), .Q(d_ff_1_q), .reset(IR1_q));  // open: Qn, preset, en
  D_Flip_Flop d_ff_2 (.clk(\_2号中断 ), .D(1'b1), .Q(d_ff_2_q), .reset(IR2_q));  // open: Qn, preset, en
  D_Flip_Flop d_ff_3 (.clk(\_3号中断 ), .D(1'b1), .Q(d_ff_3_q), .reset(IR1_2_q));  // open: Qn, preset, en
  or or_4 (or_4_out, d_ff_1_q, IR1_q);
  and and_1 (and_1_out, or_4_out, ~and_2_out);  // AND_Gate
  and and_2 (and_2_out, int1, IntC);
  or or_5 (or_5_out, d_ff_2_q, IR2_q);
  and and_3 (and_3_out, or_5_out, ~and_4_out);  // AND_Gate
  and and_4 (and_4_out, int2, IntC);
  or or_6 (or_6_out, d_ff_3_q, IR1_2_q);
  and and_5 (and_5_out, or_6_out, ~and_6_out);  // AND_Gate
  and and_6 (and_6_out, int3, IntC);
  D_Flip_Flop IR1 (.clk(CLK), .D(and_1_out), .Q(IR1_q), .preset(and_7_out));  // open: Qn, en, reset
  and and_7 (and_7_out, \_1号中断 , ~int1);  // AND_Gate
  D_Flip_Flop IR2 (.clk(CLK), .D(and_3_out), .Q(IR2_q), .preset(and_8_out));  // open: Qn, en, reset
  and and_8 (and_8_out, \_2号中断 , ~int2);  // AND_Gate
  D_Flip_Flop IR1_2 (.clk(CLK), .D(and_5_out), .Q(IR1_2_q), .preset(and_9_out));  // open: Qn, en, reset
  and and_9 (and_9_out, \_3号中断 , ~int3);  // AND_Gate
  and and_10 (and_10_out, IR1_q, int1);
  and and_11 (and_11_out, int2, IR2_q);
  and and_12 (and_12_out, int3, IR1_2_q);
  or or_7 (or_7_out, and_10_out, and_11_out, and_12_out);
  and and_13 (and_13_out, ~CLK, ie);  // AND_Gate
  and and_14 (IntC, and_13_out, or_7_out);

  // Notes on the sheet:
  //   Reset 
  //   Reset 
  //   Reset 
endmodule
