// Logisim project cpu_redirect_int.circ as structural Verilog: 21 circuits, main circuit cpu
module cpu (
);

  wire \_1号中断 , \_1号中断等待指示 , \_2号中断 , \_2号中断等待指示 , \_3号中断 , \_3号中断等待指示 , addr_1_addrsel, branch_1_disp,
       branch_1_halt, branch_1_pause, cli, CLK, conflitctrl_1_id_ex_clear, controller_1_p12,
       controller_1_p13, controller_1_p14, controller_1_p16, controller_1_p21, Ctrl, efc, En, EQUAL, eret,
       etc, ex_mem_1_dispout, ex_mem_1_dmldout, ex_mem_1_dmstrout, ex_mem_1_haltout, ex_mem_1_pauseout,
       id_ex_1_dmldout, id_ex_1_dmstrout, id_ex_1_shaout, istrsplit_1_syscall, LESS, mem_wb_1_haltout,
       mem_wb_1_pauseout, or_1_out, or_2_out, PAU, Pause, PcCtrl, power, RST, WE, WE_DE, WE_ID, WE_ME;
  wire [1:0] branch_1_m4out, controller_1_p17, controller_1_p19, controller_1_p20, controller_1_p22,
       ex_mem_1_m3out, id_ex_1_m1out, id_ex_1_m2out, id_ex_1_m3out, id_ex_1_m4out, mem_wb_1_m3out,
       redirect_1_rs_sel, redirect_1_rt_sel;
  wire [3:0] controller_1_p15, controller_1_p18, ex_mem_1_dmselout, id_ex_1__5bout4, id_ex_1_aluout,
       id_ex_1_dmselout;
  wire [4:0] addr_1_m1out, controller_1_p11, ex_mem_1__5bout1, id_ex_1__5bout1, id_ex_1__5bout2,
       id_ex_1__5bout3, int_ctrl, istrsplit_1_rd, istrsplit_1_rs, istrsplit_1_rt, istrsplit_1_shamt,
       registerfile_1_p4;
  wire [4:1] ex_mem_1__5bout4;
  wire [5:0] istrsplit_1_func, istrsplit_1_op;
  wire [15:0] istrsplit_1_imm16, \总周期数 , \无条件分支指令数 , \有条件分支成功跳转 , \有条件分支指令数 ;
  wire [25:0] istrsplit_1_imm26;
  wire [29:0] Istr, Istr1, Istr2, Istr3;
  wire [31:0] addr_1_m4out, address_1_addrout, address_1_pcout, alu_1_result, controller_1_p9,
       controller_1_p10, epc, ex_mem_1__32bout2, ex_mem_1__32bout3, ex_mem_1__32bout4, id_ex_1__32bout1,
       id_ex_1__32bout2, id_ex_1__32bout3, id_ex_1__32bout4, id_ex_1_r1out, id_ex_1_r2out, if_id_1_instrout,
       if_id_1_pcout, int_1_addrin, istrsplit_1_istrout, mem_wb_1__32bout1, mem_wb_1__32bout2,
       mem_wb_1__32bout3, mips_ram_1_p8, multiplexer_1_out, multiplexer_2_out, multiplexer_3_out,
       pc_1_addrout, redirectmux_1_rsout, registerfile_1_p1, rom_1_data, romshm_1_dataout, rt,
       signextend_1_out_2, SyscallOut;

  \int  int_1 (
    .etc(etc), .cli(cli), .\_1号中断 (\_1号中断 ), .rst(RST), .\_2号中断 (\_2号中断 ), .rt(rt), .PcOut(address_1_pcout),
    .eret(eret), .sti(int_ctrl[2]), .\_3号中断 (\_3号中断 ), .clk(CLK), .AddrIn(int_1_addrin), .epc(epc),
    .inf({\_3号中断等待指示 , \_2号中断等待指示 , \_1号中断等待指示 }));
  Ctrl ctrl_1 (.En(En), .Pause(Pause), .PAU(PAU), .Ctrl(Ctrl), .PcCtrl(PcCtrl), .Power(power));
  PC pc_1 (.AddrIn(int_1_addrin), .Clk(CLK), .Rst(RST), .PcCtrl(PcCtrl), .AddrOut(pc_1_addrout));
  Button _1 (.out(\_1号中断 ));
  Button _2 (.out(\_2号中断 ));
  Button _3 (.out(\_3号中断 ));
  InstCounter instcounter_1 (
    .CLK(CLK), .Halt(Ctrl), .CLR(RST), .EQUAL(EQUAL), .LESS(LESS), .J(\无条件分支指令数 ), .B(\有条件分支指令数 ),
    .Br(\有条件分支成功跳转 ), .All(\总周期数 ), .IstrIn(Istr1));
  Address address_1 (
    .AddrIn(pc_1_addrout[9:0]), .AddrBranch(addr_1_m4out), .Sel(addr_1_addrsel), .AddrOut(address_1_addrout),
    .PcOut(address_1_pcout));
  ROM #(.addrWidth(10), .dataWidth(32)) rom_1 (.addr(pc_1_addrout[9:0]), .data(rom_1_data));  // open: sel
  LED _1_2 (.in(\_1号中断等待指示 ));
  LED _2_2 (.in(\_2号中断等待指示 ));
  LED _3_2 (.in(\_3号中断等待指示 ));
  IF_ID if_id_1 (
    .InstrIn(rom_1_data), .\传输状态In (PcCtrl), .CLK(CLK), .InstrOut(if_id_1_instrout), .\同步清零 (or_1_out),
    .PcIn(address_1_addrout), .PcOut(if_id_1_pcout), .\异步清零 (RST));  // open: 传输状态Out
  or or_1 (or_1_out, addr_1_addrsel, eret);
  IstrSplit istrsplit_1 (
    .in_1(if_id_1_instrout), .OP(istrsplit_1_op), .FUNC(istrsplit_1_func), .RD(istrsplit_1_rd),
    .IMM16(istrsplit_1_imm16), .IMM26(istrsplit_1_imm26), .SHAMT(istrsplit_1_shamt), .RS(istrsplit_1_rs),
    .RT(istrsplit_1_rt), .Syscall(istrsplit_1_syscall), .istrOut(istrsplit_1_istrout));
  // Probe on \_1号中断 
  // Probe on \_2号中断 
  // Probe on \_3号中断 
  // Controller controller_1: pin names not known; wires that end beside it: Istr, WE_ID, istrsplit_1_op, istrsplit_1_rd, istrsplit_1_func, istrsplit_1_rt, istrsplit_1_istrout, istrsplit_1_syscall, controller_1_p9, controller_1_p10, controller_1_p11, controller_1_p12, controller_1_p13, controller_1_p14, controller_1_p15, controller_1_p16, controller_1_p17, controller_1_p18, controller_1_p19, controller_1_p20, controller_1_p21, controller_1_p22
  ConflitCtrl conflitctrl_1 (
    .RS(istrsplit_1_rs), .RD_EX(addr_1_m1out), .RT(istrsplit_1_rt), .Istr1(Istr1), .RD_ID(istrsplit_1_rd),
    .IF_ID_STOP(power), .ID_EX_CLEAR(conflitctrl_1_id_ex_clear), .RD_MEM({5{1'b0}}), .Istr2({30{1'b0}}),
    .Istr(Istr));
  Button \u_总复位  (.out(RST));
  Clock clock_1 (.out(CLK));
  Button \continue  (.out(PAU));
  // RegisterFile registerfile_1: pin names not known; wires that end beside it: registerfile_1_p1, CLK, WE, registerfile_1_p4, istrsplit_1_rs, istrsplit_1_rt, controller_1_p9
  SignExtend signextend_1 (.in_1(istrsplit_1_imm16), .out_2(signextend_1_out_2));
  Hex_Digit_Display hex_digit_display_1 (.value(SyscallOut[27:24]));  // open: dp
  Hex_Digit_Display hex_digit_display_2 (.value(SyscallOut[31:28]));  // open: dp
  ID_EX id_ex_1 (
    ._32bIn3({{6{1'b0}}, istrsplit_1_imm26}), ._32bOut3(id_ex_1__32bout3), ._32bIn4(if_id_1_pcout),
    ._32bOut4(id_ex_1__32bout4), .\传输状态In (Ctrl), .CLK(CLK), .\同步清零 (or_2_out), ._32bIn2(signextend_1_out_2),
    ._32bOut2(id_ex_1__32bout2), ._32bIn1({{27{1'b0}}, istrsplit_1_shamt}), ._32bOut1(id_ex_1__32bout1),
    .R2In(controller_1_p9), .R2Out(id_ex_1_r2out), .R1In(controller_1_p10), .R1Out(id_ex_1_r1out),
    ._5bIn2(istrsplit_1_rt), ._5bOut2(id_ex_1__5bout2), ._5bIn1(istrsplit_1_rd), ._5bOut1(id_ex_1__5bout1),
    .M2In(controller_1_p20), .M2Out(id_ex_1_m2out), .M1In(controller_1_p22), .M1Out(id_ex_1_m1out),
    .DispIn(controller_1_p13), .M4In(controller_1_p17), .M4Out(id_ex_1_m4out), .M3In(controller_1_p19),
    .M3Out(id_ex_1_m3out), .RegWriteIn(WE_ID), .RegWriteOut(WE_DE), .DmStrIn(controller_1_p14),
    .DmStrOut(id_ex_1_dmstrout), .shaIn(controller_1_p21), .shaOut(id_ex_1_shaout),
    .DmLdIn(controller_1_p16), .DmLdOut(id_ex_1_dmldout), .DmSelIn(controller_1_p15),
    .DmSelOut(id_ex_1_dmselout), .AluIn(controller_1_p18), .AluOut(id_ex_1_aluout),
    .haltIn(controller_1_p12), .\异步清零 (RST), .IstrIn(Istr), .IstrOut(Istr1), ._5bIn3(istrsplit_1_rs),
    ._5bOut3(id_ex_1__5bout3), ._5bIn4(controller_1_p11),
    ._5bOut4({eret, id_ex_1__5bout4[3:2], etc, id_ex_1__5bout4[0]}));  // open: 传输状态Out, DispOut, haltOut, efcIn, efcOut
  or or_2 (or_2_out, addr_1_addrsel, eret, conflitctrl_1_id_ex_clear);
  Hex_Digit_Display hex_digit_display_3 (.value(SyscallOut[19:16]));  // open: dp
  Hex_Digit_Display hex_digit_display_4 (.value(SyscallOut[23:20]));  // open: dp
  RedirectMux redirectmux_1 (
    .RS(id_ex_1_r1out), .EX(multiplexer_3_out), .WB(registerfile_1_p1), .RT(id_ex_1_r2out),
    .RSSel(redirect_1_rs_sel), .RSOut(redirectmux_1_rsout), .RTSel(redirect_1_rt_sel), .RTOut(rt));
  Hex_Digit_Display hex_digit_display_5 (.value(SyscallOut[15:12]));  // open: dp
  Hex_Digit_Display hex_digit_display_6 (.value(SyscallOut[11:8]));  // open: dp
  Branch branch_1 (
    .InstrIn(Istr1), .RS(redirectmux_1_rsout), .RT(rt), .M4In(id_ex_1_m4out), .M4Out(branch_1_m4out),
    .Disp(branch_1_disp), .Halt(branch_1_halt), .EQUAL(EQUAL), .LESS(LESS), .Pause(branch_1_pause));
  addr addr_1 (
    .M4(branch_1_m4out), .PC(id_ex_1__32bout4), .IMM26(id_ex_1__32bout3), .IMM16(id_ex_1__32bout2),
    .RS(multiplexer_1_out), .M1(id_ex_1_m1out), .RT(id_ex_1__5bout2), .RD(id_ex_1__5bout1),
    .AddrSel(addr_1_addrsel), .M4Out(addr_1_m4out), .M1Out(addr_1_m1out));
  redirect redirect_1 (
    .RS(id_ex_1__5bout3), .RD_EX(ex_mem_1__5bout1), .RD_MEM(registerfile_1_p4), .RT(id_ex_1__5bout2),
    .Istr1(Istr2), .Istr2(Istr3), .Istr(Istr1), .RT_Sel(redirect_1_rt_sel), .RS_Sel(redirect_1_rs_sel));  // open: RD_ID
  Hex_Digit_Display hex_digit_display_7 (.value(SyscallOut[7:4]));  // open: dp
  Hex_Digit_Display hex_digit_display_8 (.value(SyscallOut[3:0]));  // open: dp
  Multiplexer #(.width(32)) multiplexer_1 (
    .in0(redirectmux_1_rsout), .in1(rt), .out(multiplexer_1_out), .sel(id_ex_1_shaout));  // open: en
  Multiplexer #(.select(2), .width(32)) multiplexer_2 (
    .in0(rt), .in1(id_ex_1__32bout2), .in2(id_ex_1__32bout1), .in3(redirectmux_1_rsout),
    .out(multiplexer_2_out), .sel(id_ex_1_m2out));  // open: en
  ALU alu_1 (
    .AluOP(id_ex_1_aluout), .X(multiplexer_1_out), .Result(alu_1_result), .Y(multiplexer_2_out));  // open: Equal, Signed_Overflow, Result_2, UnSigned_Overflow
  EX_MEM ex_mem_1 (
    ._5bIn1(addr_1_m1out), ._5bOut1(ex_mem_1__5bout1), .DmSelIn(id_ex_1_dmselout),
    .DmSelOut(ex_mem_1_dmselout), .DmLdIn(id_ex_1_dmldout), .DmLdOut(ex_mem_1_dmldout),
    .DmStrIn(id_ex_1_dmstrout), .DmStrOut(ex_mem_1_dmstrout), .RegWriteIn(WE_DE), .RegWriteOut(WE_ME),
    ._32bIn2(alu_1_result), ._32bOut2(ex_mem_1__32bout2), .M3In(id_ex_1_m3out), .M3Out(ex_mem_1_m3out),
    ._32bIn3(rt), ._32bOut3(ex_mem_1__32bout3), .\传输状态In (Ctrl), .DispIn(branch_1_disp),
    .DispOut(ex_mem_1_dispout), .CLK(CLK), .\同步清零 (1'b0), ._32bIn4(id_ex_1__32bout4),
    ._32bOut4(ex_mem_1__32bout4), .haltIn(branch_1_halt), .haltOut(ex_mem_1_haltout), .\异步清零 (RST),
    .IstrIn(Istr1), .IstrOut(Istr2), .pauseIn(branch_1_pause), .pauseOut(ex_mem_1_pauseout),
    ._5bIn4({eret, id_ex_1__5bout4[3:2], etc, id_ex_1__5bout4[0]}), ._5bOut4({ex_mem_1__5bout4, efc}));  // open: _32bIn1, _32bOut1, _1bIn1, _1bOut1, 传输状态Out, _1bOut2, _1bIn2, efcIn, efcOut
  // Probe on \总周期数 
  // Probe on \无条件分支指令数 
  // Probe on \有条件分支指令数 
  // Probe on \有条件分支成功跳转 
  Multiplexer #(.width(32)) multiplexer_3 (
    .in0(ex_mem_1__32bout2), .in1(epc), .out(multiplexer_3_out), .sel(efc));  // open: en
  romshm romshm_1 (.DataIn(ex_mem_1__32bout3), .selIn(ex_mem_1_dmselout), .DataOut(romshm_1_dataout));
  Register #(.width(32)) register_1 (.D(romshm_1_dataout), .en(ex_mem_1_dispout), .Q(SyscallOut), .clk(CLK), .clr(RST));
  // MIPS_RAM mips_ram_1: pin names not known; wires that end beside it: multiplexer_3_out[21:2], romshm_1_dataout, ex_mem_1_dmstrout, ex_mem_1_dmselout, CLK, ex_mem_1_dmldout, RST, mips_ram_1_p8
  MEM_WB mem_wb_1 (
    ._1bIn1(WE_ME), ._1bOut1(WE), ._32bIn1(mips_ram_1_p8), ._32bOut1(mem_wb_1__32bout1),
    ._32bIn2(ex_mem_1__32bout4), ._32bOut2(mem_wb_1__32bout2), ._5bIn1(ex_mem_1__5bout1),
    ._5bOut1(registerfile_1_p4), .M3In(ex_mem_1_m3out), .M3Out(mem_wb_1_m3out), .\传输状态In (Ctrl), .CLK(CLK),
    .\同步清零 (1'b0), ._32bIn3(multiplexer_3_out), ._32bOut3(mem_wb_1__32bout3), .haltIn(ex_mem_1_haltout),
    .haltOut(mem_wb_1_haltout), .\异步清零 (RST), .IstrIn(Istr2), .IstrOut(Istr3), .pauseIn(ex_mem_1_pauseout),
    .pauseOut(mem_wb_1_pauseout), ._5bIn4({ex_mem_1__5bout4, efc}),
    ._5bOut4({int_ctrl[4], cli, int_ctrl[2:0]}));  // open: 传输状态Out, efcIn, efcOut, _32bIn4, _32bOut4
  lock lock_1 (
    .en(mem_wb_1_haltout), .Clk(CLK), .rst(RST), .En_2(En), .pause(Pause), .pauseIn(mem_wb_1_pauseout),
    .cont(PAU));
  Multiplexer #(.select(2), .width(32)) multiplexer_4 (
    .in0(mem_wb_1__32bout3), .in1(mem_wb_1__32bout1), .in2(mem_wb_1__32bout2), .out(registerfile_1_p1),
    .sel(mem_wb_1_m3out));  // open: in3, en

  // Other names for the same wires on the sheet: sti = int_ctrl[2]; int_ctrl[3] = cli

  // Notes on the sheet:
  //   指令存储器
  //   contents of rom_1 (hex, n*v repeats v):
  //   201d0100 20110001 8000c06 20110001 20120002 20130003 8000c0a 20110001 20120002 20130003 8000c0e
  //   20110001 20120002 20130003 8000c12 20110001 20120002 20130003 c000cf6 20100001 20110001 118fc0
  //   112020 20020022 c 118882 12200001 8000c16 112020 20020022 c 20110001 118880 112020 20020022 c
  //   12200001 8000c20 20110001 118fc0 112020 20020022 c 1188c3 112020 20020022 c 118903 112020 20020022 c
  //   118903 112020 20020022 c 118903 112020 20020022 c 118903 112020 20020022 c 118903 112020 20020022 c
  //   118903 112020 20020022 c 118903 112020 20020022 c 20100001 109fc0 139fc3 8021 2012000c 24160003
  //   26100001 3210000f 20080008 20090001 139900 2709825 132020 20020022 c 1094022 1500fff9 22100001
  //   2018000f 2188024 108700 20080008 20090001 139902 2709825 132021 20020022 c 1094022 1500fff9 108702
  //   2c9b022 12c00001 8000c51 4020 1084027 84400 3508ffff 82021 20020022 c 2010ffff 20110000 ae300000
  //   22100001 22310004 ae300000 22100001 22310004 ae300000 22100001 22310004 ae300000 22100001 22310004
  //   ae300000 22100001 22310004 ae300000 22100001 22310004 ae300000 22100001 22310004 ae300000 22100001
  //   22310004 ae300000 22100001 22310004 ae300000 22100001 22310004 ae300000 22100001 22310004 ae300000
  //   22100001 22310004 ae300000 22100001 22310004 ae300000 22100001 22310004 ae300000 22100001 22310004
  //   ae300000 22100001 22310004 22100001 8020 2011003c 8e130000 8e340000 274402a 11000002 ae330000
  //   ae140000 2231fffc 1611fff8 102020 20020022 c 22100004 2011003c 1611fff2 20020032 c 20080001 20090003
  //   20110876 118d00 112020 20020022 c 200b0008 1118806 1318806 112020 20020022 c 216bffff 1560fff9
  //   20090000 200b0020 20110000 20120001 a1310000 112020 20020022 c 2328820 21290001 216bffff 1560fff8
  //   200b0008 20090000 8d310000 112020 20020022 c 21290004 216bffff 1560fff9 2011fff1 112020 20020022 c
  //   22310001 620fffb 20080001 20090003 20110876 118d00 112020 20020022 c 200b0008 1118807 1318807 112020
  //   20020022 c 216bffff 1560fff9 2002000a c 2002000a c 20100000 22100001 102020 20020022 c 22100002
  //   102020 20020022 c 22100003 102020 20020022 c 22100004 102020 20020022 c 22100005 102020 20020022 c
  //   22100006 102020 20020022 c 22100007 102020 20020022 c 22100008 102020 20020022 20020022 c 3e00008
  //   afb00000 23bd0004 afb30000 23bd0004 afb40000 23bd0004 afb50000 23bd0004 afb60000 23bd0004 afa20000
  //   23bd0004 afa40000 23bd0004 40001000 afa20000 23bd0004 40000000 20160001 20140006 20150001 168020
  //   108100 2149825 132020 20020022 c 1600fffa 295a022 1680fff7 40800000 20010004 3a1e822 8fa20000
  //   40820000 20010004 3a1e822 8fa40000 20010004 3a1e822 8fa20000 20010004 3a1e822 8fb60000 20010004
  //   3a1e822 8fb50000 20010004 3a1e822 8fb40000 20010004 3a1e822 8fb30000 20010004 3a1e822 8fb00000
  //   40000000 42000018 2002000a c afb00000 23bd0004 afb30000 23bd0004 afb40000 23bd0004 afb50000 23bd0004
  //   afb60000 23bd0004 afa20000 23bd0004 afa40000 23bd0004 40001000 afa20000 23bd0004 40000000 20160002
  //   20140006 20150001 168020 108100 2149825 132020 20020022 c 1600fffa 295a022 1680fff7 40800000
  //   20010004 3a1e822 8fa20000 40820000 20010004 3a1e822 8fa40000 20010004 3a1e822 8fa20000 20010004
  //   3a1e822 8fb60000 20010004 3a1e822 8fb50000 20010004 3a1e822 8fb40000 20010004 3a1e822 8fb30000
  //   20010004 3a1e822 8fb00000 40000000 42000018 2002000a c afb00000 23bd0004 afb30000 23bd0004 afb40000
  //   23bd0004 afb50000 23bd0004 afb60000 23bd0004 afa20000 23bd0004 afa40000 23bd0004 40001000 afa20000
  //   23bd0004 40000000 20160003 20140006 20150001 168020 108100 2149825 132020 20020022 c 1600fffa
  //   295a022 1680fff7 40800000 20010004 3a1e822 8fa20000 40820000 20010004 3a1e822 8fa40000 20010004
  //   3a1e822 8fa20000 20010004 3a1e822 8fb60000 20010004 3a1e822 8fb50000 20010004 3a1e822 8fb40000
  //   20010004 3a1e822 8fb30000 20010004 3a1e822 8fb00000 40000000 42000018 2002000a c
  //   中断信号源及指示电路规范（优先级3>2>1>CPU(0）)
  //   寄存器文件
  //   数码管输出应该用寄存器锁存，否则显示数据只能一闪而过
  //   可以通过项目增加Logisim库的方式将前几次实验完成的电路作为子电路引入到本电路中使用
  //   数码管输出
  //   sha
  //   M2
  //   总复位信号应将除ROM以外所有存储组件全部清零
  //   数据存储器
  //   M3
endmodule

// Sign Extend
module SignExtend (
  input  [15:0] in_1,
  output [31:0] out_2
);


  assign out_2 = {{17{in_1[15]}}, in_1[14:0]};
endmodule

// Decoder
module IstrSplit (
  input  [31:0] in_1,
  output [5:0] OP,
  output [5:0] FUNC,
  output [4:0] RS,
  output [4:0] RT,
  output [31:0] istrOut,
  output [4:0] RD,
  output [15:0] IMM16,
  output [25:0] IMM26,
  output [4:0] SHAMT,
  output Syscall
);

  wire comparator_2_eq, ISR, NR;

  Comparator #(.width(6)) comparator_1 (.a(in_1[31:26]), .b({6{1'b0}}), .eq(ISR));  // open: gt, lt
  Comparator #(.width(6)) comparator_2 (.a(in_1[5:0]), .b(6'b001100), .eq(comparator_2_eq));  // open: gt, lt
  not not_1 (NR, ISR);
  and and_1 (Syscall, comparator_2_eq, ISR);
  Multiplexer #(.width(5)) multiplexer_1 (.in0(in_1[25:21]), .in1(5'b00010), .out(RS), .sel(Syscall));  // open: en
  Multiplexer #(.width(5)) multiplexer_2 (.in0(in_1[20:16]), .in1(5'b00100), .out(RT), .sel(Syscall));  // open: en

  assign FUNC = in_1[5:0];
  assign IMM16 = in_1[15:0];
  assign IMM26 = in_1[25:0];
  assign istrOut = in_1;
  assign OP = in_1[31:26];
  assign RD = in_1[15:11];
  assign SHAMT = in_1[10:6];

  // Other names for the same wires on the sheet: RT_t[4:0] = in_1[20:16]; RS_t[4:0] = in_1[25:21]; SYSCAL = Syscall
endmodule

module Controller (
  input  [5:0] OP,
  input  [4:0] Rd,
  input  [4:0] Rt,
  input  [5:0] FUNCT,
  input  [31:0] RS,
  input  [31:0] RT_2,
  input  [31:0] istr,
  output [3:0] Alu,
  output [1:0] M2,
  output DmLd,
  output Sha,
  output BrCount,
  output RegWrite,
  output [1:0] M3,
  output [3:0] DmSel,
  output Halt,
  output BCount,
  output [29:0] out_18,
  output [4:0] int_ctrl,
  output Disp,
  output JCount,
  output [1:0] M1,
  output [1:0] M4,
  output DmStr
);

  wire add_t, and_33_out, and_34_out, and_t, cmpu, comparator_3_eq, comparator_4_eq, comparator_5_eq,
       comparator_6_eq, comparator_7_eq, comparator_8_eq, comparator_9_eq, comparator_10_eq,
       comparator_11_eq, comparator_12_eq, comparator_13_eq, comparator_14_eq, comparator_15_eq,
       comparator_17_eq, comparator_18_eq, comparator_19_eq, comparator_20_eq, comparator_21_eq,
       comparator_22_eq, comparator_23_eq, comparator_24_eq, comparator_25_eq, comparator_26_eq,
       comparator_27_eq, comparator_28_eq, comparator_29_eq, comparator_30_eq, comparator_31_eq,
       comparator_34_eq, comparator_35_eq, comparator_37_eq, comparator_38_eq, comparator_39_eq,
       comparator_40_eq, EQUAL, ISR, LESS, NR, or_t, sra_t, srl_t;
  wire [3:0] sel_t;

  Comparator #(.width(32)) comparator_1 (.a(RS), .b({32{1'b0}}), .lt(LESS));  // open: gt, eq
  Comparator #(.width(6)) comparator_2 (.a(OP), .b({6{1'b0}}), .eq(ISR));  // open: gt, lt
  not not_1 (NR, ISR);
  Comparator #(.width(6)) comparator_3 (.a(OP), .b(6'b001000), .eq(comparator_3_eq));  // open: gt, lt
  Comparator #(.width(6)) comparator_4 (.a(OP), .b(6'b001001), .eq(comparator_4_eq));  // open: gt, lt
  Comparator #(.width(6)) comparator_5 (.a(OP), .b(6'b001100), .eq(comparator_5_eq));  // open: gt, lt
  Comparator #(.width(6)) comparator_6 (.a(OP), .b(6'b001101), .eq(comparator_6_eq));  // open: gt, lt
  Comparator #(.width(6)) comparator_7 (.a(OP), .b(6'b100011), .eq(comparator_7_eq));  // open: gt, lt
  Comparator #(.width(6)) comparator_8 (.a(OP), .b(6'b101011), .eq(comparator_8_eq));  // open: gt, lt
  Comparator #(.width(6)) comparator_9 (.a(OP), .b(6'b000100), .eq(comparator_9_eq));  // open: gt, lt
  Comparator #(.width(6)) comparator_10 (.a(OP), .b(6'b000101), .eq(comparator_10_eq));  // open: gt, lt
  Comparator #(.width(6)) comparator_11 (.a(OP), .b(6'b001010), .eq(comparator_11_eq));  // open: gt, lt
  Comparator #(.width(6)) comparator_12 (.a(OP), .b(6'b000010), .eq(comparator_12_eq));  // open: gt, lt
  Comparator #(.width(6)) comparator_13 (.a(OP), .b(6'b000011), .eq(comparator_13_eq));  // open: gt, lt
  Comparator #(.width(6)) comparator_14 (.a(OP), .b(6'b101000), .eq(comparator_14_eq));  // open: gt, lt
  Comparator #(.width(6)) comparator_15 (.a(OP), .b(6'b000001), .eq(comparator_15_eq));  // open: gt, lt
  and and_1 (out_18[0], comparator_3_eq, NR);
  and and_2 (out_18[1], comparator_4_eq, NR);
  and and_3 (out_18[2], comparator_5_eq, NR);
  and and_4 (out_18[3], comparator_6_eq, NR);
  and and_5 (DmLd, comparator_7_eq, NR);
  and and_6 (out_18[5], comparator_8_eq, NR);
  and and_7 (out_18[6], comparator_9_eq, NR);
  and and_8 (out_18[7], comparator_10_eq, NR);
  and and_9 (out_18[8], comparator_11_eq, NR);
  and and_10 (out_18[9], comparator_12_eq, NR);
  and and_11 (M3[1], comparator_13_eq, NR);
  and and_12 (out_18[11], comparator_14_eq, NR);
  and and_13 (out_18[12], comparator_15_eq, NR);
  Comparator #(.width(32)) comparator_16 (.a(RS), .b(RT_2), .eq(EQUAL));  // open: gt, lt
  Comparator #(.width(6)) comparator_17 (.a(FUNCT), .b(6'b100000), .eq(comparator_17_eq));  // open: gt, lt
  Comparator #(.width(6)) comparator_18 (.a(FUNCT), .b(6'b100001), .eq(comparator_18_eq));  // open: gt, lt
  Comparator #(.width(6)) comparator_19 (.a(FUNCT), .b(6'b100100), .eq(comparator_19_eq));  // open: gt, lt
  Comparator #(.width(6)) comparator_20 (.a(FUNCT), .b(6'b100010), .eq(comparator_20_eq));  // open: gt, lt
  Comparator #(.width(6)) comparator_21 (.a(FUNCT), .b(6'b100101), .eq(comparator_21_eq));  // open: gt, lt
  Comparator #(.width(6)) comparator_22 (.a(FUNCT), .b(6'b100111), .eq(comparator_22_eq));  // open: gt, lt
  Comparator #(.width(6)) comparator_23 (.a(FUNCT), .b(6'b101010), .eq(comparator_23_eq));  // open: gt, lt
  Comparator #(.width(6)) comparator_24 (.a(FUNCT), .b(6'b101011), .eq(comparator_24_eq));  // open: gt, lt
  Comparator #(.width(6)) comparator_25 (.a(FUNCT), .b(6'b000110), .eq(comparator_25_eq));  // open: gt, lt
  Comparator #(.width(6)) comparator_26 (.a(FUNCT), .b(6'b000111), .eq(comparator_26_eq));  // open: gt, lt
  Comparator #(.width(6)) comparator_27 (.a(FUNCT), .b({6{1'b0}}), .eq(comparator_27_eq));  // open: gt, lt
  Comparator #(.width(6)) comparator_28 (.a(FUNCT), .b(6'b000011), .eq(comparator_28_eq));  // open: gt, lt
  Comparator #(.width(6)) comparator_29 (.a(FUNCT), .b(6'b000010), .eq(comparator_29_eq));  // open: gt, lt
  Comparator #(.width(6)) comparator_30 (.a(FUNCT), .b(6'b001000), .eq(comparator_30_eq));  // open: gt, lt
  Comparator #(.width(6)) comparator_31 (.a(FUNCT), .b(6'b001100), .eq(comparator_31_eq));  // open: gt, lt
  and and_14 (out_18[13], comparator_17_eq, ISR);
  and and_15 (out_18[14], comparator_18_eq, ISR);
  and and_16 (out_18[15], comparator_19_eq, ISR);
  and and_17 (out_18[16], comparator_20_eq, ISR);
  and and_18 (out_18[17], comparator_21_eq, ISR);
  and and_19 (out_18[18], comparator_22_eq, ISR);
  and and_20 (out_18[19], comparator_23_eq, ISR);
  and and_21 (out_18[20], comparator_24_eq, ISR);
  and and_22 (out_18[21], comparator_25_eq, ISR);
  and and_23 (out_18[22], comparator_26_eq, ISR);
  and and_24 (out_18[23], comparator_27_eq, ISR);
  and and_25 (out_18[24], comparator_28_eq, ISR);
  and and_26 (out_18[25], comparator_29_eq, ISR);
  and and_27 (M4[1], comparator_30_eq, ISR);
  and and_28 (out_18[27], comparator_31_eq, ISR);
  or or_1 (and_t, out_18[15], out_18[2]);
  or or_2 (or_t, out_18[17], out_18[3]);
  or or_3 (sra_t, out_18[24], out_18[22]);
  or or_4 (srl_t, out_18[21], out_18[25]);
  or or_5 (add_t, out_18[13], out_18[0], out_18[1], out_18[14], DmLd, out_18[5], out_18[11]);
  or or_6 (cmpu, out_18[19], out_18[20], out_18[8]);
  nor nor_1 (RegWrite, out_18[5], out_18[6], out_18[7], out_18[9], out_18[29], out_18[27], M4[1], out_18[12], out_18[11]);
  Multiplexer #(.select(2), .width(4)) multiplexer_1 (
    .in0(4'b0001), .in1(4'b0010), .in2(4'b0100), .in3(4'b1000), .out(sel_t), .sel(RS[1:0]));  // open: en
  // Probe on istr[31:21]
  Comparator #(.width(11)) comparator_32 (.a(istr[31:21]), .b(11'h200), .eq(out_18[28]));  // open: gt, lt
  Comparator #(.width(11)) comparator_33 (.a(istr[31:21]), .b(11'h204), .eq(out_18[29]));  // open: gt, lt
  Multiplexer #(.width(4)) multiplexer_2 (.in0(4'b1111), .in1(sel_t), .out(DmSel), .sel(out_18[11]));  // open: en
  or or_7 (M1[1], out_18[5], M3[1], out_18[11]);
  or or_8 (DmStr, out_18[5], out_18[11]);
  or or_9 (M1[0], out_18[17], out_18[13], out_18[14], out_18[15], out_18[23], out_18[24], out_18[25], out_18[16], out_18[18], out_18[5], out_18[19], out_18[20], out_18[21], out_18[22], out_18[11], int_ctrl[0]);
  or or_10 (M2[1], out_18[23], out_18[21], out_18[25], M3[1], out_18[24], out_18[22]);
  or or_11 (M2[0], out_18[22], out_18[1], out_18[2], out_18[0], out_18[3], DmLd, out_18[5], out_18[11], M3[1], out_18[8], out_18[21]);
  Comparator #(.width(5)) comparator_34 (.a(Rd), .b({5{1'b0}}), .eq(comparator_34_eq));  // open: gt, lt
  Comparator #(.width(5)) comparator_35 (.a(Rt), .b({5{1'b0}}), .eq(comparator_35_eq));  // open: gt, lt
  Comparator #(.width(32), .mode("unsigned")) comparator_36 (
    .a(32'h42000018), .b(istr), .eq(int_ctrl[4]));  // open: gt, lt
  and and_29 (int_ctrl[2], comparator_34_eq, out_18[28]);
  and and_30 (int_ctrl[3], comparator_35_eq, out_18[29]);
  or or_12 (JCount, M4[1], M3[1], out_18[9]);
  AluCtrl aluctrl_1 (
    .add(add_t), .sub(out_18[16]), .\and (and_t), .\or (or_t), .sra(sra_t), .srl(srl_t), .sll(out_18[23]),
    .cmpu(cmpu), .\nor (out_18[18]), .A3(Alu[3]), .A2(Alu[2]), .A1(Alu[1]), .A0(Alu[0]));
  Comparator #(.width(5)) comparator_37 (.a(Rd), .b({5{1'b0}}), .eq(comparator_37_eq));  // open: gt, lt
  Comparator #(.width(5)) comparator_38 (.a(Rt), .b({5{1'b0}}), .eq(comparator_38_eq));  // open: gt, lt
  Comparator #(.width(32)) comparator_39 (.a(RS), .b(32'ha), .eq(comparator_39_eq));  // open: gt, lt
  Comparator #(.width(32)) comparator_40 (.a(RS), .b(32'ha), .eq(comparator_40_eq));  // open: gt, lt
  and and_31 (int_ctrl[0], ~comparator_37_eq, out_18[28]);  // AND_Gate
  and and_32 (int_ctrl[1], ~comparator_38_eq, out_18[29]);  // AND_Gate
  and and_33 (and_33_out, EQUAL, out_18[6]);
  or or_13 (BrCount, and_33_out, and_34_out);
  and and_34 (and_34_out, ~EQUAL, out_18[7]);  // AND_Gate
  or or_14 (BCount, out_18[6], out_18[7]);
  or or_15 (Sha, out_18[23], out_18[22], out_18[25], out_18[21], out_18[24]);
  and and_35 (Disp, out_18[27], ~comparator_39_eq);  // AND_Gate
  and and_36 (Halt, out_18[27], comparator_40_eq);

  assign M3[0] = DmLd;
  assign M4[0] = JCount;
  assign {out_18[26], out_18[10], out_18[4]} = {M4[1], M3[1], DmLd};

  // Other names for the same wires on the sheet: efc_t = int_ctrl[0]; etc_t = int_ctrl[1]; STI = int_ctrl[2];
  //   CLI = int_ctrl[3]; eret = int_ctrl[4]; ADDI = out_18[0];
  //   Istr_t[29:0] = {out_18[29:27], M4[1], out_18[25:11], M3[1], out_18[9:5], DmLd, out_18[3:0]}; ADDIU = out_18[1];
  //   ANDI = out_18[2]; ORI = out_18[3]; SW = out_18[5]; BEQ = out_18[6]; BNE = out_18[7]; SLTI = out_18[8];
  //   J = out_18[9]; SB = out_18[11]; BLTZ = out_18[12]; ADD = out_18[13]; ADDU = out_18[14]; AND = out_18[15];
  //   SUB = out_18[16]; OR = out_18[17]; NOR = out_18[18]; SLT = out_18[19]; SLTU = out_18[20]; SRLV = out_18[21];
  //   SRAV = out_18[22]; SLL = out_18[23]; SRA = out_18[24]; SRL = out_18[25]; SYSCAL = out_18[27]; EFC = out_18[28];
  //   ETC = out_18[29]; LD = DmLd; LW = DmLd; M30 = DmLd; JAL = M3[1]; M40 = JCount; JR = M4[1]; RT_t[31:0] = RT_2;
  //   SEL[3:0] = DmSel; STR = DmStr; WE = RegWrite
endmodule

module AluCtrl (
  input  add,
  input  sub,
  input  \and ,
  input  \or ,
  input  sra,
  input  srl,
  input  sll,
  input  cmpu,
  input  \nor ,
  output A3,
  output A2,
  output A1,
  output A0
);

  wire and_2_out, and_3_out, and_4_out, and_5_out, and_6_out, and_7_out, and_8_out, and_9_out, not_1_out,
       not_2_out, not_3_out, not_4_out, not_5_out, not_6_out, not_7_out, not_8_out, not_9_out, not_10_out,
       not_11_out, not_12_out, not_13_out, not_14_out, not_15_out, not_16_out, not_17_out, not_18_out,
       not_19_out, not_20_out, not_21_out, not_22_out, not_23_out, not_24_out, not_25_out, not_26_out,
       not_27_out, not_28_out, not_29_out, not_30_out, not_31_out, not_32_out, not_33_out, not_34_out,
       not_35_out, not_36_out, not_37_out, not_38_out, not_39_out, not_40_out, not_41_out, not_42_out,
       not_43_out, not_44_out, not_45_out, not_46_out, not_47_out, not_48_out, not_49_out, not_50_out,
       not_51_out, not_52_out, not_53_out, not_54_out;

  not not_1 (not_1_out, add);
  not not_2 (not_2_out, sub);
  not not_3 (not_3_out, \and );
  not not_4 (not_4_out, sra);
  not not_5 (not_5_out, srl);
  not not_6 (not_6_out, sll);
  not not_7 (not_7_out, \or );
  not not_8 (not_8_out, sra);
  not not_9 (not_9_out, srl);
  not not_10 (not_10_out, sll);
  not not_11 (not_11_out, cmpu);
  not not_12 (not_12_out, \nor );
  not not_13 (not_13_out, \or );
  not not_14 (not_14_out, sra);
  not not_15 (not_15_out, srl);
  not not_16 (not_16_out, sll);
  not not_17 (not_17_out, \nor );
  not not_18 (not_18_out, \or );
  not not_19 (not_19_out, sra);
  not not_20 (not_20_out, srl);
  not not_21 (not_21_out, sll);
  not not_22 (not_22_out, \nor );
  not not_23 (not_23_out, \or );
  not not_24 (not_24_out, sra);
  not not_25 (not_25_out, srl);
  not not_26 (not_26_out, sll);
  not not_27 (not_27_out, \nor );
  not not_28 (not_28_out, add);
  not not_29 (not_29_out, sub);
  not not_30 (not_30_out, \and );
  not not_31 (not_31_out, \or );
  not not_32 (not_32_out, sra);
  not not_33 (not_33_out, srl);
  not not_34 (not_34_out, sll);
  not not_35 (not_35_out, \nor );
  not not_36 (not_36_out, add);
  not not_37 (not_37_out, \or );
  not not_38 (not_38_out, sra);
  not not_39 (not_39_out, sll);
  not not_40 (not_40_out, cmpu);
  not not_41 (not_41_out, add);
  not not_42 (not_42_out, sub);
  not not_43 (not_43_out, \and );
  not not_44 (not_44_out, \or );
  not not_45 (not_45_out, sra);
  not not_46 (not_46_out, srl);
  not not_47 (not_47_out, sll);
  not not_48 (not_48_out, \nor );
  not not_49 (not_49_out, sub);
  not not_50 (not_50_out, \or );
  not not_51 (not_51_out, srl);
  not not_52 (not_52_out, sll);
  not not_53 (not_53_out, cmpu);
  not not_54 (not_54_out, \nor );
  and and_1 (A3, not_1_out, not_2_out, not_3_out, not_4_out, not_5_out, not_6_out);
  and and_2 (and_2_out, not_7_out, not_8_out, not_9_out, not_10_out, not_11_out, not_12_out);
  and and_3 (and_3_out, \and , not_13_out, not_14_out, not_15_out, not_16_out, not_17_out);
  and and_4 (and_4_out, sub, not_18_out, not_19_out, not_20_out, not_21_out, not_22_out);
  and and_5 (and_5_out, add, not_23_out, not_24_out, not_25_out, not_26_out, not_27_out);
  and and_6 (and_6_out, not_28_out, not_29_out, not_30_out, not_31_out, not_32_out, not_33_out, not_34_out, not_35_out);
  and and_7 (and_7_out, not_36_out, not_37_out, not_38_out, not_39_out, not_40_out);
  and and_8 (and_8_out, not_41_out, not_42_out, not_43_out, not_44_out, not_45_out, not_46_out, not_47_out, not_48_out);
  and and_9 (and_9_out, not_49_out, not_50_out, not_51_out, not_52_out, not_53_out, not_54_out);
  or or_1 (A2, and_2_out, and_3_out, and_4_out, and_5_out);
  or or_2 (A1, and_6_out, and_7_out);
  or or_3 (A0, and_8_out, and_9_out);
endmodule

module InstCounter (
  input  CLK,
  input  Halt,
  input  CLR,
  input  EQUAL,
  input  LESS,
  input  [29:0] IstrIn,
  output [15:0] J,
  output [15:0] B,
  output [15:0] Br,
  output [15:0] All
);

  wire and_1_out, and_2_out, and_3_out, BC, BrC, JC;
  wire [15:0] adder_1_out, adder_2_out, adder_3_out, adder_4_out, multiplexer_1_out, multiplexer_2_out,
       multiplexer_3_out;

  Register #(.width(16)) register_1 (.D(adder_1_out), .en(Halt), .Q(All), .clk(CLK), .clr(CLR));
  Register #(.width(16)) register_2 (.D(adder_2_out), .en(Halt), .Q(J), .clk(CLK), .clr(CLR));
  Register #(.width(16)) register_3 (.D(adder_3_out), .en(Halt), .Q(B), .clk(CLK), .clr(CLR));
  Register #(.width(16)) register_4 (.D(adder_4_out), .en(Halt), .Q(Br), .clk(CLK), .clr(CLR));
  Adder #(.width(16)) adder_1 (.a(All), .b(16'h1), .out(adder_1_out));  // open: cin, cout
  Adder #(.width(16)) adder_2 (.a(J), .b(multiplexer_1_out), .out(adder_2_out));  // open: cin, cout
  Multiplexer #(.width(16)) multiplexer_1 (
    .in0({16{1'b0}}), .in1(16'h1), .out(multiplexer_1_out), .sel(JC));  // open: en
  Adder #(.width(16)) adder_3 (.a(B), .b(multiplexer_2_out), .out(adder_3_out));  // open: cin, cout
  Multiplexer #(.width(16)) multiplexer_2 (
    .in0({16{1'b0}}), .in1(16'h1), .out(multiplexer_2_out), .sel(BC));  // open: en
  Adder #(.width(16)) adder_4 (.a(Br), .b(multiplexer_3_out), .out(adder_4_out));  // open: cin, cout
  Multiplexer #(.width(16)) multiplexer_3 (
    .in0({16{1'b0}}), .in1(16'h1), .out(multiplexer_3_out), .sel(BrC));  // open: en
  and and_1 (and_1_out, EQUAL, IstrIn[6]);
  and and_2 (and_2_out, ~EQUAL, IstrIn[7]);  // AND_Gate
  and and_3 (and_3_out, IstrIn[12], LESS);
  or or_1 (BrC, and_1_out, and_2_out, and_3_out);
  or or_2 (BC, IstrIn[6], IstrIn[7], IstrIn[12]);
  or or_3 (JC, IstrIn[26], IstrIn[10], IstrIn[9]);

  // Other names for the same wires on the sheet: ADDI = IstrIn[0]; Istr[29:0] = IstrIn; ADDIU = IstrIn[1];
  //   ANDI = IstrIn[2]; ORI = IstrIn[3]; LW = IstrIn[4]; SW = IstrIn[5]; BEQ = IstrIn[6]; BNE = IstrIn[7];
  //   SLTI = IstrIn[8]; JI = IstrIn[9]; JAL = IstrIn[10]; SB = IstrIn[11]; BLTZ = IstrIn[12]; ADD = IstrIn[13];
  //   ADDU = IstrIn[14]; AND = IstrIn[15]; SUB = IstrIn[16]; OR = IstrIn[17]; NOR = IstrIn[18]; SLT = IstrIn[19];
  //   SLTU = IstrIn[20]; SRLV = IstrIn[21]; SRAV = IstrIn[22]; SLL = IstrIn[23]; SRA = IstrIn[24]; SRL = IstrIn[25];
  //   JR = IstrIn[26]; SYSCAL = IstrIn[27]
endmodule

module lock (
  input  en,
  input  pauseIn,
  input  Clk,
  input  rst,
  input  cont,
  output En_2,
  output pause
);

  wire or_1_out, register_1_q, register_2_q;

  not not_1 (En_2, register_1_q);
  Register #(.width(1)) register_1 (.D(en), .en(En_2), .Q(register_1_q), .clk(Clk), .clr(rst));
  or or_1 (or_1_out, rst, cont);
  Register #(.width(1)) register_2 (.D(pauseIn), .en(pause), .Q(register_2_q), .clk(Clk), .clr(or_1_out));
  not not_2 (pause, register_2_q);
endmodule

module IF_ID (
  input  [31:0] PcIn,
  input  [31:0] InstrIn,
  input  \传输状态In ,
  input  CLK,
  input  \同步清零 ,
  input  \异步清零 ,
  output [31:0] PcOut,
  output [31:0] InstrOut,
  output \传输状态Out 
);

  wire multiplexer_3_out;
  wire [31:0] multiplexer_1_out, multiplexer_2_out;

  Multiplexer #(.width(32), .enable("false")) multiplexer_1 (
    .in0(PcIn), .in1({32{1'b0}}), .out(multiplexer_1_out), .sel(\同步清零 ));
  Multiplexer #(.width(32), .enable("false")) multiplexer_2 (
    .in0(InstrIn), .in1({32{1'b0}}), .out(multiplexer_2_out), .sel(\同步清零 ));
  Multiplexer #(.enable("false")) multiplexer_3 (.in0(\传输状态In ), .in1(1'b0), .out(multiplexer_3_out), .sel(\同步清零 ));
  Register #(.width(32)) register_1 (.D(multiplexer_1_out), .en(\传输状态In ), .Q(PcOut), .clk(CLK), .clr(\异步清零 ));
  Register #(.width(32)) register_2 (.D(multiplexer_2_out), .en(\传输状态In ), .Q(InstrOut), .clk(CLK), .clr(\异步清零 ));
  Register #(.width(1)) register_3 (.D(multiplexer_3_out), .en(\传输状态In ), .Q(\传输状态Out ), .clk(CLK), .clr(\异步清零 ));
endmodule

module ID_EX (
  input  [29:0] IstrIn,
  input  [4:0] _5bIn4,
  input  [4:0] _5bIn1,
  input  efcIn,
  input  [4:0] _5bIn2,
  input  haltIn,
  input  [4:0] _5bIn3,
  input  [3:0] AluIn,
  input  [31:0] R1In,
  input  [3:0] DmSelIn,
  input  shaIn,
  input  [31:0] R2In,
  input  DmLdIn,
  input  [31:0] _32bIn1,
  input  DmStrIn,
  input  RegWriteIn,
  input  [31:0] _32bIn2,
  input  [1:0] M4In,
  input  [1:0] M3In,
  input  [31:0] _32bIn3,
  input  [1:0] M2In,
  input  [31:0] _32bIn4,
  input  [1:0] M1In,
  input  \传输状态In ,
  input  DispIn,
  input  CLK,
  input  \同步清零 ,
  input  \异步清零 ,
  output [29:0] IstrOut,
  output [4:0] _5bOut4,
  output [4:0] _5bOut1,
  output efcOut,
  output [4:0] _5bOut2,
  output haltOut,
  output [4:0] _5bOut3,
  output [3:0] AluOut,
  output [31:0] R1Out,
  output [3:0] DmSelOut,
  output shaOut,
  output [31:0] R2Out,
  output DmLdOut,
  output [31:0] _32bOut1,
  output DmStrOut,
  output RegWriteOut,
  output [31:0] _32bOut2,
  output [1:0] M4Out,
  output [1:0] M3Out,
  output [31:0] _32bOut3,
  output [1:0] M2Out,
  output [31:0] _32bOut4,
  output [1:0] M1Out,
  output \传输状态Out ,
  output DispOut
);

  wire multiplexer_11_out, multiplexer_13_out, multiplexer_14_out, multiplexer_17_out, multiplexer_18_out,
       multiplexer_19_out, multiplexer_20_out, multiplexer_25_out;
  wire [1:0] multiplexer_21_out, multiplexer_22_out, multiplexer_23_out, multiplexer_24_out;
  wire [3:0] multiplexer_15_out, multiplexer_16_out;
  wire [4:0] multiplexer_2_out, multiplexer_3_out, multiplexer_4_out, multiplexer_12_out;
  wire [29:0] multiplexer_1_out;
  wire [31:0] multiplexer_5_out, multiplexer_6_out, multiplexer_7_out, multiplexer_8_out, multiplexer_9_out,
       multiplexer_10_out;

  Multiplexer #(.width(30), .enable("false")) multiplexer_1 (
    .in0(IstrIn), .in1({30{1'b0}}), .out(multiplexer_1_out), .sel(\同步清零 ));
  Multiplexer #(.width(5), .enable("false")) multiplexer_2 (
    .in0(_5bIn1), .in1({5{1'b0}}), .out(multiplexer_2_out), .sel(\同步清零 ));
  Multiplexer #(.width(5), .enable("false")) multiplexer_3 (
    .in0(_5bIn2), .in1({5{1'b0}}), .out(multiplexer_3_out), .sel(\同步清零 ));
  Multiplexer #(.width(5), .enable("false")) multiplexer_4 (
    .in0(_5bIn3), .in1({5{1'b0}}), .out(multiplexer_4_out), .sel(\同步清零 ));
  Multiplexer #(.width(32), .enable("false")) multiplexer_5 (
    .in0(R1In), .in1({32{1'b0}}), .out(multiplexer_5_out), .sel(\同步清零 ));
  Multiplexer #(.width(32), .enable("false")) multiplexer_6 (
    .in0(R2In), .in1({32{1'b0}}), .out(multiplexer_6_out), .sel(\同步清零 ));
  Multiplexer #(.width(32), .enable("false")) multiplexer_7 (
    .in0(_32bIn1), .in1({32{1'b0}}), .out(multiplexer_7_out), .sel(\同步清零 ));
  Multiplexer #(.width(32), .enable("false")) multiplexer_8 (
    .in0(_32bIn2), .in1({32{1'b0}}), .out(multiplexer_8_out), .sel(\同步清零 ));
  Multiplexer #(.width(32), .enable("false")) multiplexer_9 (
    .in0(_32bIn3), .in1({32{1'b0}}), .out(multiplexer_9_out), .sel(\同步清零 ));
  Multiplexer #(.width(32), .enable("false")) multiplexer_10 (
    .in0(_32bIn4), .in1({32{1'b0}}), .out(multiplexer_10_out), .sel(\同步清零 ));
  Multiplexer #(.enable("false")) multiplexer_11 (.in0(\传输状态In ), .in1(1'b0), .out(multiplexer_11_out), .sel(\同步清零 ));
  Register #(.width(30)) register_1 (.D(multiplexer_1_out), .en(\传输状态In ), .Q(IstrOut), .clk(CLK), .clr(\异步清零 ));
  Register #(.width(5)) register_2 (.D(multiplexer_2_out), .en(\传输状态In ), .Q(_5bOut1), .clk(CLK), .clr(\异步清零 ));
  Register #(.width(5)) register_3 (.D(multiplexer_3_out), .en(\传输状态In ), .Q(_5bOut2), .clk(CLK), .clr(\异步清零 ));
  Register #(.width(5)) register_4 (.D(multiplexer_4_out), .en(\传输状态In ), .Q(_5bOut3), .clk(CLK), .clr(\异步清零 ));
  Register #(.width(32)) register_5 (.D(multiplexer_5_out), .en(\传输状态In ), .Q(R1Out), .clk(CLK), .clr(\异步清零 ));
  Register #(.width(32)) register_6 (.D(multiplexer_6_out), .en(\传输状态In ), .Q(R2Out), .clk(CLK), .clr(\异步清零 ));
  Register #(.width(32)) register_7 (.D(multiplexer_7_out), .en(\传输状态In ), .Q(_32bOut1), .clk(CLK), .clr(\异步清零 ));
  Register #(.width(32)) register_8 (.D(multiplexer_8_out), .en(\传输状态In ), .Q(_32bOut2), .clk(CLK), .clr(\异步清零 ));
  Register #(.width(32)) register_9 (.D(multiplexer_9_out), .en(\传输状态In ), .Q(_32bOut3), .clk(CLK), .clr(\异步清零 ));
  Register #(.width(32)) register_10 (.D(multiplexer_10_out), .en(\传输状态In ), .Q(_32bOut4), .clk(CLK), .clr(\异步清零 ));
  Register #(.width(1)) register_11 (.D(multiplexer_11_out), .en(\传输状态In ), .Q(\传输状态Out ), .clk(CLK), .clr(\异步清零 ));
  Multiplexer #(.width(5), .enable("false")) multiplexer_12 (
    .in0(_5bIn4), .in1({5{1'b0}}), .out(multiplexer_12_out), .sel(\同步清零 ));
  Multiplexer #(.enable("false")) multiplexer_13 (.in0(efcIn), .in1(1'b0), .out(multiplexer_13_out), .sel(\同步清零 ));
  Multiplexer #(.enable("false")) multiplexer_14 (.in0(haltIn), .in1(1'b0), .out(multiplexer_14_out), .sel(\同步清零 ));
  Multiplexer #(.width(4), .enable("false")) multiplexer_15 (
    .in0(AluIn), .in1(4'b0000), .out(multiplexer_15_out), .sel(\同步清零 ));
  Multiplexer #(.width(4), .enable("false")) multiplexer_16 (
    .in0(DmSelIn), .in1(4'b0000), .out(multiplexer_16_out), .sel(\同步清零 ));
  Multiplexer #(.enable("false")) multiplexer_17 (.in0(shaIn), .in1(1'b0), .out(multiplexer_17_out), .sel(\同步清零 ));
  Multiplexer #(.enable("false")) multiplexer_18 (.in0(DmLdIn), .in1(1'b0), .out(multiplexer_18_out), .sel(\同步清零 ));
  Multiplexer #(.enable("false")) multiplexer_19 (.in0(DmStrIn), .in1(1'b0), .out(multiplexer_19_out), .sel(\同步清零 ));
  Multiplexer #(.enable("false")) multiplexer_20 (.in0(RegWriteIn), .in1(1'b0), .out(multiplexer_20_out), .sel(\同步清零 ));
  Multiplexer #(.width(2), .enable("false")) multiplexer_21 (
    .in0(M4In), .in1(2'b00), .out(multiplexer_21_out), .sel(\同步清零 ));
  Multiplexer #(.width(2), .enable("false")) multiplexer_22 (
    .in0(M3In), .in1(2'b00), .out(multiplexer_22_out), .sel(\同步清零 ));
  Multiplexer #(.width(2), .enable("false")) multiplexer_23 (
    .in0(M2In), .in1(2'b00), .out(multiplexer_23_out), .sel(\同步清零 ));
  Multiplexer #(.width(2), .enable("false")) multiplexer_24 (
    .in0(M1In), .in1(2'b00), .out(multiplexer_24_out), .sel(\同步清零 ));
  Multiplexer #(.enable("false")) multiplexer_25 (.in0(DispIn), .in1(1'b0), .out(multiplexer_25_out), .sel(\同步清零 ));
  Register #(.width(5)) register_12 (.D(multiplexer_12_out), .en(\传输状态In ), .Q(_5bOut4), .clk(CLK), .clr(\异步清零 ));
  Register #(.width(1)) register_13 (.D(multiplexer_13_out), .en(\传输状态In ), .Q(efcOut), .clk(CLK), .clr(\异步清零 ));
  Register #(.width(1)) register_14 (.D(multiplexer_14_out), .en(\传输状态In ), .Q(haltOut), .clk(CLK), .clr(\异步清零 ));
  Register #(.width(4)) register_15 (.D(multiplexer_15_out), .en(\传输状态In ), .Q(AluOut), .clk(CLK), .clr(\异步清零 ));
  Register #(.width(4)) register_16 (.D(multiplexer_16_out), .en(\传输状态In ), .Q(DmSelOut), .clk(CLK), .clr(\异步清零 ));
  Register #(.width(1)) register_17 (.D(multiplexer_17_out), .en(\传输状态In ), .Q(shaOut), .clk(CLK), .clr(\异步清零 ));
  Register #(.width(1)) register_18 (.D(multiplexer_18_out), .en(\传输状态In ), .Q(DmLdOut), .clk(CLK), .clr(\异步清零 ));
  Register #(.width(1)) register_19 (.D(multiplexer_19_out), .en(\传输状态In ), .Q(DmStrOut), .clk(CLK), .clr(\异步清零 ));
  Register #(.width(1)) register_20 (.D(multiplexer_20_out), .en(\传输状态In ), .Q(RegWriteOut), .clk(CLK), .clr(\异步清零 ));
  Register #(.width(2)) register_21 (.D(multiplexer_21_out), .en(\传输状态In ), .Q(M4Out), .clk(CLK), .clr(\异步清零 ));
  Register #(.width(2)) register_22 (.D(multiplexer_22_out), .en(\传输状态In ), .Q(M3Out), .clk(CLK), .clr(\异步清零 ));
  Register #(.width(2)) register_23 (.D(multiplexer_23_out), .en(\传输状态In ), .Q(M2Out), .clk(CLK), .clr(\异步清零 ));
  Register #(.width(2)) register_24 (.D(multiplexer_24_out), .en(\传输状态In ), .Q(M1Out), .clk(CLK), .clr(\异步清零 ));
  Register #(.width(1)) register_25 (.D(multiplexer_25_out), .en(\传输状态In ), .Q(DispOut), .clk(CLK), .clr(\异步清零 ));
endmodule

module EX_MEM (
  input  [29:0] IstrIn,
  input  [4:0] _5bIn4,
  input  [31:0] _32bIn4,
  input  efcIn,
  input  _1bIn1,
  input  _1bIn2,
  input  pauseIn,
  input  [31:0] _32bIn1,
  input  haltIn,
  input  [3:0] DmSelIn,
  input  [31:0] _32bIn2,
  input  DmLdIn,
  input  DmStrIn,
  input  [31:0] _32bIn3,
  input  RegWriteIn,
  input  [4:0] _5bIn1,
  input  [1:0] M3In,
  input  \传输状态In ,
  input  DispIn,
  input  CLK,
  input  \同步清零 ,
  input  \异步清零 ,
  output [29:0] IstrOut,
  output [4:0] _5bOut4,
  output [31:0] _32bOut4,
  output efcOut,
  output _1bOut1,
  output _1bOut2,
  output pauseOut,
  output [31:0] _32bOut1,
  output haltOut,
  output [3:0] DmSelOut,
  output [31:0] _32bOut2,
  output DmLdOut,
  output DmStrOut,
  output [31:0] _32bOut3,
  output RegWriteOut,
  output [4:0] _5bOut1,
  output [1:0] M3Out,
  output \传输状态Out ,
  output DispOut
);

  wire multiplexer_3_out, multiplexer_4_out, multiplexer_9_out, multiplexer_11_out, multiplexer_12_out,
       multiplexer_13_out, multiplexer_15_out, multiplexer_16_out, multiplexer_17_out, multiplexer_19_out;
  wire [1:0] multiplexer_18_out;
  wire [3:0] multiplexer_14_out;
  wire [4:0] multiplexer_8_out, multiplexer_10_out;
  wire [29:0] multiplexer_1_out;
  wire [31:0] multiplexer_2_out, multiplexer_5_out, multiplexer_6_out, multiplexer_7_out;

  Multiplexer #(.width(30), .enable("false")) multiplexer_1 (
    .in0(IstrIn), .in1({30{1'b0}}), .out(multiplexer_1_out), .sel(\同步清零 ));
  Multiplexer #(.width(32), .enable("false")) multiplexer_2 (
    .in0(_32bIn4), .in1({32{1'b0}}), .out(multiplexer_2_out), .sel(\同步清零 ));
  Multiplexer #(.enable("false")) multiplexer_3 (.in0(_1bIn1), .in1(1'b0), .out(multiplexer_3_out), .sel(\同步清零 ));
  Multiplexer #(.enable("false")) multiplexer_4 (.in0(_1bIn2), .in1(1'b0), .out(multiplexer_4_out), .sel(\同步清零 ));
  Multiplexer #(.width(32), .enable("false")) multiplexer_5 (
    .in0(_32bIn1), .in1({32{1'b0}}), .out(multiplexer_5_out), .sel(\同步清零 ));
  Multiplexer #(.width(32), .enable("false")) multiplexer_6 (
    .in0(_32bIn2), .in1({32{1'b0}}), .out(multiplexer_6_out), .sel(\同步清零 ));
  Multiplexer #(.width(32), .enable("false")) multiplexer_7 (
    .in0(_32bIn3), .in1({32{1'b0}}), .out(multiplexer_7_out), .sel(\同步清零 ));
  Multiplexer #(.width(5), .enable("false")) multiplexer_8 (
    .in0(_5bIn1), .in1({5{1'b0}}), .out(multiplexer_8_out), .sel(\同步清零 ));
  Multiplexer #(.enable("false")) multiplexer_9 (.in0(\传输状态In ), .in1(1'b0), .out(multiplexer_9_out), .sel(\同步清零 ));
  Register #(.width(30)) register_1 (.D(multiplexer_1_out), .en(\传输状态In ), .Q(IstrOut), .clk(CLK), .clr(\异步清零 ));
  Register #(.width(32)) register_2 (.D(multiplexer_2_out), .en(\传输状态In ), .Q(_32bOut4), .clk(CLK), .clr(\异步清零 ));
  Register #(.width(1)) register_3 (.D(multiplexer_3_out), .en(\传输状态In ), .Q(_1bOut1), .clk(CLK), .clr(\异步清零 ));
  Register #(.width(1)) register_4 (.D(multiplexer_4_out), .en(\传输状态In ), .Q(_1bOut2), .clk(CLK), .clr(\异步清零 ));
  Register #(.width(32)) register_5 (.D(multiplexer_5_out), .en(\传输状态In ), .Q(_32bOut1), .clk(CLK), .clr(\异步清零 ));
  Register #(.width(32)) register_6 (.D(multiplexer_6_out), .en(\传输状态In ), .Q(_32bOut2), .clk(CLK), .clr(\异步清零 ));
  Register #(.width(32)) register_7 (.D(multiplexer_7_out), .en(\传输状态In ), .Q(_32bOut3), .clk(CLK), .clr(\异步清零 ));
  Register #(.width(5)) register_8 (.D(multiplexer_8_out), .en(\传输状态In ), .Q(_5bOut1), .clk(CLK), .clr(\异步清零 ));
  Register #(.width(1)) register_9 (.D(multiplexer_9_out), .en(\传输状态In ), .Q(\传输状态Out ), .clk(CLK), .clr(\异步清零 ));
  Multiplexer #(.width(5), .enable("false")) multiplexer_10 (
    .in0(_5bIn4), .in1({5{1'b0}}), .out(multiplexer_10_out), .sel(\同步清零 ));
  Multiplexer #(.enable("false")) multiplexer_11 (.in0(efcIn), .in1(1'b0), .out(multiplexer_11_out), .sel(\同步清零 ));
  Multiplexer #(.enable("false")) multiplexer_12 (.in0(pauseIn), .in1(1'b0), .out(multiplexer_12_out), .sel(\同步清零 ));
  Multiplexer #(.enable("false")) multiplexer_13 (.in0(haltIn), .in1(1'b0), .out(multiplexer_13_out), .sel(\同步清零 ));
  Multiplexer #(.width(4), .enable("false")) multiplexer_14 (
    .in0(DmSelIn), .in1(4'b0000), .out(multiplexer_14_out), .sel(\同步清零 ));
  Multiplexer #(.enable("false")) multiplexer_15 (.in0(DmLdIn), .in1(1'b0), .out(multiplexer_15_out), .sel(\同步清零 ));
  Multiplexer #(.enable("false")) multiplexer_16 (.in0(DmStrIn), .in1(1'b0), .out(multiplexer_16_out), .sel(\同步清零 ));
  Multiplexer #(.enable("false")) multiplexer_17 (.in0(RegWriteIn), .in1(1'b0), .out(multiplexer_17_out), .sel(\同步清零 ));
  Multiplexer #(.width(2), .enable("false")) multiplexer_18 (
    .in0(M3In), .in1(2'b00), .out(multiplexer_18_out), .sel(\同步清零 ));
  Multiplexer #(.enable("false")) multiplexer_19 (.in0(DispIn), .in1(1'b0), .out(multiplexer_19_out), .sel(\同步清零 ));
  Register #(.width(5)) register_10 (.D(multiplexer_10_out), .en(\传输状态In ), .Q(_5bOut4), .clk(CLK), .clr(\异步清零 ));
  Register #(.width(1)) register_11 (.D(multiplexer_11_out), .en(\传输状态In ), .Q(efcOut), .clk(CLK), .clr(\异步清零 ));
  Register #(.width(1)) register_12 (.D(multiplexer_12_out), .en(\传输状态In ), .Q(pauseOut), .clk(CLK), .clr(\异步清零 ));
  Register #(.width(1)) register_13 (.D(multiplexer_13_out), .en(\传输状态In ), .Q(haltOut), .clk(CLK), .clr(\异步清零 ));
  Register #(.width(4)) register_14 (.D(multiplexer_14_out), .en(\传输状态In ), .Q(DmSelOut), .clk(CLK), .clr(\异步清零 ));
  Register #(.width(1)) register_15 (.D(multiplexer_15_out), .en(\传输状态In ), .Q(DmLdOut), .clk(CLK), .clr(\异步清零 ));
  Register #(.width(1)) register_16 (.D(multiplexer_16_out), .en(\传输状态In ), .Q(DmStrOut), .clk(CLK), .clr(\异步清零 ));
  Register #(.width(1)) register_17 (.D(multiplexer_17_out), .en(\传输状态In ), .Q(RegWriteOut), .clk(CLK), .clr(\异步清零 ));
  Register #(.width(2)) register_18 (.D(multiplexer_18_out), .en(\传输状态In ), .Q(M3Out), .clk(CLK), .clr(\异步清零 ));
  Register #(.width(1)) register_19 (.D(multiplexer_19_out), .en(\传输状态In ), .Q(DispOut), .clk(CLK), .clr(\异步清零 ));
endmodule

module MEM_WB (
  input  [31:0] _32bIn4,
  input  [29:0] IstrIn,
  input  [31:0] _32bIn3,
  input  [4:0] _5bIn4,
  input  _1bIn1,
  input  efcIn,
  input  [31:0] _32bIn1,
  input  pauseIn,
  input  [31:0] _32bIn2,
  input  [4:0] _5bIn1,
  input  haltIn,
  input  \传输状态In ,
  input  [1:0] M3In,
  input  CLK,
  input  \同步清零 ,
  input  \异步清零 ,
  output [31:0] _32bOut4,
  output [29:0] IstrOut,
  output [31:0] _32bOut3,
  output [4:0] _5bOut4,
  output _1bOut1,
  output efcOut,
  output [31:0] _32bOut1,
  output pauseOut,
  output [31:0] _32bOut2,
  output [4:0] _5bOut1,
  output haltOut,
  output \传输状态Out ,
  output [1:0] M3Out
);

  wire multiplexer_4_out, multiplexer_8_out, multiplexer_10_out, multiplexer_11_out, multiplexer_12_out;
  wire [1:0] multiplexer_13_out;
  wire [4:0] multiplexer_7_out, multiplexer_9_out;
  wire [29:0] multiplexer_2_out;
  wire [31:0] multiplexer_1_out, multiplexer_3_out, multiplexer_5_out, multiplexer_6_out;

  Multiplexer #(.width(32), .enable("false")) multiplexer_1 (
    .in0(_32bIn4), .in1({32{1'b0}}), .out(multiplexer_1_out), .sel(\同步清零 ));
  Multiplexer #(.width(30), .enable("false")) multiplexer_2 (
    .in0(IstrIn), .in1({30{1'b0}}), .out(multiplexer_2_out), .sel(\同步清零 ));
  Multiplexer #(.width(32), .enable("false")) multiplexer_3 (
    .in0(_32bIn3), .in1({32{1'b0}}), .out(multiplexer_3_out), .sel(\同步清零 ));
  Multiplexer #(.enable("false")) multiplexer_4 (.in0(_1bIn1), .in1(1'b0), .out(multiplexer_4_out), .sel(\同步清零 ));
  Multiplexer #(.width(32), .enable("false")) multiplexer_5 (
    .in0(_32bIn1), .in1({32{1'b0}}), .out(multiplexer_5_out), .sel(\同步清零 ));
  Multiplexer #(.width(32), .enable("false")) multiplexer_6 (
    .in0(_32bIn2), .in1({32{1'b0}}), .out(multiplexer_6_out), .sel(\同步清零 ));
  Multiplexer #(.width(5), .enable("false")) multiplexer_7 (
    .in0(_5bIn1), .in1({5{1'b0}}), .out(multiplexer_7_out), .sel(\同步清零 ));
  Multiplexer #(.enable("false")) multiplexer_8 (.in0(\传输状态In ), .in1(1'b0), .out(multiplexer_8_out), .sel(\同步清零 ));
  Register #(.width(32)) register_1 (.D(multiplexer_1_out), .en(\传输状态In ), .Q(_32bOut4), .clk(CLK), .clr(\异步清零 ));
  Register #(.width(30)) register_2 (.D(multiplexer_2_out), .en(\传输状态In ), .Q(IstrOut), .clk(CLK), .clr(\异步清零 ));
  Register #(.width(32)) register_3 (.D(multiplexer_3_out), .en(\传输状态In ), .Q(_32bOut3), .clk(CLK), .clr(\异步清零 ));
  Register #(.width(1)) register_4 (.D(multiplexer_4_out), .en(\传输状态In ), .Q(_1bOut1), .clk(CLK), .clr(\异步清零 ));
  Register #(.width(32)) register_5 (.D(multiplexer_5_out), .en(\传输状态In ), .Q(_32bOut1), .clk(CLK), .clr(\异步清零 ));
  Register #(.width(32)) register_6 (.D(multiplexer_6_out), .en(\传输状态In ), .Q(_32bOut2), .clk(CLK), .clr(\异步清零 ));
  Register #(.width(5)) register_7 (.D(multiplexer_7_out), .en(\传输状态In ), .Q(_5bOut1), .clk(CLK), .clr(\异步清零 ));
  Register #(.width(1)) register_8 (.D(multiplexer_8_out), .en(\传输状态In ), .Q(\传输状态Out ), .clk(CLK), .clr(\异步清零 ));
  Multiplexer #(.width(5), .enable("false")) multiplexer_9 (
    .in0(_5bIn4), .in1({5{1'b0}}), .out(multiplexer_9_out), .sel(\同步清零 ));
  Multiplexer #(.enable("false")) multiplexer_10 (.in0(efcIn), .in1(1'b0), .out(multiplexer_10_out), .sel(\同步清零 ));
  Multiplexer #(.enable("false")) multiplexer_11 (.in0(pauseIn), .in1(1'b0), .out(multiplexer_11_out), .sel(\同步清零 ));
  Multiplexer #(.enable("false")) multiplexer_12 (.in0(haltIn), .in1(1'b0), .out(multiplexer_12_out), .sel(\同步清零 ));
  Multiplexer #(.width(2), .enable("false")) multiplexer_13 (
    .in0(M3In), .in1(2'b00), .out(multiplexer_13_out), .sel(\同步清零 ));
  Register #(.width(5)) register_9 (.D(multiplexer_9_out), .en(\传输状态In ), .Q(_5bOut4), .clk(CLK), .clr(\异步清零 ));
  Register #(.width(1)) register_10 (.D(multiplexer_10_out), .en(\传输状态In ), .Q(efcOut), .clk(CLK), .clr(\异步清零 ));
  Register #(.width(1)) register_11 (.D(multiplexer_11_out), .en(\传输状态In ), .Q(pauseOut), .clk(CLK), .clr(\异步清零 ));
  Register #(.width(1)) register_12 (.D(multiplexer_12_out), .en(\传输状态In ), .Q(haltOut), .clk(CLK), .clr(\异步清零 ));
  Register #(.width(2)) register_13 (.D(multiplexer_13_out), .en(\传输状态In ), .Q(M3Out), .clk(CLK), .clr(\异步清零 ));
endmodule

// CfltCtrl
module ConflitCtrl (
  input  [4:0] RS,
  input  [4:0] RD_EX,
  input  [4:0] RD_MEM,
  input  [4:0] RT,
  input  [29:0] Istr1,
  input  [29:0] Istr2,
  input  [29:0] Istr,
  input  [4:0] RD_ID,
  output IF_ID_STOP,
  output ID_EX_CLEAR
);

  wire _RD1, _RD2, _RS, _RT, and_7_out, and_8_out, and_9_out, and_10_out, and_11_out, and_12_out, and_13_out,
       and_14_out, and_15_out, and_16_out, and_17_out, and_18_out, and_19_out, comparator_5_eq,
       comparator_6_eq, comparator_7_eq, comparator_8_eq, nor_1_out, nor_2_out, or_6_out, or_7_out, RD_RS1,
       RD_RS2, RD_RT1, RD_RT2, RDEX_IS0, RDMEM_IS0, RS_IS0, RS_RT, RT_IS0, WriteReg1, WriteReg2;

  Comparator #(.width(5)) comparator_1 (.a({5{1'b0}}), .b(RS), .eq(RS_IS0));  // open: gt, lt
  Comparator #(.width(5)) comparator_2 (.a({5{1'b0}}), .b(RT), .eq(RT_IS0));  // open: gt, lt
  Comparator #(.width(5)) comparator_3 (.a({5{1'b0}}), .b(RD_EX), .eq(RDEX_IS0));  // open: gt, lt
  Comparator #(.width(5)) comparator_4 (.a({5{1'b0}}), .b(RD_MEM), .eq(RDMEM_IS0));  // open: gt, lt
  or or_1 (RS_RT, Istr[5], Istr[13], Istr[14], Istr[15], Istr[16], Istr[17], Istr[18], Istr[27], Istr[7], Istr[6], Istr[20], Istr[19], Istr[22], Istr[21], Istr[4]);
  or or_2 (_RS, Istr[0], Istr[1], Istr[2], Istr[3], Istr[10], Istr[26], Istr[8], Istr[12]);
  or or_3 (_RT, Istr[23], Istr[11], Istr[29], Istr[25], Istr[24]);
  or or_4 (_RD2, Istr2[0], Istr2[2], Istr2[4], Istr2[1], Istr2[8], Istr2[3], Istr2[10], Istr2[13], Istr2[14], Istr2[15], Istr2[28], Istr2[17], Istr2[16], Istr2[19], Istr2[18], Istr2[21], Istr2[20], Istr2[23], Istr2[22], Istr2[25], Istr2[24]);
  Comparator #(.width(5)) comparator_5 (.a(RD_EX), .b(RS), .eq(comparator_5_eq));  // open: gt, lt
  Comparator #(.width(5)) comparator_6 (.a(RD_EX), .b(RT), .eq(comparator_6_eq));  // open: gt, lt
  Comparator #(.width(5)) comparator_7 (.a(RD_MEM), .b(RS), .eq(comparator_7_eq));  // open: gt, lt
  Comparator #(.width(5)) comparator_8 (.a(RD_MEM), .b(RT), .eq(comparator_8_eq));  // open: gt, lt
  and and_1 (WriteReg1, _RD1, ~RDEX_IS0);  // AND_Gate
  and and_2 (WriteReg2, _RD2, ~RDMEM_IS0);  // AND_Gate
  or or_5 (_RD1, Istr1[0], Istr1[2], Istr1[4], Istr1[1], Istr1[8], Istr1[3], Istr1[10], Istr1[13], Istr1[14], Istr1[15], Istr1[28], Istr1[17], Istr1[16], Istr1[19], Istr1[18], Istr1[21], Istr1[20], Istr1[23], Istr1[22], Istr1[25], Istr1[24]);
  and and_3 (RD_RS1, ~RS_IS0, comparator_5_eq);  // AND_Gate
  and and_4 (RD_RT1, ~RT_IS0, comparator_6_eq);  // AND_Gate
  and and_5 (RD_RS2, ~RS_IS0, comparator_7_eq);  // AND_Gate
  and and_6 (RD_RT2, ~RT_IS0, comparator_8_eq);  // AND_Gate
  or or_6 (or_6_out, RD_RS1, RD_RT1);
  and and_7 (and_7_out, RS_RT, WriteReg1);
  and and_8 (and_8_out, _RT, WriteReg1);
  and and_9 (and_9_out, _RS, WriteReg1);
  or or_7 (or_7_out, RD_RS2, RD_RT2);
  and and_10 (and_10_out, RS_RT, WriteReg2);
  and and_11 (and_11_out, _RT, WriteReg2);
  and and_12 (and_12_out, _RS, WriteReg2);
  and and_13 (and_13_out, or_6_out, and_7_out);
  and and_14 (and_14_out, RD_RT1, and_8_out);
  and and_15 (and_15_out, RD_RS1, and_9_out);
  and and_16 (and_16_out, or_7_out, and_10_out);
  and and_17 (and_17_out, RD_RT2, and_11_out);
  and and_18 (and_18_out, RD_RS2, and_12_out);
  nor nor_1 (nor_1_out, and_13_out, and_14_out, and_15_out);
  and and_19 (and_19_out, nor_1_out, nor_2_out);
  nor nor_2 (nor_2_out, and_16_out, and_17_out, and_18_out);
  Multiplexer multiplexer_1 (.in0(1'b1), .in1(and_19_out), .out(IF_ID_STOP), .sel(Istr1[4]));  // open: en
  not not_1 (ID_EX_CLEAR, IF_ID_STOP);

  // Other names for the same wires on the sheet: clearID_EX = ID_EX_CLEAR; ADDI = Istr[0]; ADDIU = Istr[1];
  //   ANDI = Istr[2]; ORI = Istr[3]; LW = Istr[4]; SW = Istr[5]; BEQ = Istr[6]; BNE = Istr[7]; SLTI = Istr[8];
  //   J = Istr[9]; JAL = Istr[10]; SB = Istr[11]; BLTZ = Istr[12]; ADD = Istr[13]; ADDU = Istr[14]; AND = Istr[15];
  //   SUB = Istr[16]; OR = Istr[17]; NOR = Istr[18]; SLT = Istr[19]; SLTU = Istr[20]; SRLV = Istr[21];
  //   SRAV = Istr[22]; SLL = Istr[23]; SRA = Istr[24]; SRL = Istr[25]; JR = Istr[26]; SYSCAL = Istr[27];
  //   EFC = Istr[28]; ETC = Istr[29]; ADDI1 = Istr1[0]; ADDIU1 = Istr1[1]; ANDI1 = Istr1[2]; ORI1 = Istr1[3];
  //   LW1 = Istr1[4]; SW1 = Istr1[5]; BEQ1 = Istr1[6]; BNE1 = Istr1[7]; SLTI1 = Istr1[8]; J1 = Istr1[9];
  //   JAL1 = Istr1[10]; SB1 = Istr1[11]; BLTZ1 = Istr1[12]; ADD1 = Istr1[13]; ADDU1 = Istr1[14]; AND1 = Istr1[15];
  //   SUB1 = Istr1[16]; OR1 = Istr1[17]; NOR1 = Istr1[18]; SLT1 = Istr1[19]; SLTU1 = Istr1[20]; SRLV1 = Istr1[21];
  //   SRAV1 = Istr1[22]; SLL1 = Istr1[23]; SRA1 = Istr1[24]; SRL1 = Istr1[25]; JR1 = Istr1[26]; SYSCAL1 = Istr1[27];
  //   EFC1 = Istr1[28]; ETC1 = Istr1[29]; ADDI2 = Istr2[0]; ADDIU2 = Istr2[1]; ANDI2 = Istr2[2]; ORI2 = Istr2[3];
  //   LW2 = Istr2[4]; SW2 = Istr2[5]; BEQ2 = Istr2[6]; BNE2 = Istr2[7]; SLTI2 = Istr2[8]; J2 = Istr2[9];
  //   JAL2 = Istr2[10]; SB2 = Istr2[11]; BLTZ2 = Istr2[12]; ADD2 = Istr2[13]; ADDU2 = Istr2[14]; AND2 = Istr2[15];
  //   SUB2 = Istr2[16]; OR2 = Istr2[17]; NOR2 = Istr2[18]; SLT2 = Istr2[19]; SLTU2 = Istr2[20]; SRLV2 = Istr2[21];
  //   SRAV2 = Istr2[22]; SLL2 = Istr2[23]; SRA2 = Istr2[24]; SRL2 = Istr2[25]; JR2 = Istr2[26]; SYSCAL2 = Istr2[27];
  //   EFC2 = Istr2[28]; ETC2 = Istr2[29]; stopIF_ID = IF_ID_STOP
endmodule

// Redirect
module redirect (
  input  [4:0] RS,
  input  [4:0] RD_EX,
  input  [4:0] RD_MEM,
  input  [4:0] RT,
  input  [29:0] Istr1,
  input  [29:0] Istr2,
  input  [29:0] Istr,
  input  [4:0] RD_ID,
  output [1:0] RT_Sel,
  output [1:0] RS_Sel
);

  wire _RD1, _RD2, _RS, _RT, and_7_out, and_8_out, and_9_out, and_10_out, and_11_out, and_12_out, and_13_out,
       and_14_out, and_15_out, and_16_out, and_17_out, and_18_out, and_19_out, and_20_out, and_21_out,
       and_22_out, and_23_out, comparator_5_eq, comparator_6_eq, comparator_7_eq, comparator_8_eq,
       comparator_9_eq, RD_RS1, RD_RS2, RD_RT1, RD_RT2, RDEX_IS0, RDMEM_IS0, RS_IS0, RS_RT, RT_IS0,
       WriteReg1, WriteReg2;

  Comparator #(.width(5)) comparator_1 (.a({5{1'b0}}), .b(RS), .eq(RS_IS0));  // open: gt, lt
  Comparator #(.width(5)) comparator_2 (.a({5{1'b0}}), .b(RT), .eq(RT_IS0));  // open: gt, lt
  Comparator #(.width(5)) comparator_3 (.a({5{1'b0}}), .b(RD_EX), .eq(RDEX_IS0));  // open: gt, lt
  Comparator #(.width(5)) comparator_4 (.a({5{1'b0}}), .b(RD_MEM), .eq(RDMEM_IS0));  // open: gt, lt
  or or_1 (RS_RT, Istr[5], Istr[13], Istr[14], Istr[15], Istr[16], Istr[17], Istr[18], Istr[27], Istr[7], Istr[6], Istr[20], Istr[19], Istr[22], Istr[21], Istr[4]);
  or or_2 (_RS, Istr[0], Istr[1], Istr[2], Istr[3], Istr[10], Istr[26], Istr[8], Istr[12]);
  Comparator #(.width(5)) comparator_5 (.a(RD_EX), .b(RS), .eq(comparator_5_eq));  // open: gt, lt
  Comparator #(.width(5)) comparator_6 (.a(RD_EX), .b(RT), .eq(comparator_6_eq));  // open: gt, lt
  Comparator #(.width(5)) comparator_7 (.a(RD_MEM), .b(RS), .eq(comparator_7_eq));  // open: gt, lt
  Comparator #(.width(5)) comparator_8 (.a(RD_MEM), .b(RT), .eq(comparator_8_eq));  // open: gt, lt
  and and_1 (WriteReg1, _RD1, ~RDEX_IS0);  // AND_Gate
  and and_2 (WriteReg2, _RD2, ~RDMEM_IS0);  // AND_Gate
  and and_3 (RD_RS1, ~RS_IS0, comparator_5_eq);  // AND_Gate
  and and_4 (RD_RT1, ~RT_IS0, comparator_6_eq);  // AND_Gate
  and and_5 (RD_RS2, ~RS_IS0, comparator_7_eq);  // AND_Gate
  and and_6 (RD_RT2, ~RT_IS0, comparator_8_eq);  // AND_Gate
  or or_3 (_RT, Istr[23], Istr[11], Istr[29], Istr[25], Istr[24]);
  Comparator #(.width(5)) comparator_9 (.a(RD_EX), .b(5'b00010), .eq(comparator_9_eq));  // open: gt, lt
  and and_7 (and_7_out, Istr[27], comparator_9_eq, WriteReg1);
  or or_4 (_RD2, Istr2[0], Istr2[2], Istr2[4], Istr2[1], Istr2[8], Istr2[3], Istr2[10], Istr2[13], Istr2[14], Istr2[15], Istr2[28], Istr2[17], Istr2[16], Istr2[19], Istr2[18], Istr2[21], Istr2[20], Istr2[23], Istr2[22], Istr2[25], Istr2[24]);
  and and_8 (and_8_out, RD_RT1, and_9_out);
  and and_9 (and_9_out, RS_RT, WriteReg1);
  and and_10 (and_10_out, RD_RT1, and_11_out);
  and and_11 (and_11_out, _RT, WriteReg1);
  and and_12 (and_12_out, RD_RS1, and_13_out);
  and and_13 (and_13_out, _RS, WriteReg1);
  and and_14 (and_14_out, RD_RS1, and_15_out);
  and and_15 (and_15_out, RS_RT, WriteReg1);
  or or_5 (RT_Sel[0], and_8_out, and_10_out);
  or or_6 (RS_Sel[0], and_12_out, and_7_out, and_14_out);
  or or_7 (_RD1, Istr1[0], Istr1[2], Istr1[4], Istr1[1], Istr1[8], Istr1[3], Istr1[10], Istr1[13], Istr1[14], Istr1[15], Istr1[28], Istr1[17], Istr1[16], Istr1[19], Istr1[18], Istr1[21], Istr1[20], Istr1[23], Istr1[22], Istr1[25], Istr1[24]);
  and and_16 (and_16_out, RS_RT, WriteReg2);
  and and_17 (and_17_out, _RT, WriteReg2);
  and and_18 (and_18_out, _RS, WriteReg2);
  and and_19 (and_19_out, RS_RT, WriteReg2);
  and and_20 (and_20_out, RD_RT2, and_16_out);
  and and_21 (and_21_out, RD_RT2, and_17_out);
  and and_22 (and_22_out, RD_RS2, and_18_out);
  and and_23 (and_23_out, RD_RS2, and_19_out);
  or or_8 (RT_Sel[1], and_20_out, and_21_out);
  or or_9 (RS_Sel[1], and_22_out, and_23_out);

  // Other names for the same wires on the sheet: ADDI = Istr[0]; ADDIU = Istr[1]; ANDI = Istr[2]; ORI = Istr[3];
  //   LW = Istr[4]; SW = Istr[5]; BEQ = Istr[6]; BNE = Istr[7]; SLTI = Istr[8]; J = Istr[9]; JAL = Istr[10];
  //   SB = Istr[11]; BLTZ = Istr[12]; ADD = Istr[13]; ADDU = Istr[14]; AND = Istr[15]; SUB = Istr[16]; OR = Istr[17];
  //   NOR = Istr[18]; SLT = Istr[19]; SLTU = Istr[20]; SRLV = Istr[21]; SRAV = Istr[22]; SLL = Istr[23];
  //   SRA = Istr[24]; SRL = Istr[25]; JR = Istr[26]; SYSCAL = Istr[27]; EFC = Istr[28]; ETC = Istr[29];
  //   ADDI1 = Istr1[0]; ADDIU1 = Istr1[1]; ANDI1 = Istr1[2]; ORI1 = Istr1[3]; LW1 = Istr1[4]; SW1 = Istr1[5];
  //   BEQ1 = Istr1[6]; BNE1 = Istr1[7]; SLTI1 = Istr1[8]; J1 = Istr1[9]; JAL1 = Istr1[10]; SB1 = Istr1[11];
  //   BLTZ1 = Istr1[12]; ADD1 = Istr1[13]; ADDU1 = Istr1[14]; AND1 = Istr1[15]; SUB1 = Istr1[16]; OR1 = Istr1[17];
  //   NOR1 = Istr1[18]; SLT1 = Istr1[19]; SLTU1 = Istr1[20]; SRLV1 = Istr1[21]; SRAV1 = Istr1[22]; SLL1 = Istr1[23];
  //   SRA1 = Istr1[24]; SRL1 = Istr1[25]; JR1 = Istr1[26]; SYSCAL1 = Istr1[27]; EFC1 = Istr1[28]; ETC1 = Istr1[29];
  //   ADDI2 = Istr2[0]; ADDIU2 = Istr2[1]; ANDI2 = Istr2[2]; ORI2 = Istr2[3]; LW2 = Istr2[4]; SW2 = Istr2[5];
  //   BEQ2 = Istr2[6]; BNE2 = Istr2[7]; SLTI2 = Istr2[8]; J2 = Istr2[9]; JAL2 = Istr2[10]; SB2 = Istr2[11];
  //   BLTZ2 = Istr2[12]; ADD2 = Istr2[13]; ADDU2 = Istr2[14]; AND2 = Istr2[15]; SUB2 = Istr2[16]; OR2 = Istr2[17];
  //   NOR2 = Istr2[18]; SLT2 = Istr2[19]; SLTU2 = Istr2[20]; SRLV2 = Istr2[21]; SRAV2 = Istr2[22]; SLL2 = Istr2[23];
  //   SRA2 = Istr2[24]; SRL2 = Istr2[25]; JR2 = Istr2[26]; SYSCAL2 = Istr2[27]; EFC2 = Istr2[28]; ETC2 = Istr2[29];
  //   RS_sel_0 = RS_Sel[0]; RS_sel_1 = RS_Sel[1]; RT_sel_0 = RT_Sel[0]; RT_sel_1 = RT_Sel[1]
endmodule

module Branch (
  input  [29:0] InstrIn,
  input  [31:0] RS,
  input  [31:0] RT,
  input  [1:0] M4In,
  output [1:0] M4Out,
  output Disp,
  output Halt,
  output EQUAL,
  output LESS,
  output Pause
);

  wire and_1_out, and_2_out, and_3_out, comparator_3_eq, comparator_4_eq, comparator_5_eq;

  Comparator #(.width(32)) comparator_1 (.a(RS), .b(RT), .eq(EQUAL));  // open: gt, lt
  Comparator #(.width(32)) comparator_2 (.a(RS), .b({32{1'b0}}), .lt(LESS));  // open: gt, eq
  and and_1 (and_1_out, EQUAL, InstrIn[6]);
  and and_2 (and_2_out, ~EQUAL, InstrIn[7]);  // AND_Gate
  and and_3 (and_3_out, InstrIn[12], LESS);
  or or_1 (M4Out[1], and_1_out, and_2_out, and_3_out, M4In[1]);
  Comparator #(.width(32)) comparator_3 (.a(RS), .b(32'ha), .eq(comparator_3_eq));  // open: gt, lt
  Comparator #(.width(32)) comparator_4 (.a(RS), .b(32'h22), .eq(comparator_4_eq));  // open: gt, lt
  Comparator #(.width(32)) comparator_5 (.a(RS), .b(32'h32), .eq(comparator_5_eq));  // open: gt, lt
  and and_4 (Disp, InstrIn[27], comparator_4_eq);
  and and_5 (Halt, InstrIn[27], comparator_3_eq);
  and and_6 (Pause, InstrIn[27], comparator_5_eq);

  assign M4Out[0] = M4In[0];

  // Other names for the same wires on the sheet: ADDI = InstrIn[0]; Istr[29:0] = InstrIn; ADDIU = InstrIn[1];
  //   ANDI = InstrIn[2]; ORI = InstrIn[3]; LW = InstrIn[4]; SW = InstrIn[5]; BEQ = InstrIn[6]; BNE = InstrIn[7];
  //   SLTI = InstrIn[8]; J = InstrIn[9]; JAL = InstrIn[10]; SB = InstrIn[11]; BLTZ = InstrIn[12]; ADD = InstrIn[13];
  //   ADDU = InstrIn[14]; AND = InstrIn[15]; SUB = InstrIn[16]; OR = InstrIn[17]; NOR = InstrIn[18];
  //   SLT = InstrIn[19]; SLTU = InstrIn[20]; SRLV = InstrIn[21]; SRAV = InstrIn[22]; SLL = InstrIn[23];
  //   SRA = InstrIn[24]; SRL = InstrIn[25]; JR = InstrIn[26]; SYSCAL = InstrIn[27]
endmodule

// DCtrl
module romshm (
  input  [31:0] DataIn,
  input  [3:0] selIn,
  output [31:0] DataOut
);

  wire comparator_1_eq, comparator_2_eq, comparator_3_eq, comparator_4_eq, comparator_5_eq, comparator_6_eq,
       comparator_7_eq, or_1_out, or_2_out;
  wire [1:0] or_3_out;

  Comparator #(.width(4)) comparator_1 (.a(selIn), .b(4'b1111), .eq(comparator_1_eq));  // open: gt, lt
  Comparator #(.width(4)) comparator_2 (.a(selIn), .b(4'b0011), .eq(comparator_2_eq));  // open: gt, lt
  Comparator #(.width(4)) comparator_3 (.a(selIn), .b(4'b1100), .eq(comparator_3_eq));  // open: gt, lt
  Comparator #(.width(4)) comparator_4 (.a(selIn), .b(4'b0001), .eq(comparator_4_eq));  // open: gt, lt
  Comparator #(.width(4)) comparator_5 (.a(selIn), .b(4'b0010), .eq(comparator_5_eq));  // open: gt, lt
  Comparator #(.width(4)) comparator_6 (.a(selIn), .b(4'b0100), .eq(comparator_6_eq));  // open: gt, lt
  Comparator #(.width(4)) comparator_7 (.a(selIn), .b(4'b1000), .eq(comparator_7_eq));  // open: gt, lt
  or or_1 (or_1_out, comparator_2_eq, comparator_3_eq);
  or or_2 (or_2_out, comparator_4_eq, comparator_5_eq, comparator_6_eq, comparator_7_eq);
  or or_3 (or_3_out[0], comparator_1_eq, or_1_out);
  or or_4 (or_3_out[1], comparator_1_eq, or_2_out);
  Multiplexer #(.select(2), .width(32)) multiplexer_1 (
    .in0(DataIn), .in1({DataIn[15:0], DataIn[15:0]}),
    .in2({DataIn[7:0], DataIn[7:0], DataIn[7:0], DataIn[7:0]}), .in3(DataIn), .out(DataOut), .sel(or_3_out));  // open: en

  // Other names for the same wires on the sheet: Byte[31:0] = {DataIn[7:0], DataIn[7:0], DataIn[7:0], DataIn[7:0]};
  //   Half[31:0] = {DataIn[15:0], DataIn[15:0]}
endmodule

module Ctrl (
  input  En,
  input  Pause,
  input  Power,
  input  PAU,
  output Ctrl,
  output PcCtrl
);

  and and_1 (Ctrl, Pause, En);
  and and_2 (PcCtrl, Pause, Power, En);
endmodule

module PC (
  input  [31:0] AddrIn,
  input  Clk,
  input  Rst,
  input  PcCtrl,
  output [31:0] AddrOut
);

  Register #(.width(32)) PC (.D(AddrIn), .en(PcCtrl), .Q(AddrOut), .clk(Clk), .clr(Rst));
endmodule

module Address (
  input  [9:0] AddrIn,
  input  [31:0] AddrBranch,
  input  Sel,
  output [31:0] AddrOut,
  output [31:0] PcOut
);

  Multiplexer #(.width(32)) multiplexer_1 (.in0(AddrOut), .in1(AddrBranch), .out(PcOut), .sel(Sel));  // open: en
  // Probe on {{22{1'b0}}, AddrIn}
  Adder #(.width(32)) adder_1 (.a({{22{1'b0}}, AddrIn}), .b(32'h1), .out(AddrOut));  // open: cin, cout
endmodule

// INT
module \int  (
  input  etc,
  input  cli,
  input  \_1号中断 ,
  input  rst,
  input  \_2号中断 ,
  input  [31:0] rt,
  input  [31:0] PcOut,
  input  eret,
  input  sti,
  input  \_3号中断 ,
  input  clk,
  output [31:0] AddrIn,
  output [31:0] epc,
  output [2:0] inf
);

  wire _1_out, _2_out, _3_out, and_1_out, and_2_out, and_3_out, button_int_1_and_1, button_int_1_and_2,
       button_int_1_and_3, decoder_1_out1, decoder_1_out2, decoder_1_out3, ie, inm_1_out_1, inm_1_out_2,
       inm_1_out_3, int1, int2, int3, IntC, multiplexer_2_out, not_1_out, not_2_out, not_3_out, or_1_out,
       or_2_out;
  wire [1:0] IR_CLR, priority_encoder_1_out;
  wire [31:0] idt_1_addr, multiplexer_1_out, multiplexer_4_out;

  Decoder #(.select(2)) decoder_1 (
    .out1(decoder_1_out1), .out2(decoder_1_out2), .out3(decoder_1_out3), .sel(IR_CLR));  // open: out0, en
  Button _1 (.out(_1_out));
  Button _2 (.out(_2_out));
  Button _3 (.out(_3_out));
  button_int button_int_1 (
    ._1st(\_1号中断 ), ._2nd(\_2号中断 ), ._3rd(\_3号中断 ), .Clk(clk), .Rst(rst), ._1st_int_wait(inf[0]),
    ._2nd_int_wait(inf[1]), ._3rd_int_wait(inf[2]), .clr_1(decoder_1_out1), .clr_2(decoder_1_out2),
    .clr_3(decoder_1_out3), .and_1(button_int_1_and_1), .and_2(button_int_1_and_2), .and_3(button_int_1_and_3));
  INM inm_1 (
    .Clk(clk), .Rst(rst), .en_1(1'b0), .en_2(1'b0), .en_3(1'b0), .init_1(_1_out), .init_2(_2_out),
    .init_3(_3_out), .Out_1(inm_1_out_1), .Out_2(inm_1_out_2), .Out_3(inm_1_out_3));  // open: INM_1, INM_2, INM_3
  or or_1 (or_1_out, IntC, etc);
  not not_1 (not_1_out, inm_1_out_1);
  not not_2 (not_2_out, inm_1_out_2);
  not not_3 (not_3_out, inm_1_out_3);
  Multiplexer #(.width(32)) multiplexer_1 (.in0(PcOut), .in1(rt), .out(multiplexer_1_out), .sel(etc));  // open: en
  EPC epc_1 (.Clk(clk), .Rst(rst), .en(or_1_out), .PC_CUR(multiplexer_1_out), .PC_EPC(epc));
  // Probe on epc
  and and_1 (and_1_out, button_int_1_and_1, not_1_out);
  and and_2 (and_2_out, button_int_1_and_2, not_2_out);
  and and_3 (and_3_out, button_int_1_and_3, not_3_out);
  // Probe on rt
  Priority_Encoder #(.select(2)) priority_encoder_1 (
    .in0(1'b1), .in1(and_1_out), .in2(and_2_out), .in3(and_3_out), .out(priority_encoder_1_out));  // open: gs, en_out, en_in
  Multiplexer multiplexer_2 (.in0(1'b1), .in1(1'b0), .out(multiplexer_2_out), .sel(sti));  // open: en
  or or_2 (or_2_out, cli, IntC, sti);
  Multiplexer #(.width(32)) multiplexer_3 (.in0(multiplexer_4_out), .in1(epc), .out(AddrIn), .sel(eret));  // open: en
  Multiplexer #(.width(32)) multiplexer_4 (
    .in0(PcOut), .in1(idt_1_addr), .out(multiplexer_4_out), .sel(IntC));  // open: en
  Multiplexer #(.width(2)) multiplexer_5 (
    .in0(2'b00), .in1(priority_encoder_1_out), .out(IR_CLR), .sel(eret));  // open: en
  IDT idt_1 (.Index(priority_encoder_1_out), .Addr(idt_1_addr));
  IE ie_1 (.Clk(clk), .Istr(multiplexer_2_out), .Rst(rst), .en(or_2_out), .ie(ie));
  Decoder #(.select(2)) decoder_2 (
    .out1(int1), .out2(int2), .out3(int3), .sel(priority_encoder_1_out));  // open: out0, en
  // Probe on priority_encoder_1_out
  wait_int wait_int_1 (
    .CLK(clk), .ie(ie), .\_1号中断 (\_1号中断 ), .int1(int1), .\_2号中断 (\_2号中断 ), .int2(int2), .\_3号中断 (\_3号中断 ),
    .int3(int3), .IntC(IntC));
endmodule

module addr (
  input  [1:0] M4,
  input  [31:0] PC,
  input  [31:0] IMM26,
  input  [31:0] IMM16,
  input  [31:0] RS,
  input  [1:0] M1,
  input  [4:0] RT,
  input  [4:0] RD,
  output AddrSel,
  output [31:0] M4Out,
  output [4:0] M1Out
);

  wire [31:0] adder_1_out;

  Multiplexer #(.select(2), .width(5)) multiplexer_1 (
    .in0(RT), .in1(RD), .in2({5{1'b1}}), .in3({5{1'b0}}), .out(M1Out), .sel(M1));  // open: en
  Adder #(.width(32)) adder_1 (.a(PC), .b(IMM16), .out(adder_1_out));  // open: cin, cout
  Multiplexer #(.select(2), .width(32)) multiplexer_2 (
    .in0(PC), .in1(IMM26), .in2(adder_1_out), .in3(RS), .out(M4Out), .sel(M4));  // open: en
  Comparator #(.width(2), .mode("unsigned")) comparator_1 (.a(M4), .b(2'b00), .gt(AddrSel));  // open: eq, lt
endmodule

// Mux_Direct
module RedirectMux (
  input  [1:0] RSSel,
  input  [31:0] RS,
  input  [31:0] EX,
  input  [31:0] WB,
  input  [1:0] RTSel,
  input  [31:0] RT,
  output [31:0] RSOut,
  output [31:0] RTOut
);

  Multiplexer #(.select(2), .width(32)) multiplexer_1 (
    .in0(RS), .in1(EX), .in2(WB), .in3(EX), .out(RSOut), .sel(RSSel));  // open: en
  Multiplexer #(.select(2), .width(32)) multiplexer_2 (
    .in0(RT), .in1(EX), .in2(WB), .in3(EX), .out(RTOut), .sel(RTSel));  // open: en
endmodule
